// Logisim project 4bit_greater_or_equal_than_and_less_than - Copy.circ as structural Verilog: 1 circuit, main circuit main
module main (
  input  [3:0] ipt,
  input  [3:0] greater_or_equal,
  input  [3:0] less_than,
  output out
);

  wire comparator_1_eq, comparator_1_gt, comparator_2_lt, or_1_out;

  or or_1 (or_1_out, comparator_1_gt, comparator_1_eq);
  Comparator #(.width(4), .mode("unsigned")) comparator_1 (
    .a(ipt), .b(greater_or_equal), .gt(comparator_1_gt), .eq(comparator_1_eq));  // open: lt
  Comparator #(.width(4), .mode("unsigned")) comparator_2 (
    .a(ipt), .b(less_than), .lt(comparator_2_lt));  // open: gt, eq
  and and_1 (out, or_1_out, comparator_2_lt);
endmodule
