// Logisim project 64x64_LED_MATRIX.circ as structural Verilog: 1 circuit, main circuit main
module main (
);

  wire clock_1_out, comparator_1_eq, counter_1_carry, not_1_out;
  wire [1:0] counter_5_q;
  wire [4:0] COL;
  wire [5:0] counter_4_q;
  wire [6:0] counter_3_q;
  wire [31:0] controlled_buffer_1_out, demultiplexer_2_out0, demultiplexer_2_out1, demultiplexer_2_out2,
       demultiplexer_2_out3, demultiplexer_2_out4, demultiplexer_2_out5, demultiplexer_2_out6,
       demultiplexer_2_out7, demultiplexer_2_out8, demultiplexer_2_out9, demultiplexer_2_out10,
       demultiplexer_2_out11, demultiplexer_2_out12, demultiplexer_2_out13, demultiplexer_2_out14,
       demultiplexer_2_out15, demultiplexer_2_out16, demultiplexer_2_out17, demultiplexer_2_out18,
       demultiplexer_2_out19, demultiplexer_2_out20, demultiplexer_2_out21, demultiplexer_2_out22,
       demultiplexer_2_out23, demultiplexer_2_out24, demultiplexer_2_out25, demultiplexer_2_out26,
       demultiplexer_2_out27, demultiplexer_2_out28, demultiplexer_2_out29, demultiplexer_2_out30,
       demultiplexer_2_out31, demultiplexer_3_out0, demultiplexer_3_out1, demultiplexer_3_out2,
       demultiplexer_3_out3, demultiplexer_3_out4, demultiplexer_3_out5, demultiplexer_3_out6,
       demultiplexer_3_out7, demultiplexer_3_out8, demultiplexer_3_out9, demultiplexer_3_out10,
       demultiplexer_3_out11, demultiplexer_3_out12, demultiplexer_3_out13, demultiplexer_3_out14,
       demultiplexer_3_out15, demultiplexer_3_out16, demultiplexer_3_out17, demultiplexer_3_out18,
       demultiplexer_3_out19, demultiplexer_3_out20, demultiplexer_3_out21, demultiplexer_3_out22,
       demultiplexer_3_out23, demultiplexer_3_out24, demultiplexer_3_out25, demultiplexer_3_out26,
       demultiplexer_3_out27, demultiplexer_3_out28, demultiplexer_3_out29, demultiplexer_3_out30,
       demultiplexer_3_out31, demultiplexer_4_out0, demultiplexer_4_out1, demultiplexer_4_out2,
       demultiplexer_4_out3, demultiplexer_4_out4, demultiplexer_4_out5, demultiplexer_4_out6,
       demultiplexer_4_out7, demultiplexer_4_out8, demultiplexer_4_out9, demultiplexer_4_out10,
       demultiplexer_4_out11, demultiplexer_4_out12, demultiplexer_4_out13, demultiplexer_4_out14,
       demultiplexer_4_out15, demultiplexer_4_out16, demultiplexer_4_out17, demultiplexer_4_out18,
       demultiplexer_4_out19, demultiplexer_4_out20, demultiplexer_4_out21, demultiplexer_4_out22,
       demultiplexer_4_out23, demultiplexer_4_out24, demultiplexer_4_out25, demultiplexer_4_out26,
       demultiplexer_4_out27, demultiplexer_4_out28, demultiplexer_4_out29, demultiplexer_4_out30,
       demultiplexer_4_out31, demultiplexer_5_out0, demultiplexer_5_out1, demultiplexer_5_out2,
       demultiplexer_5_out3, demultiplexer_5_out4, demultiplexer_5_out5, demultiplexer_5_out6,
       demultiplexer_5_out7, demultiplexer_5_out8, demultiplexer_5_out9, demultiplexer_5_out10,
       demultiplexer_5_out11, demultiplexer_5_out12, demultiplexer_5_out13, demultiplexer_5_out14,
       demultiplexer_5_out15, demultiplexer_5_out16, demultiplexer_5_out17, demultiplexer_5_out18,
       demultiplexer_5_out19, demultiplexer_5_out20, demultiplexer_5_out21, demultiplexer_5_out22,
       demultiplexer_5_out23, demultiplexer_5_out24, demultiplexer_5_out25, demultiplexer_5_out26,
       demultiplexer_5_out27, demultiplexer_5_out28, demultiplexer_5_out29, demultiplexer_5_out30,
       demultiplexer_5_out31, LB, LT, RB, rom_1_data, RT;

  Clock clock_1 (.out(clock_1_out));
  Counter #(.width(1), .max('h1)) counter_1 (
    .carry(counter_1_carry), .clk(clock_1_out));  // open: load, D, count, Q, clr
  Counter #(.width(5), .max('h1f)) counter_2 (.Q(COL), .clk(counter_1_carry));  // open: load, D, count, carry, clr
  Counter #(.width(7), .max('h7f)) counter_3 (
    .Q(counter_3_q), .clk(counter_1_carry));  // open: load, D, count, carry, clr
  Counter #(.width(6), .max('h3f)) counter_4 (
    .Q(counter_4_q), .clk(counter_1_carry), .clr(comparator_1_eq));  // open: load, D, count, carry
  Comparator #(.width(6)) comparator_1 (.a(counter_4_q), .b(6'b100000), .eq(comparator_1_eq));  // open: gt, lt
  assign controlled_buffer_1_out = counter_1_carry ? {32{1'b0}} : 32'bz;  // Controlled_Buffer controlled_buffer_1
  not not_1 (not_1_out, counter_1_carry);
  assign controlled_buffer_1_out = not_1_out ? rom_1_data : 32'bz;  // Controlled_Buffer controlled_buffer_2
  ROM #(.addrWidth(7), .dataWidth(32)) rom_1 (.addr(counter_3_q), .data(rom_1_data));  // open: sel
  Counter #(.width(2), .max('h3)) counter_5 (
    .Q(counter_5_q), .clk(comparator_1_eq));  // open: load, D, count, carry, clr
  Demultiplexer #(.select(2), .width(32)) demultiplexer_1 (
    .out0(LT), .out1(RT), .out2(LB), .out3(RB), .in(controlled_buffer_1_out), .sel(counter_5_q));  // open: en
  DotMatrix #(.matrixcols(32), .matrixrows(32), .persist(600)) dotmatrix_1 (
    .col0(demultiplexer_2_out0), .col1(demultiplexer_2_out1), .col2(demultiplexer_2_out2),
    .col3(demultiplexer_2_out3), .col4(demultiplexer_2_out4), .col5(demultiplexer_2_out5),
    .col6(demultiplexer_2_out6), .col7(demultiplexer_2_out7), .col8(demultiplexer_2_out8),
    .col9(demultiplexer_2_out9), .col10(demultiplexer_2_out10), .col11(demultiplexer_2_out11),
    .col12(demultiplexer_2_out12), .col13(demultiplexer_2_out13), .col14(demultiplexer_2_out14),
    .col15(demultiplexer_2_out15), .col16(demultiplexer_2_out16), .col17(demultiplexer_2_out17),
    .col18(demultiplexer_2_out18), .col19(demultiplexer_2_out19), .col20(demultiplexer_2_out20),
    .col21(demultiplexer_2_out21), .col22(demultiplexer_2_out22), .col23(demultiplexer_2_out23),
    .col24(demultiplexer_2_out24), .col25(demultiplexer_2_out25), .col26(demultiplexer_2_out26),
    .col27(demultiplexer_2_out27), .col28(demultiplexer_2_out28), .col29(demultiplexer_2_out29),
    .col30(demultiplexer_2_out30), .col31(demultiplexer_2_out31));
  DotMatrix #(.matrixcols(32), .matrixrows(32), .persist(600)) dotmatrix_2 (
    .col0(demultiplexer_3_out0), .col1(demultiplexer_3_out1), .col2(demultiplexer_3_out2),
    .col3(demultiplexer_3_out3), .col4(demultiplexer_3_out4), .col5(demultiplexer_3_out5),
    .col6(demultiplexer_3_out6), .col7(demultiplexer_3_out7), .col8(demultiplexer_3_out8),
    .col9(demultiplexer_3_out9), .col10(demultiplexer_3_out10), .col11(demultiplexer_3_out11),
    .col12(demultiplexer_3_out12), .col13(demultiplexer_3_out13), .col14(demultiplexer_3_out14),
    .col15(demultiplexer_3_out15), .col16(demultiplexer_3_out16), .col17(demultiplexer_3_out17),
    .col18(demultiplexer_3_out18), .col19(demultiplexer_3_out19), .col20(demultiplexer_3_out20),
    .col21(demultiplexer_3_out21), .col22(demultiplexer_3_out22), .col23(demultiplexer_3_out23),
    .col24(demultiplexer_3_out24), .col25(demultiplexer_3_out25), .col26(demultiplexer_3_out26),
    .col27(demultiplexer_3_out27), .col28(demultiplexer_3_out28), .col29(demultiplexer_3_out29),
    .col30(demultiplexer_3_out30), .col31(demultiplexer_3_out31));
  Demultiplexer #(.select(5), .width(32)) demultiplexer_2 (
    .out0(demultiplexer_2_out0), .out1(demultiplexer_2_out1), .out2(demultiplexer_2_out2),
    .out3(demultiplexer_2_out3), .out4(demultiplexer_2_out4), .out5(demultiplexer_2_out5),
    .out6(demultiplexer_2_out6), .out7(demultiplexer_2_out7), .out8(demultiplexer_2_out8),
    .out9(demultiplexer_2_out9), .out10(demultiplexer_2_out10), .out11(demultiplexer_2_out11),
    .out12(demultiplexer_2_out12), .out13(demultiplexer_2_out13), .out14(demultiplexer_2_out14),
    .out15(demultiplexer_2_out15), .out16(demultiplexer_2_out16), .out17(demultiplexer_2_out17),
    .out18(demultiplexer_2_out18), .out19(demultiplexer_2_out19), .out20(demultiplexer_2_out20),
    .out21(demultiplexer_2_out21), .out22(demultiplexer_2_out22), .out23(demultiplexer_2_out23),
    .out24(demultiplexer_2_out24), .out25(demultiplexer_2_out25), .out26(demultiplexer_2_out26),
    .out27(demultiplexer_2_out27), .out28(demultiplexer_2_out28), .out29(demultiplexer_2_out29),
    .out30(demultiplexer_2_out30), .out31(demultiplexer_2_out31), .in(LT), .sel(COL));  // open: en
  Demultiplexer #(.select(5), .width(32)) demultiplexer_3 (
    .out0(demultiplexer_3_out0), .out1(demultiplexer_3_out1), .out2(demultiplexer_3_out2),
    .out3(demultiplexer_3_out3), .out4(demultiplexer_3_out4), .out5(demultiplexer_3_out5),
    .out6(demultiplexer_3_out6), .out7(demultiplexer_3_out7), .out8(demultiplexer_3_out8),
    .out9(demultiplexer_3_out9), .out10(demultiplexer_3_out10), .out11(demultiplexer_3_out11),
    .out12(demultiplexer_3_out12), .out13(demultiplexer_3_out13), .out14(demultiplexer_3_out14),
    .out15(demultiplexer_3_out15), .out16(demultiplexer_3_out16), .out17(demultiplexer_3_out17),
    .out18(demultiplexer_3_out18), .out19(demultiplexer_3_out19), .out20(demultiplexer_3_out20),
    .out21(demultiplexer_3_out21), .out22(demultiplexer_3_out22), .out23(demultiplexer_3_out23),
    .out24(demultiplexer_3_out24), .out25(demultiplexer_3_out25), .out26(demultiplexer_3_out26),
    .out27(demultiplexer_3_out27), .out28(demultiplexer_3_out28), .out29(demultiplexer_3_out29),
    .out30(demultiplexer_3_out30), .out31(demultiplexer_3_out31), .in(LB), .sel(COL));  // open: en
  DotMatrix #(.matrixcols(32), .matrixrows(32), .persist(600)) dotmatrix_3 (
    .col0(demultiplexer_4_out0), .col1(demultiplexer_4_out1), .col2(demultiplexer_4_out2),
    .col3(demultiplexer_4_out3), .col4(demultiplexer_4_out4), .col5(demultiplexer_4_out5),
    .col6(demultiplexer_4_out6), .col7(demultiplexer_4_out7), .col8(demultiplexer_4_out8),
    .col9(demultiplexer_4_out9), .col10(demultiplexer_4_out10), .col11(demultiplexer_4_out11),
    .col12(demultiplexer_4_out12), .col13(demultiplexer_4_out13), .col14(demultiplexer_4_out14),
    .col15(demultiplexer_4_out15), .col16(demultiplexer_4_out16), .col17(demultiplexer_4_out17),
    .col18(demultiplexer_4_out18), .col19(demultiplexer_4_out19), .col20(demultiplexer_4_out20),
    .col21(demultiplexer_4_out21), .col22(demultiplexer_4_out22), .col23(demultiplexer_4_out23),
    .col24(demultiplexer_4_out24), .col25(demultiplexer_4_out25), .col26(demultiplexer_4_out26),
    .col27(demultiplexer_4_out27), .col28(demultiplexer_4_out28), .col29(demultiplexer_4_out29),
    .col30(demultiplexer_4_out30), .col31(demultiplexer_4_out31));
  DotMatrix #(.matrixcols(32), .matrixrows(32), .persist(600)) dotmatrix_4 (
    .col0(demultiplexer_5_out0), .col1(demultiplexer_5_out1), .col2(demultiplexer_5_out2),
    .col3(demultiplexer_5_out3), .col4(demultiplexer_5_out4), .col5(demultiplexer_5_out5),
    .col6(demultiplexer_5_out6), .col7(demultiplexer_5_out7), .col8(demultiplexer_5_out8),
    .col9(demultiplexer_5_out9), .col10(demultiplexer_5_out10), .col11(demultiplexer_5_out11),
    .col12(demultiplexer_5_out12), .col13(demultiplexer_5_out13), .col14(demultiplexer_5_out14),
    .col15(demultiplexer_5_out15), .col16(demultiplexer_5_out16), .col17(demultiplexer_5_out17),
    .col18(demultiplexer_5_out18), .col19(demultiplexer_5_out19), .col20(demultiplexer_5_out20),
    .col21(demultiplexer_5_out21), .col22(demultiplexer_5_out22), .col23(demultiplexer_5_out23),
    .col24(demultiplexer_5_out24), .col25(demultiplexer_5_out25), .col26(demultiplexer_5_out26),
    .col27(demultiplexer_5_out27), .col28(demultiplexer_5_out28), .col29(demultiplexer_5_out29),
    .col30(demultiplexer_5_out30), .col31(demultiplexer_5_out31));
  Demultiplexer #(.select(5), .width(32)) demultiplexer_4 (
    .out0(demultiplexer_4_out0), .out1(demultiplexer_4_out1), .out2(demultiplexer_4_out2),
    .out3(demultiplexer_4_out3), .out4(demultiplexer_4_out4), .out5(demultiplexer_4_out5),
    .out6(demultiplexer_4_out6), .out7(demultiplexer_4_out7), .out8(demultiplexer_4_out8),
    .out9(demultiplexer_4_out9), .out10(demultiplexer_4_out10), .out11(demultiplexer_4_out11),
    .out12(demultiplexer_4_out12), .out13(demultiplexer_4_out13), .out14(demultiplexer_4_out14),
    .out15(demultiplexer_4_out15), .out16(demultiplexer_4_out16), .out17(demultiplexer_4_out17),
    .out18(demultiplexer_4_out18), .out19(demultiplexer_4_out19), .out20(demultiplexer_4_out20),
    .out21(demultiplexer_4_out21), .out22(demultiplexer_4_out22), .out23(demultiplexer_4_out23),
    .out24(demultiplexer_4_out24), .out25(demultiplexer_4_out25), .out26(demultiplexer_4_out26),
    .out27(demultiplexer_4_out27), .out28(demultiplexer_4_out28), .out29(demultiplexer_4_out29),
    .out30(demultiplexer_4_out30), .out31(demultiplexer_4_out31), .in(RT), .sel(COL));  // open: en
  Demultiplexer #(.select(5), .width(32)) demultiplexer_5 (
    .out0(demultiplexer_5_out0), .out1(demultiplexer_5_out1), .out2(demultiplexer_5_out2),
    .out3(demultiplexer_5_out3), .out4(demultiplexer_5_out4), .out5(demultiplexer_5_out5),
    .out6(demultiplexer_5_out6), .out7(demultiplexer_5_out7), .out8(demultiplexer_5_out8),
    .out9(demultiplexer_5_out9), .out10(demultiplexer_5_out10), .out11(demultiplexer_5_out11),
    .out12(demultiplexer_5_out12), .out13(demultiplexer_5_out13), .out14(demultiplexer_5_out14),
    .out15(demultiplexer_5_out15), .out16(demultiplexer_5_out16), .out17(demultiplexer_5_out17),
    .out18(demultiplexer_5_out18), .out19(demultiplexer_5_out19), .out20(demultiplexer_5_out20),
    .out21(demultiplexer_5_out21), .out22(demultiplexer_5_out22), .out23(demultiplexer_5_out23),
    .out24(demultiplexer_5_out24), .out25(demultiplexer_5_out25), .out26(demultiplexer_5_out26),
    .out27(demultiplexer_5_out27), .out28(demultiplexer_5_out28), .out29(demultiplexer_5_out29),
    .out30(demultiplexer_5_out30), .out31(demultiplexer_5_out31), .in(RB), .sel(COL));  // open: en

  // Notes on the sheet:
  //   contents of rom_1 (hex, n*v repeats v):
  //   20*0 60 1fe01f8 7ff83fc 1fffc3fc 3fffe3ff 3ffff7ff 7fffffff 10*ffffffff 7fffffff 7ffff7ff 3fffe3ff
  //   1fffc3fc 7ff83fc 1fe01f8 70 26*0 1c004 3f03f 7f07f ff8ff ffbff 4*fffff 3fffff 7fffff 1ffffff 3ffffff
  //   7ffffff fffffff 1fffffff 3fffffff 18*ffffffff 7fffffff 1fffffff fffffff 7ffffff 3ffffff 1ffffff
  //   ffffff 3fffff 4*fffff ffbff ff9ff 7f07f 3f03f 1c006
endmodule
