// Logisim project 7seg_disp_driver.circ as structural Verilog: 1 circuit, main circuit main
module main (
  input  [3:0] in_1,
  output out_2,
  output out_3,
  output out_4,
  output out_5,
  output out_6,
  output out_7,
  output out_8,
  output out_9
);

  // Probe on in_1
  Pull_Resistor pull_resistor_1 (.node(in_1));
  ROM #(.addrWidth(4)) rom_1 (
    .addr(in_1), .data({out_2, out_3, out_4, out_5, out_6, out_7, out_8, out_9}));  // open: sel

  // Notes on the sheet:
  //   contents of rom_1 (hex, n*v repeats v):
  //   7e 12 bc b6 d2 e6 ee 32 fe f2
endmodule
