// Logisim project KeyboardInputAWSD.circ as structural Verilog: 1 circuit, main circuit main
module main (
  input  [6:0] Keyboard_out,
  input  Keyboard_rst,
  output Up_pressed,
  output Down_pressed,
  output Left_pressed,
  output Right_pressed,
  output Confirm_pressed,
  output Rotate_pressed
);

  or or_1 (Keyboard_rst, Up_pressed, Down_pressed, Left_pressed, Right_pressed, Confirm_pressed, Rotate_pressed);
  DotMatrix #(.matrixcols(1), .matrixrows(1), .persist(2048)) dotmatrix_1 (.col0(Up_pressed));
  Comparator #(.width(7), .mode("unsigned")) comparator_1 (
    .a(7'b1110111), .b(Keyboard_out), .eq(Up_pressed));  // open: gt, lt
  DotMatrix #(.matrixcols(1), .matrixrows(1), .persist(2048)) dotmatrix_2 (.col0(Down_pressed));
  Comparator #(.width(7), .mode("unsigned")) comparator_2 (
    .a(7'b1110011), .b(Keyboard_out), .eq(Down_pressed));  // open: gt, lt
  DotMatrix #(.matrixcols(1), .matrixrows(1), .persist(2048)) dotmatrix_3 (.col0(Left_pressed));
  Comparator #(.width(7), .mode("unsigned")) comparator_3 (
    .a(7'b1100001), .b(Keyboard_out), .eq(Left_pressed));  // open: gt, lt
  DotMatrix #(.matrixcols(1), .matrixrows(1), .persist(2048)) dotmatrix_4 (.col0(Right_pressed));
  Comparator #(.width(7), .mode("unsigned")) comparator_4 (
    .a(7'b1100100), .b(Keyboard_out), .eq(Right_pressed));  // open: gt, lt
  DotMatrix #(.matrixcols(1), .matrixrows(1), .persist(2048)) dotmatrix_5 (.col0(Confirm_pressed));
  Comparator #(.width(7), .mode("unsigned")) comparator_5 (
    .a(7'b0001010), .b(Keyboard_out), .eq(Confirm_pressed));  // open: gt, lt
  DotMatrix #(.matrixcols(1), .matrixrows(1), .persist(2048)) dotmatrix_6 (.col0(Rotate_pressed));
  Comparator #(.width(7), .mode("unsigned")) comparator_6 (
    .a(7'b1110010), .b(Keyboard_out), .eq(Rotate_pressed));  // open: gt, lt

  // Notes on the sheet:
  //   Confirm (enter)
  //   Up (W)
  //   Down (S)
  //   Left (A)
  //   Right (D)
  //   Rotate (r)
  //   Tak, to dziala.
endmodule
