// Logisim project SRlatch.circ as structural Verilog: 1 circuit, main circuit main
module main (
  input  RESTET,
  input  SET,
  output Q
);

  wire clock_1_out, counter_1_carry, nor_2_out, not_1_out, or_1_out;

  Counter #(.width(1), .max('h1), .ongoal("stay")) counter_1 (
    .carry(counter_1_carry), .clk(clock_1_out));  // open: load, D, count, Q, clr
  Clock clock_1 (.out(clock_1_out));
  not not_1 (not_1_out, counter_1_carry);
  or or_1 (or_1_out, RESTET, not_1_out);
  nor nor_1 (Q, or_1_out, nor_2_out);
  nor nor_2 (nor_2_out, Q, SET);
endmodule
