// Logisim project TEST2.circ as structural Verilog: 1 circuit, main circuit main
module main (
  input  in_1,
  output out_2
);

  wire and_1_out, and_2_out, and_3_out, button_1_out, CHECKING, CLK, comparator_1_gt, comparator_2_eq,
       comparator_2_lt, CONFIRM, counter_1_carry, counter_3_q, CURR_SEG_ALIVE, DOT_ADDED, HIT, NEXT_SHIP,
       ROTATED, SHIP_DRAW_ENABLE, undriven;
  wire [1:0] SEGMENT_SEL, SHIP_TYPE;
  wire [2:0] SHIP_DRAW_SEL;
  wire [3:0] ALIVE, CURR_SHIP_ADD, CURSOR_X, CURSOR_Y, SHIP_X, SHIP_Y;
  wire [4:0] BL_SEL, BL_SEL1, BL_SEL2, BR_SEL, BR_SEL1, BR_SEL2, main_6_output1, main_6_output2,
       main_6_output3, main_6_output4, main_6_output5, main_6_output6, main_6_output7, main_6_output8,
       TL_SEL, TL_SEL1, TL_SEL2, TR_SEL, TR_SEL1, TR_SEL2;
  wire [5:0] main_4_out_x_00, main_4_out_x_01, main_4_out_x_10, main_4_out_x_11, main_4_out_y_00,
       main_4_out_y_01, main_4_out_y_10, main_4_out_y_11, SHIP_SCR_X, SHIP_SCR_Y;
  wire [6:0] keyboard_1_data;
  wire [29:0] BL_DATA, BL_DATA1, BL_DATA2, BR_DATA, BR_DATA1, BR_DATA2, main_7_out_0, main_7_out_1,
       main_7_out_1a, main_7_out_1b, main_7_out_1c, main_7_out_1d, main_7_out_2, main_7_out_3, main_7_out_4,
       main_7_out_5, main_7_out_6, main_7_out_7, main_7_out_8, main_7_out_9, main_7_out_10, main_7_out_11,
       main_7_out_12, main_7_out_13, main_7_out_14, main_7_out_15, main_7_out_16, main_7_out_17,
       main_7_out_18, main_7_out_19, main_7_out_a, main_7_out_b, main_7_out_c, main_7_out_d, main_7_out_e,
       main_7_out_f, main_8_out_0, main_8_out_1, main_8_out_1a, main_8_out_1b, main_8_out_1c, main_8_out_1d,
       main_8_out_2, main_8_out_3, main_8_out_4, main_8_out_5, main_8_out_6, main_8_out_7, main_8_out_8,
       main_8_out_9, main_8_out_10, main_8_out_11, main_8_out_12, main_8_out_13, main_8_out_14,
       main_8_out_15, main_8_out_16, main_8_out_17, main_8_out_18, main_8_out_19, main_8_out_a, main_8_out_b,
       main_8_out_c, main_8_out_d, main_8_out_e, main_8_out_f, main_9_out_0, main_9_out_1, main_9_out_1a,
       main_9_out_1b, main_9_out_1c, main_9_out_1d, main_9_out_2, main_9_out_3, main_9_out_4, main_9_out_5,
       main_9_out_6, main_9_out_7, main_9_out_8, main_9_out_9, main_9_out_10, main_9_out_11, main_9_out_12,
       main_9_out_13, main_9_out_14, main_9_out_15, main_9_out_16, main_9_out_17, main_9_out_18,
       main_9_out_19, main_9_out_a, main_9_out_b, main_9_out_c, main_9_out_d, main_9_out_e, main_9_out_f,
       main_10_out_0, main_10_out_1, main_10_out_1a, main_10_out_1b, main_10_out_1c, main_10_out_1d,
       main_10_out_2, main_10_out_3, main_10_out_4, main_10_out_5, main_10_out_6, main_10_out_7,
       main_10_out_8, main_10_out_9, main_10_out_10, main_10_out_11, main_10_out_12, main_10_out_13,
       main_10_out_14, main_10_out_15, main_10_out_16, main_10_out_17, main_10_out_18, main_10_out_19,
       main_10_out_a, main_10_out_b, main_10_out_c, main_10_out_d, main_10_out_e, main_10_out_f, TL_DATA,
       TL_DATA1, TL_DATA2, TR_DATA, TR_DATA1, TR_DATA2;

  Clock clock_1 (.out(CLK));
  memory_management_main main_1 (
    .X(CURSOR_X), .Y(CURSOR_Y), .ROTATED(in_1), .RAM_OUT({ALIVE, ROTATED, SHIP_TYPE, SHIP_Y, SHIP_X}),
    .CHECK_X(CURSOR_X), .CHECK_Y(CURSOR_Y), .SINK_IF_HIT(1'b1), .CONFIRM(button_1_out), .CHECK(CONFIRM),
    .CLK(CLK), .SHOW_NEXT_SHIP(NEXT_SHIP), .WIN(out_2), .HIT(HIT), .CHECKING(CHECKING),
    .CURR_SHIP_ADD(CURR_SHIP_ADD));
  Button button_1 (.out(button_1_out));
  Keyboard keyboard_1 (.clk(CLK), .clr(undriven), .data(keyboard_1_data));  // open: re, avail
  cursor_module_main main_2 (
    .CUR_X(CURSOR_X), .CUR_Y(CURSOR_Y), .CLK(CLK), .KEYBOARD_OUT(keyboard_1_data), .KEYBOARD_RST(undriven),
    .TL_SEL(TL_SEL1), .TR_SEL(TR_SEL1), .BL_SEL(BL_SEL1), .BR_SEL(BR_SEL1), .TL_DATA(TL_DATA1),
    .TR_DATA(TR_DATA1), .BL_DATA(BL_DATA1), .BR_DATA(BR_DATA1), .CONFIRM(CONFIRM));
  and and_1 (and_1_out, ~HIT, ~CHECKING);  // AND_Gate
  Counter #(.width(3), .max('h4)) counter_1 (.carry(counter_1_carry), .clk(CLK));  // open: load, D, count, Q, clr
  not_hit_module_main main_3 (
    .nHIT_X(CURSOR_X), .nHIT_Y(CURSOR_Y), .nHIT(and_1_out), .CLK(CLK), .TL_DATA(TL_DATA2),
    .TR_DATA(TR_DATA2), .BL_DATA(BL_DATA2), .BR_DATA(BR_DATA2), .TL_SEL(TL_SEL2), .TR_SEL(TR_SEL2),
    .BL_SEL(BL_SEL2), .BR_SEL(BR_SEL2), .ADDED(DOT_ADDED));
  Counter #(.width(2), .max('h3)) counter_2 (
    .Q(SEGMENT_SEL), .carry(NEXT_SHIP), .clk(counter_1_carry));  // open: load, D, count, clr
  ship_xyr_to_screen_xy_main main_4 (
    .INPUT(SHIP_X), .in_2(SHIP_Y), .CONST(ROTATED), .OUT_X_00(main_4_out_x_00), .OUT_Y_00(main_4_out_y_00),
    .OUT_X_01(main_4_out_x_01), .OUT_Y_01(main_4_out_y_01), .OUT_X_10(main_4_out_x_10),
    .OUT_Y_10(main_4_out_y_10), .OUT_X_11(main_4_out_x_11), .OUT_Y_11(main_4_out_y_11));
  Comparator #(.width(4), .mode("unsigned")) comparator_1 (
    .a(CURR_SHIP_ADD), .b(4'b0000), .gt(comparator_1_gt));  // open: eq, lt
  Multiplexer #(.select(2), .enable("false")) multiplexer_1 (
    .in0(ALIVE[0]), .in1(ALIVE[1]), .in2(ALIVE[2]), .in3(ALIVE[3]), .out(CURR_SEG_ALIVE), .sel(SEGMENT_SEL));
  screen_xy_to_screen_data_main main_5 (
    .SCREEN_X(SHIP_SCR_X), .SCREEN_Y(SHIP_SCR_Y), .DATA_TO_DISPLAY(SHIP_DRAW_SEL), .TL_SEL_OUT(TL_SEL),
    .TR_SEL_OUT(TR_SEL), .BL_SEL_OUT(BL_SEL), .BR_SEL_OUT(BR_SEL), .TL_DATA_OUT(TL_DATA),
    .TR_DATA_OUT(TR_DATA), .BL_DATA_OUT(BL_DATA), .BR_DATA_OUT(BR_DATA), .CLK(CLK), .ENABLE(and_2_out));
  and and_2 (and_2_out, SHIP_DRAW_ENABLE, comparator_1_gt);
  Multiplexer #(.width(3), .enable("false")) multiplexer_2 (
    .in0(3'b010), .in1(3'b001), .out(SHIP_DRAW_SEL), .sel(CURR_SEG_ALIVE));
  Comparator #(.width(2), .mode("unsigned")) comparator_2 (
    .a(SEGMENT_SEL), .b(SHIP_TYPE), .eq(comparator_2_eq), .lt(comparator_2_lt));  // open: gt
  or or_1 (SHIP_DRAW_ENABLE, comparator_2_eq, comparator_2_lt);
  Counter #(.width(1), .max('h1)) counter_3 (.Q(counter_3_q), .clk(and_3_out));  // open: load, D, count, carry, clr
  DotMatrix #(.matrixcols(8), .matrixrows(5)) dotmatrix_1 (
    .col0(main_6_output8), .col1(main_6_output7), .col2(main_6_output6), .col3(main_6_output5),
    .col4(main_6_output4), .col5(main_6_output3), .col6(main_6_output2), .col7(main_6_output1));
  and and_3 (and_3_out, ~HIT, ~CHECKING, DOT_ADDED);  // AND_Gate
  Multiplexer #(.select(2), .width(6), .enable("false")) multiplexer_3 (
    .in0(main_4_out_x_00), .in1(main_4_out_x_01), .in2(main_4_out_x_10), .in3(main_4_out_x_11),
    .out(SHIP_SCR_X), .sel(SEGMENT_SEL));
  Multiplexer #(.select(2), .width(6), .enable("false")) multiplexer_4 (
    .in0(main_4_out_y_00), .in1(main_4_out_y_01), .in2(main_4_out_y_10), .in3(main_4_out_y_11),
    .out(SHIP_SCR_Y), .sel(SEGMENT_SEL));
  arrow_main main_6 (
    .\input (counter_3_q), .output2(main_6_output2), .output1(main_6_output1), .output3(main_6_output3),
    .output4(main_6_output4), .output5(main_6_output5), .output6(main_6_output6), .output7(main_6_output7),
    .output8(main_6_output8));
  DotMatrix #(.matrixcols(30), .matrixrows(30), .persist(500)) dotmatrix_2 (
    .col0(main_7_out_0), .col1(main_7_out_1), .col2(main_7_out_2), .col3(main_7_out_3), .col4(main_7_out_4),
    .col5(main_7_out_5), .col6(main_7_out_6), .col7(main_7_out_7), .col8(main_7_out_8), .col9(main_7_out_9),
    .col10(main_7_out_a), .col11(main_7_out_b), .col12(main_7_out_c), .col13(main_7_out_d),
    .col14(main_7_out_e), .col15(main_7_out_f), .col16(main_7_out_10), .col17(main_7_out_11),
    .col18(main_7_out_12), .col19(main_7_out_13), .col20(main_7_out_14), .col21(main_7_out_15),
    .col22(main_7_out_16), .col23(main_7_out_17), .col24(main_7_out_18), .col25(main_7_out_19),
    .col26(main_7_out_1a), .col27(main_7_out_1b), .col28(main_7_out_1c), .col29(main_7_out_1d));
  demuxor_30x30x3_main main_7 (
    .DATA_1(TL_DATA1), .SELECT_1(TL_SEL1), .SELECT_2(TL_SEL2), .DATA_2(TL_DATA2), .SELECT_0(TL_SEL),
    .DATA_0(TL_DATA), .OUT_0(main_7_out_0), .OUT_1(main_7_out_1), .OUT_2(main_7_out_2), .OUT_3(main_7_out_3),
    .OUT_4(main_7_out_4), .OUT_6(main_7_out_6), .OUT_7(main_7_out_7), .OUT_8(main_7_out_8),
    .OUT_9(main_7_out_9), .OUT_a(main_7_out_a), .OUT_c(main_7_out_c), .OUT_12(main_7_out_12),
    .OUT_d(main_7_out_d), .OUT_13(main_7_out_13), .OUT_e(main_7_out_e), .OUT_14(main_7_out_14),
    .OUT_f(main_7_out_f), .OUT_15(main_7_out_15), .OUT_10(main_7_out_10), .OUT_16(main_7_out_16),
    .OUT_18(main_7_out_18), .OUT_19(main_7_out_19), .OUT_1a(main_7_out_1a), .OUT_1b(main_7_out_1b),
    .OUT_1c(main_7_out_1c), .OUT_5(main_7_out_5), .OUT_b(main_7_out_b), .OUT_11(main_7_out_11),
    .OUT_17(main_7_out_17), .OUT_1d(main_7_out_1d));
  DotMatrix #(.matrixcols(30), .matrixrows(30), .persist(500)) dotmatrix_3 (
    .col0(main_8_out_0), .col1(main_8_out_1), .col2(main_8_out_2), .col3(main_8_out_3), .col4(main_8_out_4),
    .col5(main_8_out_5), .col6(main_8_out_6), .col7(main_8_out_7), .col8(main_8_out_8), .col9(main_8_out_9),
    .col10(main_8_out_a), .col11(main_8_out_b), .col12(main_8_out_c), .col13(main_8_out_d),
    .col14(main_8_out_e), .col15(main_8_out_f), .col16(main_8_out_10), .col17(main_8_out_11),
    .col18(main_8_out_12), .col19(main_8_out_13), .col20(main_8_out_14), .col21(main_8_out_15),
    .col22(main_8_out_16), .col23(main_8_out_17), .col24(main_8_out_18), .col25(main_8_out_19),
    .col26(main_8_out_1a), .col27(main_8_out_1b), .col28(main_8_out_1c), .col29(main_8_out_1d));
  demuxor_30x30x3_main main_8 (
    .DATA_1(BL_DATA1), .SELECT_1(BL_SEL1), .SELECT_2(BL_SEL2), .DATA_2(BL_DATA2), .SELECT_0(BL_SEL),
    .DATA_0(BL_DATA), .OUT_0(main_8_out_0), .OUT_1(main_8_out_1), .OUT_2(main_8_out_2), .OUT_3(main_8_out_3),
    .OUT_4(main_8_out_4), .OUT_6(main_8_out_6), .OUT_7(main_8_out_7), .OUT_8(main_8_out_8),
    .OUT_9(main_8_out_9), .OUT_a(main_8_out_a), .OUT_c(main_8_out_c), .OUT_12(main_8_out_12),
    .OUT_d(main_8_out_d), .OUT_13(main_8_out_13), .OUT_e(main_8_out_e), .OUT_14(main_8_out_14),
    .OUT_f(main_8_out_f), .OUT_15(main_8_out_15), .OUT_10(main_8_out_10), .OUT_16(main_8_out_16),
    .OUT_18(main_8_out_18), .OUT_19(main_8_out_19), .OUT_1a(main_8_out_1a), .OUT_1b(main_8_out_1b),
    .OUT_1c(main_8_out_1c), .OUT_5(main_8_out_5), .OUT_b(main_8_out_b), .OUT_11(main_8_out_11),
    .OUT_17(main_8_out_17), .OUT_1d(main_8_out_1d));
  DotMatrix #(.matrixcols(30), .matrixrows(30), .persist(500)) dotmatrix_4 (
    .col0(main_9_out_0), .col1(main_9_out_1), .col2(main_9_out_2), .col3(main_9_out_3), .col4(main_9_out_4),
    .col5(main_9_out_5), .col6(main_9_out_6), .col7(main_9_out_7), .col8(main_9_out_8), .col9(main_9_out_9),
    .col10(main_9_out_a), .col11(main_9_out_b), .col12(main_9_out_c), .col13(main_9_out_d),
    .col14(main_9_out_e), .col15(main_9_out_f), .col16(main_9_out_10), .col17(main_9_out_11),
    .col18(main_9_out_12), .col19(main_9_out_13), .col20(main_9_out_14), .col21(main_9_out_15),
    .col22(main_9_out_16), .col23(main_9_out_17), .col24(main_9_out_18), .col25(main_9_out_19),
    .col26(main_9_out_1a), .col27(main_9_out_1b), .col28(main_9_out_1c), .col29(main_9_out_1d));
  demuxor_30x30x3_main main_9 (
    .DATA_1(TR_DATA1), .SELECT_1(TR_SEL1), .SELECT_2(TR_SEL2), .DATA_2(TR_DATA2), .SELECT_0(TR_SEL),
    .DATA_0(TR_DATA), .OUT_0(main_9_out_0), .OUT_1(main_9_out_1), .OUT_2(main_9_out_2), .OUT_3(main_9_out_3),
    .OUT_4(main_9_out_4), .OUT_6(main_9_out_6), .OUT_7(main_9_out_7), .OUT_8(main_9_out_8),
    .OUT_9(main_9_out_9), .OUT_a(main_9_out_a), .OUT_c(main_9_out_c), .OUT_12(main_9_out_12),
    .OUT_d(main_9_out_d), .OUT_13(main_9_out_13), .OUT_e(main_9_out_e), .OUT_14(main_9_out_14),
    .OUT_f(main_9_out_f), .OUT_15(main_9_out_15), .OUT_10(main_9_out_10), .OUT_16(main_9_out_16),
    .OUT_18(main_9_out_18), .OUT_19(main_9_out_19), .OUT_1a(main_9_out_1a), .OUT_1b(main_9_out_1b),
    .OUT_1c(main_9_out_1c), .OUT_5(main_9_out_5), .OUT_b(main_9_out_b), .OUT_11(main_9_out_11),
    .OUT_17(main_9_out_17), .OUT_1d(main_9_out_1d));
  DotMatrix #(.matrixcols(30), .matrixrows(30), .persist(500)) dotmatrix_5 (
    .col0(main_10_out_0), .col1(main_10_out_1), .col2(main_10_out_2), .col3(main_10_out_3),
    .col4(main_10_out_4), .col5(main_10_out_5), .col6(main_10_out_6), .col7(main_10_out_7),
    .col8(main_10_out_8), .col9(main_10_out_9), .col10(main_10_out_a), .col11(main_10_out_b),
    .col12(main_10_out_c), .col13(main_10_out_d), .col14(main_10_out_e), .col15(main_10_out_f),
    .col16(main_10_out_10), .col17(main_10_out_11), .col18(main_10_out_12), .col19(main_10_out_13),
    .col20(main_10_out_14), .col21(main_10_out_15), .col22(main_10_out_16), .col23(main_10_out_17),
    .col24(main_10_out_18), .col25(main_10_out_19), .col26(main_10_out_1a), .col27(main_10_out_1b),
    .col28(main_10_out_1c), .col29(main_10_out_1d));
  demuxor_30x30x3_main main_10 (
    .DATA_1(BR_DATA1), .SELECT_1(BR_SEL1), .SELECT_2(BR_SEL2), .DATA_2(BR_DATA2), .SELECT_0(BR_SEL),
    .DATA_0(BR_DATA), .OUT_0(main_10_out_0), .OUT_1(main_10_out_1), .OUT_2(main_10_out_2),
    .OUT_3(main_10_out_3), .OUT_4(main_10_out_4), .OUT_6(main_10_out_6), .OUT_7(main_10_out_7),
    .OUT_8(main_10_out_8), .OUT_9(main_10_out_9), .OUT_a(main_10_out_a), .OUT_c(main_10_out_c),
    .OUT_12(main_10_out_12), .OUT_d(main_10_out_d), .OUT_13(main_10_out_13), .OUT_e(main_10_out_e),
    .OUT_14(main_10_out_14), .OUT_f(main_10_out_f), .OUT_15(main_10_out_15), .OUT_10(main_10_out_10),
    .OUT_16(main_10_out_16), .OUT_18(main_10_out_18), .OUT_19(main_10_out_19), .OUT_1a(main_10_out_1a),
    .OUT_1b(main_10_out_1b), .OUT_1c(main_10_out_1c), .OUT_5(main_10_out_5), .OUT_b(main_10_out_b),
    .OUT_11(main_10_out_11), .OUT_17(main_10_out_17), .OUT_1d(main_10_out_1d));

  // Notes on the sheet:
  //   ^ tu enemy cursor bd podlaczony potem
  //   sunk
  //   alive
  //   ^ do tego mozna done dodac ze skonczyl rysowac
endmodule
