// Logisim project TEST_7SEG_DISP.circ as structural Verilog: 1 circuit, main circuit main
module main (
);

  wire clock_1_out, main_1_out_2, main_1_out_3, main_1_out_4, main_1_out_5, main_1_out_6, main_1_out_7,
       main_1_out_8, main_1_out_9, main_1_out_10, main_1_out_11, main_1_out_12, main_1_out_13, main_1_out_14,
       main_1_out_15, main_1_out_16, main_1_out_17, main_1_out_18, main_1_out_19, main_1_out_20,
       main_1_out_21, main_1_out_22, main_1_out_23, main_1_out_24, main_1_out_25, main_1_out_26,
       main_1_out_27, main_1_out_28, main_1_out_29, main_1_out_30, main_1_out_31, main_1_out_32,
       main_1_out_33;
  wire [9:0] counter_1_q;

  Counter #(.width(10), .max('h3ff)) counter_1 (
    .Q(counter_1_q), .clk(clock_1_out));  // open: load, D, count, carry, clr
  Clock clock_1 (.out(clock_1_out));
  _7_Segment_Display u_7_segment_display_1 (
    .g(main_1_out_14), .f(main_1_out_15), .a(main_1_out_16), .b(main_1_out_17), .e(main_1_out_30),
    .d(main_1_out_31), .c(main_1_out_32), .dp(main_1_out_33));
  secs_to_score_main main_1 (
    .SECS_IPT(counter_1_q), .out_10(main_1_out_10), .out_11(main_1_out_11), .out_12(main_1_out_12),
    .out_13(main_1_out_13), .out_26(main_1_out_26), .out_27(main_1_out_27), .out_28(main_1_out_28),
    .out_29(main_1_out_29), .out_14(main_1_out_14), .out_15(main_1_out_15), .out_16(main_1_out_16),
    .out_17(main_1_out_17), .out_30(main_1_out_30), .out_31(main_1_out_31), .out_32(main_1_out_32),
    .out_33(main_1_out_33), .out_2(main_1_out_2), .out_3(main_1_out_3), .out_4(main_1_out_4),
    .out_5(main_1_out_5), .out_18(main_1_out_18), .out_19(main_1_out_19), .out_20(main_1_out_20),
    .out_21(main_1_out_21), .out_6(main_1_out_6), .out_7(main_1_out_7), .out_8(main_1_out_8),
    .out_9(main_1_out_9), .out_22(main_1_out_22), .out_23(main_1_out_23), .out_24(main_1_out_24),
    .out_25(main_1_out_25));
  _7_Segment_Display u_7_segment_display_2 (
    .g(main_1_out_10), .f(main_1_out_11), .a(main_1_out_12), .b(main_1_out_13), .e(main_1_out_26),
    .d(main_1_out_27), .c(main_1_out_28), .dp(main_1_out_29));
  _7_Segment_Display u_7_segment_display_3 (
    .g(main_1_out_6), .f(main_1_out_7), .a(main_1_out_8), .b(main_1_out_9), .e(main_1_out_22),
    .d(main_1_out_23), .c(main_1_out_24), .dp(main_1_out_25));
  _7_Segment_Display u_7_segment_display_4 (
    .g(main_1_out_2), .f(main_1_out_3), .a(main_1_out_4), .b(main_1_out_5), .e(main_1_out_18),
    .d(main_1_out_19), .c(main_1_out_20), .dp(main_1_out_21));
endmodule
