// Logisim project app.circ as structural Verilog: 1 circuit, main circuit main
module main (
);

  wire and_1_out, and_2_out, and_3_out, and_5_out, and_6_out, and_7_out, and_8_out, and_11_out, and_12_out,
       and_13_out, and_14_out, and_15_out, and_16_out, and_17_out, and_18_out, and_19_out, and_20_out,
       and_21_out, and_22_out, CLK, CLK_5, comparator_1_eq, comparator_2_eq, comparator_3_gt,
       comparator_4_gt, comparator_5_eq, comparator_5_lt, comparator_6_gt, comparator_7_gt, comparator_8_eq,
       comparator_8_lt, CURR_PLAYER, main_2_confirm, main_17_confirm, not_1_out, not_2_out, not_3_out,
       not_4_out, not_5_out, not_6_out, not_7_out, not_8_out, or_3_out, P1_ADD_SHIP, P1_CHECK_SHIP,
       P1_CHECKING, P1_CONF, P1_CURR_SEG_ALIVE, P1_DOT_ADDED, P1_HIT, P1_NEXT_SHIP, P1_RO_ROTATED,
       P1_ROTATED, P1_SHIP_DRAW_ENABLE, P1_WIN, P2_ADD_SHIP, P2_CHECK_SHIP, P2_CHECKING, P2_CONF,
       P2_CURR_SEG_ALIVE, P2_DOT_ADDED, P2_HIT, P2_NEXT_SHIP, P2_RO_ROTATED, P2_ROTATED, P2_SHIP_DRAW_ENABLE,
       P2_WIN, PREP_PHASE_END, undriven, undriven_2;
  wire [1:0] P1_RO_SHIP_TYPE, P1_SEG_SEL, P2_RO_SHIP_TYPE, P2_SEG_SEL;
  wire [2:0] P1_SHIP_DRAW_ON_ENEMY_SEL, P1_SHIP_DRAW_SEL, P2_SHIP_DRAW_ON_ENEMY_SEL, P2_SHIP_DRAW_SEL;
  wire [3:0] P1_CUR_X, P1_CUR_Y, P1_CURR_SHIP_ADD, P1_RO_ALIVE, P1_RO_SHIP_X, P1_RO_SHIP_Y, P2_CUR_X,
       P2_CUR_Y, P2_CURR_SHIP_ADD, P2_RO_ALIVE, P2_RO_SHIP_X, P2_RO_SHIP_Y;
  wire [4:0] main_15_output1, main_15_output2, main_15_output3, main_15_output4, main_15_output5,
       main_15_output6, main_15_output7, main_15_output8, P1_CUR_BL_SEL, P1_CUR_BR_SEL, P1_CUR_TL_SEL,
       P1_CUR_TR_SEL, P1_DOT_BL_SEL, P1_DOT_BR_SEL, P1_DOT_TL_SEL, P1_DOT_TR_SEL, P1_SHIP_BL_SEL,
       P1_SHIP_BR_SEL, P1_SHIP_ON_EN_BL_SEL, P1_SHIP_ON_EN_BR_SEL, P1_SHIP_ON_EN_TL_SEL,
       P1_SHIP_ON_EN_TR_SEL, P1_SHIP_TL_SEL, P1_SHIP_TR_SEL, P2_CUR_BL_SEL, P2_CUR_BR_SEL, P2_CUR_TL_SEL,
       P2_CUR_TR_SEL, P2_DOT_BL_SEL, P2_DOT_BR_SEL, P2_DOT_TL_SEL, P2_DOT_TR_SEL, P2_SHIP_BL_SEL,
       P2_SHIP_BR_SEL, P2_SHIP_ON_EN_BL_SEL, P2_SHIP_ON_EN_BR_SEL, P2_SHIP_ON_EN_TL_SEL,
       P2_SHIP_ON_EN_TR_SEL, P2_SHIP_TL_SEL, P2_SHIP_TR_SEL;
  wire [5:0] main_12_out_x_00, main_12_out_x_01, main_12_out_x_10, main_12_out_x_11, main_12_out_y_00,
       main_12_out_y_01, main_12_out_y_10, main_12_out_y_11, main_27_out_x_00, main_27_out_x_01,
       main_27_out_x_10, main_27_out_x_11, main_27_out_y_00, main_27_out_y_01, main_27_out_y_10,
       main_27_out_y_11, P1_SHIP_SCR_X, P1_SHIP_SCR_Y, P2_SHIP_SCR_X, P2_SHIP_SCR_Y;
  wire [6:0] keyboard_1_data, keyboard_2_data;
  wire [29:0] controlled_buffer_1_out, controlled_buffer_2_out, controlled_buffer_3_out,
       controlled_buffer_4_out, controlled_buffer_5_out, controlled_buffer_6_out, controlled_buffer_7_out,
       controlled_buffer_8_out, controlled_buffer_9_out, controlled_buffer_10_out, controlled_buffer_11_out,
       controlled_buffer_12_out, controlled_buffer_13_out, controlled_buffer_14_out,
       controlled_buffer_15_out, controlled_buffer_16_out, main_3_out_0, main_3_out_1, main_3_out_1a,
       main_3_out_1b, main_3_out_1c, main_3_out_1d, main_3_out_2, main_3_out_3, main_3_out_4, main_3_out_5,
       main_3_out_6, main_3_out_7, main_3_out_8, main_3_out_9, main_3_out_10, main_3_out_11, main_3_out_12,
       main_3_out_13, main_3_out_14, main_3_out_15, main_3_out_16, main_3_out_17, main_3_out_18,
       main_3_out_19, main_3_out_a, main_3_out_b, main_3_out_c, main_3_out_d, main_3_out_e, main_3_out_f,
       main_4_out_0, main_4_out_1, main_4_out_1a, main_4_out_1b, main_4_out_1c, main_4_out_1d, main_4_out_2,
       main_4_out_3, main_4_out_4, main_4_out_5, main_4_out_6, main_4_out_7, main_4_out_8, main_4_out_9,
       main_4_out_10, main_4_out_11, main_4_out_12, main_4_out_13, main_4_out_14, main_4_out_15,
       main_4_out_16, main_4_out_17, main_4_out_18, main_4_out_19, main_4_out_a, main_4_out_b, main_4_out_c,
       main_4_out_d, main_4_out_e, main_4_out_f, main_5_out_0, main_5_out_1, main_5_out_1a, main_5_out_1b,
       main_5_out_1c, main_5_out_1d, main_5_out_2, main_5_out_3, main_5_out_4, main_5_out_5, main_5_out_6,
       main_5_out_7, main_5_out_8, main_5_out_9, main_5_out_10, main_5_out_11, main_5_out_12, main_5_out_13,
       main_5_out_14, main_5_out_15, main_5_out_16, main_5_out_17, main_5_out_18, main_5_out_19,
       main_5_out_a, main_5_out_b, main_5_out_c, main_5_out_d, main_5_out_e, main_5_out_f, main_6_out_0,
       main_6_out_1, main_6_out_1a, main_6_out_1b, main_6_out_1c, main_6_out_1d, main_6_out_2, main_6_out_3,
       main_6_out_4, main_6_out_5, main_6_out_6, main_6_out_7, main_6_out_8, main_6_out_9, main_6_out_10,
       main_6_out_11, main_6_out_12, main_6_out_13, main_6_out_14, main_6_out_15, main_6_out_16,
       main_6_out_17, main_6_out_18, main_6_out_19, main_6_out_a, main_6_out_b, main_6_out_c, main_6_out_d,
       main_6_out_e, main_6_out_f, main_8_out_0, main_8_out_1, main_8_out_1a, main_8_out_1b, main_8_out_1c,
       main_8_out_1d, main_8_out_2, main_8_out_3, main_8_out_4, main_8_out_5, main_8_out_6, main_8_out_7,
       main_8_out_8, main_8_out_9, main_8_out_10, main_8_out_11, main_8_out_12, main_8_out_13, main_8_out_14,
       main_8_out_15, main_8_out_16, main_8_out_17, main_8_out_18, main_8_out_19, main_8_out_a, main_8_out_b,
       main_8_out_c, main_8_out_d, main_8_out_e, main_8_out_f, main_9_out_0, main_9_out_1, main_9_out_1a,
       main_9_out_1b, main_9_out_1c, main_9_out_1d, main_9_out_2, main_9_out_3, main_9_out_4, main_9_out_5,
       main_9_out_6, main_9_out_7, main_9_out_8, main_9_out_9, main_9_out_10, main_9_out_11, main_9_out_12,
       main_9_out_13, main_9_out_14, main_9_out_15, main_9_out_16, main_9_out_17, main_9_out_18,
       main_9_out_19, main_9_out_a, main_9_out_b, main_9_out_c, main_9_out_d, main_9_out_e, main_9_out_f,
       main_10_out_0, main_10_out_1, main_10_out_1a, main_10_out_1b, main_10_out_1c, main_10_out_1d,
       main_10_out_2, main_10_out_3, main_10_out_4, main_10_out_5, main_10_out_6, main_10_out_7,
       main_10_out_8, main_10_out_9, main_10_out_10, main_10_out_11, main_10_out_12, main_10_out_13,
       main_10_out_14, main_10_out_15, main_10_out_16, main_10_out_17, main_10_out_18, main_10_out_19,
       main_10_out_a, main_10_out_b, main_10_out_c, main_10_out_d, main_10_out_e, main_10_out_f,
       main_11_out_0, main_11_out_1, main_11_out_1a, main_11_out_1b, main_11_out_1c, main_11_out_1d,
       main_11_out_2, main_11_out_3, main_11_out_4, main_11_out_5, main_11_out_6, main_11_out_7,
       main_11_out_8, main_11_out_9, main_11_out_10, main_11_out_11, main_11_out_12, main_11_out_13,
       main_11_out_14, main_11_out_15, main_11_out_16, main_11_out_17, main_11_out_18, main_11_out_19,
       main_11_out_a, main_11_out_b, main_11_out_c, main_11_out_d, main_11_out_e, main_11_out_f,
       main_18_out_0, main_18_out_1, main_18_out_1a, main_18_out_1b, main_18_out_1c, main_18_out_1d,
       main_18_out_2, main_18_out_3, main_18_out_4, main_18_out_5, main_18_out_6, main_18_out_7,
       main_18_out_8, main_18_out_9, main_18_out_10, main_18_out_11, main_18_out_12, main_18_out_13,
       main_18_out_14, main_18_out_15, main_18_out_16, main_18_out_17, main_18_out_18, main_18_out_19,
       main_18_out_a, main_18_out_b, main_18_out_c, main_18_out_d, main_18_out_e, main_18_out_f,
       main_19_out_0, main_19_out_1, main_19_out_1a, main_19_out_1b, main_19_out_1c, main_19_out_1d,
       main_19_out_2, main_19_out_3, main_19_out_4, main_19_out_5, main_19_out_6, main_19_out_7,
       main_19_out_8, main_19_out_9, main_19_out_10, main_19_out_11, main_19_out_12, main_19_out_13,
       main_19_out_14, main_19_out_15, main_19_out_16, main_19_out_17, main_19_out_18, main_19_out_19,
       main_19_out_a, main_19_out_b, main_19_out_c, main_19_out_d, main_19_out_e, main_19_out_f,
       main_20_out_0, main_20_out_1, main_20_out_1a, main_20_out_1b, main_20_out_1c, main_20_out_1d,
       main_20_out_2, main_20_out_3, main_20_out_4, main_20_out_5, main_20_out_6, main_20_out_7,
       main_20_out_8, main_20_out_9, main_20_out_10, main_20_out_11, main_20_out_12, main_20_out_13,
       main_20_out_14, main_20_out_15, main_20_out_16, main_20_out_17, main_20_out_18, main_20_out_19,
       main_20_out_a, main_20_out_b, main_20_out_c, main_20_out_d, main_20_out_e, main_20_out_f,
       main_21_out_0, main_21_out_1, main_21_out_1a, main_21_out_1b, main_21_out_1c, main_21_out_1d,
       main_21_out_2, main_21_out_3, main_21_out_4, main_21_out_5, main_21_out_6, main_21_out_7,
       main_21_out_8, main_21_out_9, main_21_out_10, main_21_out_11, main_21_out_12, main_21_out_13,
       main_21_out_14, main_21_out_15, main_21_out_16, main_21_out_17, main_21_out_18, main_21_out_19,
       main_21_out_a, main_21_out_b, main_21_out_c, main_21_out_d, main_21_out_e, main_21_out_f,
       main_23_out_0, main_23_out_1, main_23_out_1a, main_23_out_1b, main_23_out_1c, main_23_out_1d,
       main_23_out_2, main_23_out_3, main_23_out_4, main_23_out_5, main_23_out_6, main_23_out_7,
       main_23_out_8, main_23_out_9, main_23_out_10, main_23_out_11, main_23_out_12, main_23_out_13,
       main_23_out_14, main_23_out_15, main_23_out_16, main_23_out_17, main_23_out_18, main_23_out_19,
       main_23_out_a, main_23_out_b, main_23_out_c, main_23_out_d, main_23_out_e, main_23_out_f,
       main_24_out_0, main_24_out_1, main_24_out_1a, main_24_out_1b, main_24_out_1c, main_24_out_1d,
       main_24_out_2, main_24_out_3, main_24_out_4, main_24_out_5, main_24_out_6, main_24_out_7,
       main_24_out_8, main_24_out_9, main_24_out_10, main_24_out_11, main_24_out_12, main_24_out_13,
       main_24_out_14, main_24_out_15, main_24_out_16, main_24_out_17, main_24_out_18, main_24_out_19,
       main_24_out_a, main_24_out_b, main_24_out_c, main_24_out_d, main_24_out_e, main_24_out_f,
       main_25_out_0, main_25_out_1, main_25_out_1a, main_25_out_1b, main_25_out_1c, main_25_out_1d,
       main_25_out_2, main_25_out_3, main_25_out_4, main_25_out_5, main_25_out_6, main_25_out_7,
       main_25_out_8, main_25_out_9, main_25_out_10, main_25_out_11, main_25_out_12, main_25_out_13,
       main_25_out_14, main_25_out_15, main_25_out_16, main_25_out_17, main_25_out_18, main_25_out_19,
       main_25_out_a, main_25_out_b, main_25_out_c, main_25_out_d, main_25_out_e, main_25_out_f,
       main_26_out_0, main_26_out_1, main_26_out_1a, main_26_out_1b, main_26_out_1c, main_26_out_1d,
       main_26_out_2, main_26_out_3, main_26_out_4, main_26_out_5, main_26_out_6, main_26_out_7,
       main_26_out_8, main_26_out_9, main_26_out_10, main_26_out_11, main_26_out_12, main_26_out_13,
       main_26_out_14, main_26_out_15, main_26_out_16, main_26_out_17, main_26_out_18, main_26_out_19,
       main_26_out_a, main_26_out_b, main_26_out_c, main_26_out_d, main_26_out_e, main_26_out_f,
       P1_CUR_BL_DATA, P1_CUR_BR_DATA, P1_CUR_TL_DATA, P1_CUR_TR_DATA, P1_DOT_BL_DATA, P1_DOT_BR_DATA,
       P1_DOT_TL_DATA, P1_DOT_TR_DATA, P1_SHIP_BL_DATA, P1_SHIP_BR_DATA, P1_SHIP_ON_EN_BL_DATA,
       P1_SHIP_ON_EN_BR_DATA, P1_SHIP_ON_EN_TL_DATA, P1_SHIP_ON_EN_TR_DATA, P1_SHIP_TL_DATA, P1_SHIP_TR_DATA,
       P2_CUR_BL_DATA, P2_CUR_BR_DATA, P2_CUR_TL_DATA, P2_CUR_TR_DATA, P2_DOT_BL_DATA, P2_DOT_BR_DATA,
       P2_DOT_TL_DATA, P2_DOT_TR_DATA, P2_SHIP_BL_DATA, P2_SHIP_BR_DATA, P2_SHIP_ON_EN_BL_DATA,
       P2_SHIP_ON_EN_BR_DATA, P2_SHIP_ON_EN_TL_DATA, P2_SHIP_ON_EN_TR_DATA, P2_SHIP_TL_DATA, P2_SHIP_TR_DATA;

  Clock clock_1 (.out(CLK));
  Counter #(.width(3), .max('h4)) counter_1 (.carry(CLK_5), .clk(CLK));  // open: load, D, count, Q, clr
  Counter #(.width(2), .max('h3)) counter_2 (
    .Q(P1_SEG_SEL), .carry(P1_NEXT_SHIP), .clk(CLK_5));  // open: load, D, count, clr
  memory_management_main main_1 (
    .X(P1_CUR_X), .Y(P1_CUR_Y), .ROTATED(P1_ROTATED),
    .RAM_OUT({P1_RO_ALIVE, P1_RO_ROTATED, P1_RO_SHIP_TYPE, P1_RO_SHIP_Y, P1_RO_SHIP_X}), .CHECK_X(P2_CUR_X),
    .CHECK_Y(P2_CUR_Y), .SINK_IF_HIT(1'b1), .CONFIRM(P1_ADD_SHIP), .CHECK(P2_CHECK_SHIP), .CLK(CLK),
    .SHOW_NEXT_SHIP(P1_NEXT_SHIP), .WIN(P1_WIN), .HIT(P1_HIT), .CHECKING(P1_CHECKING),
    .CURR_SHIP_ADD(P1_CURR_SHIP_ADD));
  Keyboard keyboard_1 (.clk(CLK), .clr(undriven), .data(keyboard_1_data));  // open: re, avail
  cursor_module_main main_2 (
    .CUR_X(P1_CUR_X), .CLK(CLK), .KEYBOARD_OUT(keyboard_1_data), .KEYBOARD_RST(undriven),
    .TL_SEL(P1_CUR_TL_SEL), .TR_SEL(P1_CUR_TR_SEL), .BL_SEL(P1_CUR_BL_SEL), .BR_SEL(P1_CUR_BR_SEL),
    .TL_DATA(P1_CUR_TL_DATA), .TR_DATA(P1_CUR_TR_DATA), .BL_DATA(P1_CUR_BL_DATA), .BR_DATA(P1_CUR_BR_DATA),
    .CONFIRM(main_2_confirm), .CUR_Y(P1_CUR_Y), .ROTATED(P1_ROTATED));
  and and_1 (and_1_out, ~P1_HIT, ~P1_CHECKING, PREP_PHASE_END);  // AND_Gate
  DotMatrix #(.matrixcols(30), .matrixrows(30), .persist(500)) dotmatrix_1 (
    .col0(main_3_out_0), .col1(main_3_out_1), .col2(main_3_out_2), .col3(main_3_out_3), .col4(main_3_out_4),
    .col5(main_3_out_5), .col6(main_3_out_6), .col7(main_3_out_7), .col8(main_3_out_8), .col9(main_3_out_9),
    .col10(main_3_out_a), .col11(main_3_out_b), .col12(main_3_out_c), .col13(main_3_out_d),
    .col14(main_3_out_e), .col15(main_3_out_f), .col16(main_3_out_10), .col17(main_3_out_11),
    .col18(main_3_out_12), .col19(main_3_out_13), .col20(main_3_out_14), .col21(main_3_out_15),
    .col22(main_3_out_16), .col23(main_3_out_17), .col24(main_3_out_18), .col25(main_3_out_19),
    .col26(main_3_out_1a), .col27(main_3_out_1b), .col28(main_3_out_1c), .col29(main_3_out_1d));
  demuxor_30x30x3_main main_3 (
    .DATA_1(P1_SHIP_TL_DATA), .SELECT_1(P1_SHIP_TL_SEL), .SELECT_2(P2_DOT_TL_SEL), .DATA_2(P2_DOT_TL_DATA),
    .SELECT_0(P1_CUR_TL_SEL), .DATA_0(controlled_buffer_1_out), .OUT_0(main_3_out_0), .OUT_1(main_3_out_1),
    .OUT_2(main_3_out_2), .OUT_3(main_3_out_3), .OUT_4(main_3_out_4), .OUT_6(main_3_out_6),
    .OUT_7(main_3_out_7), .OUT_8(main_3_out_8), .OUT_9(main_3_out_9), .OUT_a(main_3_out_a),
    .OUT_c(main_3_out_c), .OUT_12(main_3_out_12), .OUT_d(main_3_out_d), .OUT_13(main_3_out_13),
    .OUT_e(main_3_out_e), .OUT_14(main_3_out_14), .OUT_f(main_3_out_f), .OUT_15(main_3_out_15),
    .OUT_10(main_3_out_10), .OUT_16(main_3_out_16), .OUT_18(main_3_out_18), .OUT_19(main_3_out_19),
    .OUT_1a(main_3_out_1a), .OUT_1b(main_3_out_1b), .OUT_1c(main_3_out_1c), .OUT_5(main_3_out_5),
    .OUT_b(main_3_out_b), .OUT_11(main_3_out_11), .OUT_17(main_3_out_17), .OUT_1d(main_3_out_1d));
  assign controlled_buffer_1_out = not_1_out ? P1_CUR_TL_DATA : 30'bz;  // Controlled_Buffer controlled_buffer_1
  not not_1 (not_1_out, PREP_PHASE_END);
  DotMatrix #(.matrixcols(30), .matrixrows(30), .persist(500)) dotmatrix_2 (
    .col0(main_4_out_0), .col1(main_4_out_1), .col2(main_4_out_2), .col3(main_4_out_3), .col4(main_4_out_4),
    .col5(main_4_out_5), .col6(main_4_out_6), .col7(main_4_out_7), .col8(main_4_out_8), .col9(main_4_out_9),
    .col10(main_4_out_a), .col11(main_4_out_b), .col12(main_4_out_c), .col13(main_4_out_d),
    .col14(main_4_out_e), .col15(main_4_out_f), .col16(main_4_out_10), .col17(main_4_out_11),
    .col18(main_4_out_12), .col19(main_4_out_13), .col20(main_4_out_14), .col21(main_4_out_15),
    .col22(main_4_out_16), .col23(main_4_out_17), .col24(main_4_out_18), .col25(main_4_out_19),
    .col26(main_4_out_1a), .col27(main_4_out_1b), .col28(main_4_out_1c), .col29(main_4_out_1d));
  demuxor_30x30x3_main main_4 (
    .DATA_1(P1_SHIP_BL_DATA), .SELECT_1(P1_SHIP_BL_SEL), .SELECT_2(P2_DOT_BL_SEL), .DATA_2(P2_DOT_BL_DATA),
    .SELECT_0(P1_CUR_BL_SEL), .DATA_0(controlled_buffer_2_out), .OUT_0(main_4_out_0), .OUT_1(main_4_out_1),
    .OUT_2(main_4_out_2), .OUT_3(main_4_out_3), .OUT_4(main_4_out_4), .OUT_6(main_4_out_6),
    .OUT_7(main_4_out_7), .OUT_8(main_4_out_8), .OUT_9(main_4_out_9), .OUT_a(main_4_out_a),
    .OUT_c(main_4_out_c), .OUT_12(main_4_out_12), .OUT_d(main_4_out_d), .OUT_13(main_4_out_13),
    .OUT_e(main_4_out_e), .OUT_14(main_4_out_14), .OUT_f(main_4_out_f), .OUT_15(main_4_out_15),
    .OUT_10(main_4_out_10), .OUT_16(main_4_out_16), .OUT_18(main_4_out_18), .OUT_19(main_4_out_19),
    .OUT_1a(main_4_out_1a), .OUT_1b(main_4_out_1b), .OUT_1c(main_4_out_1c), .OUT_5(main_4_out_5),
    .OUT_b(main_4_out_b), .OUT_11(main_4_out_11), .OUT_17(main_4_out_17), .OUT_1d(main_4_out_1d));
  assign controlled_buffer_2_out = not_2_out ? P1_CUR_BL_DATA : 30'bz;  // Controlled_Buffer controlled_buffer_2
  not not_2 (not_2_out, PREP_PHASE_END);
  demuxor_30x30x3_main main_5 (
    .DATA_1(P2_SHIP_ON_EN_TL_DATA), .SELECT_1(P2_SHIP_ON_EN_TL_SEL), .SELECT_2(P1_DOT_TL_SEL),
    .DATA_2(P1_DOT_TL_DATA), .SELECT_0(P1_CUR_TL_SEL), .DATA_0(controlled_buffer_3_out),
    .OUT_0(main_5_out_0), .OUT_1(main_5_out_1), .OUT_2(main_5_out_2), .OUT_3(main_5_out_3),
    .OUT_4(main_5_out_4), .OUT_6(main_5_out_6), .OUT_7(main_5_out_7), .OUT_8(main_5_out_8),
    .OUT_9(main_5_out_9), .OUT_a(main_5_out_a), .OUT_c(main_5_out_c), .OUT_12(main_5_out_12),
    .OUT_d(main_5_out_d), .OUT_13(main_5_out_13), .OUT_e(main_5_out_e), .OUT_14(main_5_out_14),
    .OUT_f(main_5_out_f), .OUT_15(main_5_out_15), .OUT_10(main_5_out_10), .OUT_16(main_5_out_16),
    .OUT_18(main_5_out_18), .OUT_19(main_5_out_19), .OUT_1a(main_5_out_1a), .OUT_1b(main_5_out_1b),
    .OUT_1c(main_5_out_1c), .OUT_5(main_5_out_5), .OUT_b(main_5_out_b), .OUT_11(main_5_out_11),
    .OUT_17(main_5_out_17), .OUT_1d(main_5_out_1d));
  DotMatrix #(.matrixcols(30), .matrixrows(30), .persist(500)) dotmatrix_3 (
    .col0(main_5_out_0), .col1(main_5_out_1), .col2(main_5_out_2), .col3(main_5_out_3), .col4(main_5_out_4),
    .col5(main_5_out_5), .col6(main_5_out_6), .col7(main_5_out_7), .col8(main_5_out_8), .col9(main_5_out_9),
    .col10(main_5_out_a), .col11(main_5_out_b), .col12(main_5_out_c), .col13(main_5_out_d),
    .col14(main_5_out_e), .col15(main_5_out_f), .col16(main_5_out_10), .col17(main_5_out_11),
    .col18(main_5_out_12), .col19(main_5_out_13), .col20(main_5_out_14), .col21(main_5_out_15),
    .col22(main_5_out_16), .col23(main_5_out_17), .col24(main_5_out_18), .col25(main_5_out_19),
    .col26(main_5_out_1a), .col27(main_5_out_1b), .col28(main_5_out_1c), .col29(main_5_out_1d));
  assign controlled_buffer_3_out = and_2_out ? P1_CUR_TL_DATA : 30'bz;  // Controlled_Buffer controlled_buffer_3
  and and_2 (and_2_out, PREP_PHASE_END, ~CURR_PLAYER);  // AND_Gate
  demuxor_30x30x3_main main_6 (
    .DATA_1(P2_SHIP_ON_EN_BL_DATA), .SELECT_1(P2_SHIP_ON_EN_BL_SEL), .SELECT_2(P1_DOT_BL_SEL),
    .DATA_2(P1_DOT_BL_DATA), .SELECT_0(P1_CUR_BL_SEL), .DATA_0(controlled_buffer_4_out),
    .OUT_0(main_6_out_0), .OUT_1(main_6_out_1), .OUT_2(main_6_out_2), .OUT_3(main_6_out_3),
    .OUT_4(main_6_out_4), .OUT_6(main_6_out_6), .OUT_7(main_6_out_7), .OUT_8(main_6_out_8),
    .OUT_9(main_6_out_9), .OUT_a(main_6_out_a), .OUT_c(main_6_out_c), .OUT_12(main_6_out_12),
    .OUT_d(main_6_out_d), .OUT_13(main_6_out_13), .OUT_e(main_6_out_e), .OUT_14(main_6_out_14),
    .OUT_f(main_6_out_f), .OUT_15(main_6_out_15), .OUT_10(main_6_out_10), .OUT_16(main_6_out_16),
    .OUT_18(main_6_out_18), .OUT_19(main_6_out_19), .OUT_1a(main_6_out_1a), .OUT_1b(main_6_out_1b),
    .OUT_1c(main_6_out_1c), .OUT_5(main_6_out_5), .OUT_b(main_6_out_b), .OUT_11(main_6_out_11),
    .OUT_17(main_6_out_17), .OUT_1d(main_6_out_1d));
  DotMatrix #(.matrixcols(30), .matrixrows(30), .persist(500)) dotmatrix_4 (
    .col0(main_6_out_0), .col1(main_6_out_1), .col2(main_6_out_2), .col3(main_6_out_3), .col4(main_6_out_4),
    .col5(main_6_out_5), .col6(main_6_out_6), .col7(main_6_out_7), .col8(main_6_out_8), .col9(main_6_out_9),
    .col10(main_6_out_a), .col11(main_6_out_b), .col12(main_6_out_c), .col13(main_6_out_d),
    .col14(main_6_out_e), .col15(main_6_out_f), .col16(main_6_out_10), .col17(main_6_out_11),
    .col18(main_6_out_12), .col19(main_6_out_13), .col20(main_6_out_14), .col21(main_6_out_15),
    .col22(main_6_out_16), .col23(main_6_out_17), .col24(main_6_out_18), .col25(main_6_out_19),
    .col26(main_6_out_1a), .col27(main_6_out_1b), .col28(main_6_out_1c), .col29(main_6_out_1d));
  assign controlled_buffer_4_out = and_3_out ? P1_CUR_BL_DATA : 30'bz;  // Controlled_Buffer controlled_buffer_4
  and and_3 (and_3_out, PREP_PHASE_END, ~CURR_PLAYER);  // AND_Gate
  not_hit_module_main main_7 (
    .nHIT_X(P2_CUR_X), .nHIT_Y(P2_CUR_Y), .nHIT(and_1_out), .CLK(CLK), .TL_DATA(P2_DOT_TL_DATA),
    .TR_DATA(P2_DOT_TR_DATA), .BL_DATA(P2_DOT_BL_DATA), .BR_DATA(P2_DOT_BR_DATA), .TL_SEL(P2_DOT_TL_SEL),
    .TR_SEL(P2_DOT_TR_SEL), .BL_SEL(P2_DOT_BL_SEL), .BR_SEL(P2_DOT_BR_SEL), .ADDED(P1_DOT_ADDED));
  Comparator #(.width(4), .mode("unsigned")) comparator_1 (
    .a(P1_CURR_SHIP_ADD), .b(4'b1010), .eq(comparator_1_eq));  // open: gt, lt
  Comparator #(.width(4), .mode("unsigned")) comparator_2 (
    .a(4'b1010), .b(P2_CURR_SHIP_ADD), .eq(comparator_2_eq));  // open: gt, lt
  Multiplexer #(.select(2), .enable("false")) multiplexer_1 (
    .in0(P1_RO_ALIVE[0]), .in1(P1_RO_ALIVE[1]), .in2(P1_RO_ALIVE[2]), .in3(P1_RO_ALIVE[3]),
    .out(P1_CURR_SEG_ALIVE), .sel(P1_SEG_SEL));
  and and_4 (PREP_PHASE_END, comparator_1_eq, comparator_2_eq);
  Multiplexer #(.width(3), .enable("false")) multiplexer_2 (
    .in0(3'b010), .in1(3'b001), .out(P1_SHIP_DRAW_SEL), .sel(P1_CURR_SEG_ALIVE));
  Multiplexer #(.width(3), .enable("false")) multiplexer_3 (
    .in0(3'b010), .in1(3'b100), .out(P1_SHIP_DRAW_ON_ENEMY_SEL), .sel(P1_CURR_SEG_ALIVE));
  and and_5 (and_5_out, ~PREP_PHASE_END, main_2_confirm);  // AND_Gate
  and and_6 (and_6_out, main_2_confirm, ~CURR_PLAYER);  // AND_Gate
  demuxor_30x30x3_main main_8 (
    .DATA_1(P1_SHIP_TR_DATA), .SELECT_1(P1_SHIP_TR_SEL), .SELECT_2(P2_DOT_TR_SEL), .DATA_2(P2_DOT_TR_DATA),
    .SELECT_0(P1_CUR_TR_SEL), .DATA_0(controlled_buffer_5_out), .OUT_0(main_8_out_0), .OUT_1(main_8_out_1),
    .OUT_2(main_8_out_2), .OUT_3(main_8_out_3), .OUT_4(main_8_out_4), .OUT_6(main_8_out_6),
    .OUT_7(main_8_out_7), .OUT_8(main_8_out_8), .OUT_9(main_8_out_9), .OUT_a(main_8_out_a),
    .OUT_c(main_8_out_c), .OUT_12(main_8_out_12), .OUT_d(main_8_out_d), .OUT_13(main_8_out_13),
    .OUT_e(main_8_out_e), .OUT_14(main_8_out_14), .OUT_f(main_8_out_f), .OUT_15(main_8_out_15),
    .OUT_10(main_8_out_10), .OUT_16(main_8_out_16), .OUT_18(main_8_out_18), .OUT_19(main_8_out_19),
    .OUT_1a(main_8_out_1a), .OUT_1b(main_8_out_1b), .OUT_1c(main_8_out_1c), .OUT_5(main_8_out_5),
    .OUT_b(main_8_out_b), .OUT_11(main_8_out_11), .OUT_17(main_8_out_17), .OUT_1d(main_8_out_1d));
  DotMatrix #(.matrixcols(30), .matrixrows(30), .persist(500)) dotmatrix_5 (
    .col0(main_8_out_0), .col1(main_8_out_1), .col2(main_8_out_2), .col3(main_8_out_3), .col4(main_8_out_4),
    .col5(main_8_out_5), .col6(main_8_out_6), .col7(main_8_out_7), .col8(main_8_out_8), .col9(main_8_out_9),
    .col10(main_8_out_a), .col11(main_8_out_b), .col12(main_8_out_c), .col13(main_8_out_d),
    .col14(main_8_out_e), .col15(main_8_out_f), .col16(main_8_out_10), .col17(main_8_out_11),
    .col18(main_8_out_12), .col19(main_8_out_13), .col20(main_8_out_14), .col21(main_8_out_15),
    .col22(main_8_out_16), .col23(main_8_out_17), .col24(main_8_out_18), .col25(main_8_out_19),
    .col26(main_8_out_1a), .col27(main_8_out_1b), .col28(main_8_out_1c), .col29(main_8_out_1d));
  demuxor_30x30x3_main main_9 (
    .DATA_1(P1_SHIP_BR_DATA), .SELECT_1(P1_SHIP_BR_SEL), .SELECT_2(P2_DOT_BR_SEL), .DATA_2(P2_DOT_BR_DATA),
    .SELECT_0(P1_CUR_BR_SEL), .DATA_0(controlled_buffer_6_out), .OUT_0(main_9_out_0), .OUT_1(main_9_out_1),
    .OUT_2(main_9_out_2), .OUT_3(main_9_out_3), .OUT_4(main_9_out_4), .OUT_6(main_9_out_6),
    .OUT_7(main_9_out_7), .OUT_8(main_9_out_8), .OUT_9(main_9_out_9), .OUT_a(main_9_out_a),
    .OUT_c(main_9_out_c), .OUT_12(main_9_out_12), .OUT_d(main_9_out_d), .OUT_13(main_9_out_13),
    .OUT_e(main_9_out_e), .OUT_14(main_9_out_14), .OUT_f(main_9_out_f), .OUT_15(main_9_out_15),
    .OUT_10(main_9_out_10), .OUT_16(main_9_out_16), .OUT_18(main_9_out_18), .OUT_19(main_9_out_19),
    .OUT_1a(main_9_out_1a), .OUT_1b(main_9_out_1b), .OUT_1c(main_9_out_1c), .OUT_5(main_9_out_5),
    .OUT_b(main_9_out_b), .OUT_11(main_9_out_11), .OUT_17(main_9_out_17), .OUT_1d(main_9_out_1d));
  DotMatrix #(.matrixcols(30), .matrixrows(30), .persist(500)) dotmatrix_6 (
    .col0(main_9_out_0), .col1(main_9_out_1), .col2(main_9_out_2), .col3(main_9_out_3), .col4(main_9_out_4),
    .col5(main_9_out_5), .col6(main_9_out_6), .col7(main_9_out_7), .col8(main_9_out_8), .col9(main_9_out_9),
    .col10(main_9_out_a), .col11(main_9_out_b), .col12(main_9_out_c), .col13(main_9_out_d),
    .col14(main_9_out_e), .col15(main_9_out_f), .col16(main_9_out_10), .col17(main_9_out_11),
    .col18(main_9_out_12), .col19(main_9_out_13), .col20(main_9_out_14), .col21(main_9_out_15),
    .col22(main_9_out_16), .col23(main_9_out_17), .col24(main_9_out_18), .col25(main_9_out_19),
    .col26(main_9_out_1a), .col27(main_9_out_1b), .col28(main_9_out_1c), .col29(main_9_out_1d));
  not not_3 (not_3_out, PREP_PHASE_END);
  DotMatrix #(.matrixcols(30), .matrixrows(30), .persist(500)) dotmatrix_7 (
    .col0(main_10_out_0), .col1(main_10_out_1), .col2(main_10_out_2), .col3(main_10_out_3),
    .col4(main_10_out_4), .col5(main_10_out_5), .col6(main_10_out_6), .col7(main_10_out_7),
    .col8(main_10_out_8), .col9(main_10_out_9), .col10(main_10_out_a), .col11(main_10_out_b),
    .col12(main_10_out_c), .col13(main_10_out_d), .col14(main_10_out_e), .col15(main_10_out_f),
    .col16(main_10_out_10), .col17(main_10_out_11), .col18(main_10_out_12), .col19(main_10_out_13),
    .col20(main_10_out_14), .col21(main_10_out_15), .col22(main_10_out_16), .col23(main_10_out_17),
    .col24(main_10_out_18), .col25(main_10_out_19), .col26(main_10_out_1a), .col27(main_10_out_1b),
    .col28(main_10_out_1c), .col29(main_10_out_1d));
  demuxor_30x30x3_main main_10 (
    .DATA_1(P2_SHIP_ON_EN_TR_DATA), .SELECT_1(P2_SHIP_ON_EN_TR_SEL), .SELECT_2(P1_DOT_TR_SEL),
    .DATA_2(P1_DOT_TR_DATA), .SELECT_0(P1_CUR_TR_SEL), .DATA_0(controlled_buffer_7_out),
    .OUT_0(main_10_out_0), .OUT_1(main_10_out_1), .OUT_2(main_10_out_2), .OUT_3(main_10_out_3),
    .OUT_4(main_10_out_4), .OUT_6(main_10_out_6), .OUT_7(main_10_out_7), .OUT_8(main_10_out_8),
    .OUT_9(main_10_out_9), .OUT_a(main_10_out_a), .OUT_c(main_10_out_c), .OUT_12(main_10_out_12),
    .OUT_d(main_10_out_d), .OUT_13(main_10_out_13), .OUT_e(main_10_out_e), .OUT_14(main_10_out_14),
    .OUT_f(main_10_out_f), .OUT_15(main_10_out_15), .OUT_10(main_10_out_10), .OUT_16(main_10_out_16),
    .OUT_18(main_10_out_18), .OUT_19(main_10_out_19), .OUT_1a(main_10_out_1a), .OUT_1b(main_10_out_1b),
    .OUT_1c(main_10_out_1c), .OUT_5(main_10_out_5), .OUT_b(main_10_out_b), .OUT_11(main_10_out_11),
    .OUT_17(main_10_out_17), .OUT_1d(main_10_out_1d));
  and and_7 (and_7_out, PREP_PHASE_END, ~CURR_PLAYER);  // AND_Gate
  DotMatrix #(.matrixcols(30), .matrixrows(30), .persist(500)) dotmatrix_8 (
    .col0(main_11_out_0), .col1(main_11_out_1), .col2(main_11_out_2), .col3(main_11_out_3),
    .col4(main_11_out_4), .col5(main_11_out_5), .col6(main_11_out_6), .col7(main_11_out_7),
    .col8(main_11_out_8), .col9(main_11_out_9), .col10(main_11_out_a), .col11(main_11_out_b),
    .col12(main_11_out_c), .col13(main_11_out_d), .col14(main_11_out_e), .col15(main_11_out_f),
    .col16(main_11_out_10), .col17(main_11_out_11), .col18(main_11_out_12), .col19(main_11_out_13),
    .col20(main_11_out_14), .col21(main_11_out_15), .col22(main_11_out_16), .col23(main_11_out_17),
    .col24(main_11_out_18), .col25(main_11_out_19), .col26(main_11_out_1a), .col27(main_11_out_1b),
    .col28(main_11_out_1c), .col29(main_11_out_1d));
  demuxor_30x30x3_main main_11 (
    .DATA_1(P2_SHIP_ON_EN_BR_DATA), .SELECT_1(P2_SHIP_ON_EN_BR_SEL), .SELECT_2(P1_DOT_BR_SEL),
    .DATA_2(P1_DOT_BR_DATA), .SELECT_0(P1_CUR_BR_SEL), .DATA_0(controlled_buffer_8_out),
    .OUT_0(main_11_out_0), .OUT_1(main_11_out_1), .OUT_2(main_11_out_2), .OUT_3(main_11_out_3),
    .OUT_4(main_11_out_4), .OUT_6(main_11_out_6), .OUT_7(main_11_out_7), .OUT_8(main_11_out_8),
    .OUT_9(main_11_out_9), .OUT_a(main_11_out_a), .OUT_c(main_11_out_c), .OUT_12(main_11_out_12),
    .OUT_d(main_11_out_d), .OUT_13(main_11_out_13), .OUT_e(main_11_out_e), .OUT_14(main_11_out_14),
    .OUT_f(main_11_out_f), .OUT_15(main_11_out_15), .OUT_10(main_11_out_10), .OUT_16(main_11_out_16),
    .OUT_18(main_11_out_18), .OUT_19(main_11_out_19), .OUT_1a(main_11_out_1a), .OUT_1b(main_11_out_1b),
    .OUT_1c(main_11_out_1c), .OUT_5(main_11_out_5), .OUT_b(main_11_out_b), .OUT_11(main_11_out_11),
    .OUT_17(main_11_out_17), .OUT_1d(main_11_out_1d));
  and and_8 (and_8_out, PREP_PHASE_END, ~CURR_PLAYER);  // AND_Gate
  or or_1 (P1_CONF, and_5_out, and_6_out);
  assign controlled_buffer_5_out = not_4_out ? P1_CUR_TR_DATA : 30'bz;  // Controlled_Buffer controlled_buffer_5
  not not_4 (not_4_out, PREP_PHASE_END);
  assign controlled_buffer_6_out = not_3_out ? P1_CUR_BR_DATA : 30'bz;  // Controlled_Buffer controlled_buffer_6
  assign controlled_buffer_7_out = and_7_out ? P1_CUR_TR_DATA : 30'bz;  // Controlled_Buffer controlled_buffer_7
  assign controlled_buffer_8_out = and_8_out ? P1_CUR_BR_DATA : 30'bz;  // Controlled_Buffer controlled_buffer_8
  and and_9 (P1_ADD_SHIP, P1_CONF, ~PREP_PHASE_END);  // AND_Gate
  and and_10 (P1_CHECK_SHIP, P1_CONF, PREP_PHASE_END);
  Comparator #(.width(4), .mode("unsigned")) comparator_3 (
    .a(P1_CURR_SHIP_ADD), .b(4'b0000), .gt(comparator_3_gt));  // open: eq, lt
  Comparator #(.width(4), .mode("unsigned")) comparator_4 (
    .a(P1_CURR_SHIP_ADD), .b(4'b0000), .gt(comparator_4_gt));  // open: eq, lt
  ship_xyr_to_screen_xy_main main_12 (
    .INPUT(P1_RO_SHIP_X), .in_2(P1_RO_SHIP_Y), .CONST(P1_RO_ROTATED), .OUT_X_00(main_12_out_x_00),
    .OUT_Y_00(main_12_out_y_00), .OUT_X_01(main_12_out_x_01), .OUT_Y_01(main_12_out_y_01),
    .OUT_X_10(main_12_out_x_10), .OUT_Y_10(main_12_out_y_10), .OUT_X_11(main_12_out_x_11),
    .OUT_Y_11(main_12_out_y_11));
  screen_xy_to_screen_data_main main_13 (
    .SCREEN_X(P1_SHIP_SCR_X), .SCREEN_Y(P1_SHIP_SCR_Y), .DATA_TO_DISPLAY(P1_SHIP_DRAW_SEL),
    .TL_SEL_OUT(P1_SHIP_TL_SEL), .TR_SEL_OUT(P1_SHIP_TR_SEL), .BL_SEL_OUT(P1_SHIP_BL_SEL),
    .BR_SEL_OUT(P1_SHIP_BR_SEL), .TL_DATA_OUT(P1_SHIP_TL_DATA), .TR_DATA_OUT(P1_SHIP_TR_DATA),
    .BL_DATA_OUT(P1_SHIP_BL_DATA), .BR_DATA_OUT(P1_SHIP_BR_DATA), .CLK(CLK), .ENABLE(and_11_out));
  and and_11 (and_11_out, P1_SHIP_DRAW_ENABLE, comparator_3_gt);
  screen_xy_to_screen_data_main main_14 (
    .SCREEN_X(P1_SHIP_SCR_X), .SCREEN_Y(P1_SHIP_SCR_Y), .DATA_TO_DISPLAY(P1_SHIP_DRAW_ON_ENEMY_SEL),
    .TL_SEL_OUT(P1_SHIP_ON_EN_TL_SEL), .TR_SEL_OUT(P1_SHIP_ON_EN_TR_SEL), .BL_SEL_OUT(P1_SHIP_ON_EN_BL_SEL),
    .BR_SEL_OUT(P1_SHIP_ON_EN_BR_SEL), .TL_DATA_OUT(P1_SHIP_ON_EN_TL_DATA),
    .TR_DATA_OUT(P1_SHIP_ON_EN_TR_DATA), .BL_DATA_OUT(P1_SHIP_ON_EN_BL_DATA),
    .BR_DATA_OUT(P1_SHIP_ON_EN_BR_DATA), .CLK(CLK), .ENABLE(and_12_out));
  and and_12 (and_12_out, P1_SHIP_DRAW_ENABLE, comparator_4_gt);
  Comparator #(.width(2), .mode("unsigned")) comparator_5 (
    .a(P1_SEG_SEL), .b(P1_RO_SHIP_TYPE), .eq(comparator_5_eq), .lt(comparator_5_lt));  // open: gt
  or or_2 (P1_SHIP_DRAW_ENABLE, comparator_5_eq, comparator_5_lt);
  or or_3 (or_3_out, P1_DOT_ADDED, P2_DOT_ADDED);
  Multiplexer #(.select(2), .width(6), .enable("false")) multiplexer_4 (
    .in0(main_12_out_x_00), .in1(main_12_out_x_01), .in2(main_12_out_x_10), .in3(main_12_out_x_11),
    .out(P1_SHIP_SCR_X), .sel(P1_SEG_SEL));
  Multiplexer #(.select(2), .width(6), .enable("false")) multiplexer_5 (
    .in0(main_12_out_y_00), .in1(main_12_out_y_01), .in2(main_12_out_y_10), .in3(main_12_out_y_11),
    .out(P1_SHIP_SCR_Y), .sel(P1_SEG_SEL));
  Counter #(.width(1), .max('h1)) counter_3 (.Q(CURR_PLAYER), .clk(and_13_out));  // open: load, D, count, carry, clr
  and and_13 (and_13_out, ~P1_CHECKING, ~P2_CHECKING, ~P1_HIT, ~P2_HIT, or_3_out);  // AND_Gate
  DotMatrix #(.matrixcols(8), .matrixrows(5)) dotmatrix_9 (
    .col0(main_15_output8), .col1(main_15_output7), .col2(main_15_output6), .col3(main_15_output5),
    .col4(main_15_output4), .col5(main_15_output3), .col6(main_15_output2), .col7(main_15_output1));
  arrow_main main_15 (
    .\input (CURR_PLAYER), .output2(main_15_output2), .output1(main_15_output1), .output3(main_15_output3),
    .output4(main_15_output4), .output5(main_15_output5), .output6(main_15_output6),
    .output7(main_15_output7), .output8(main_15_output8));
  Counter #(.width(2), .max('h3)) counter_4 (
    .Q(P2_SEG_SEL), .carry(P2_NEXT_SHIP), .clk(CLK_5));  // open: load, D, count, clr
  memory_management_main main_16 (
    .X(P2_CUR_X), .Y(P2_CUR_Y), .ROTATED(P2_ROTATED),
    .RAM_OUT({P2_RO_ALIVE, P2_RO_ROTATED, P2_RO_SHIP_TYPE, P2_RO_SHIP_Y, P2_RO_SHIP_X}), .CHECK_X(P1_CUR_X),
    .CHECK_Y(P1_CUR_Y), .SINK_IF_HIT(1'b1), .CONFIRM(P2_ADD_SHIP), .CHECK(P1_CHECK_SHIP), .CLK(CLK),
    .SHOW_NEXT_SHIP(P2_NEXT_SHIP), .WIN(P2_WIN), .HIT(P2_HIT), .CHECKING(P2_CHECKING),
    .CURR_SHIP_ADD(P2_CURR_SHIP_ADD));
  Keyboard keyboard_2 (.clk(CLK), .clr(undriven_2), .data(keyboard_2_data));  // open: re, avail
  cursor_module_main main_17 (
    .CUR_X(P2_CUR_X), .CLK(CLK), .KEYBOARD_OUT(keyboard_2_data), .KEYBOARD_RST(undriven_2),
    .TL_SEL(P2_CUR_TL_SEL), .TR_SEL(P2_CUR_TR_SEL), .BL_SEL(P2_CUR_BL_SEL), .BR_SEL(P2_CUR_BR_SEL),
    .TL_DATA(P2_CUR_TL_DATA), .TR_DATA(P2_CUR_TR_DATA), .BL_DATA(P2_CUR_BL_DATA), .BR_DATA(P2_CUR_BR_DATA),
    .CONFIRM(main_17_confirm), .CUR_Y(P2_CUR_Y), .ROTATED(P2_ROTATED));
  and and_14 (and_14_out, ~P2_HIT, ~P2_CHECKING, PREP_PHASE_END);  // AND_Gate
  DotMatrix #(.matrixcols(30), .matrixrows(30), .persist(500)) dotmatrix_10 (
    .col0(main_18_out_0), .col1(main_18_out_1), .col2(main_18_out_2), .col3(main_18_out_3),
    .col4(main_18_out_4), .col5(main_18_out_5), .col6(main_18_out_6), .col7(main_18_out_7),
    .col8(main_18_out_8), .col9(main_18_out_9), .col10(main_18_out_a), .col11(main_18_out_b),
    .col12(main_18_out_c), .col13(main_18_out_d), .col14(main_18_out_e), .col15(main_18_out_f),
    .col16(main_18_out_10), .col17(main_18_out_11), .col18(main_18_out_12), .col19(main_18_out_13),
    .col20(main_18_out_14), .col21(main_18_out_15), .col22(main_18_out_16), .col23(main_18_out_17),
    .col24(main_18_out_18), .col25(main_18_out_19), .col26(main_18_out_1a), .col27(main_18_out_1b),
    .col28(main_18_out_1c), .col29(main_18_out_1d));
  demuxor_30x30x3_main main_18 (
    .DATA_1(P2_SHIP_TL_DATA), .SELECT_1(P2_SHIP_TL_SEL), .SELECT_2(P1_DOT_TL_SEL), .DATA_2(P1_DOT_TL_DATA),
    .SELECT_0(P2_CUR_TL_SEL), .DATA_0(controlled_buffer_9_out), .OUT_0(main_18_out_0), .OUT_1(main_18_out_1),
    .OUT_2(main_18_out_2), .OUT_3(main_18_out_3), .OUT_4(main_18_out_4), .OUT_6(main_18_out_6),
    .OUT_7(main_18_out_7), .OUT_8(main_18_out_8), .OUT_9(main_18_out_9), .OUT_a(main_18_out_a),
    .OUT_c(main_18_out_c), .OUT_12(main_18_out_12), .OUT_d(main_18_out_d), .OUT_13(main_18_out_13),
    .OUT_e(main_18_out_e), .OUT_14(main_18_out_14), .OUT_f(main_18_out_f), .OUT_15(main_18_out_15),
    .OUT_10(main_18_out_10), .OUT_16(main_18_out_16), .OUT_18(main_18_out_18), .OUT_19(main_18_out_19),
    .OUT_1a(main_18_out_1a), .OUT_1b(main_18_out_1b), .OUT_1c(main_18_out_1c), .OUT_5(main_18_out_5),
    .OUT_b(main_18_out_b), .OUT_11(main_18_out_11), .OUT_17(main_18_out_17), .OUT_1d(main_18_out_1d));
  not not_5 (not_5_out, PREP_PHASE_END);
  demuxor_30x30x3_main main_19 (
    .DATA_1(P2_SHIP_BL_DATA), .SELECT_1(P2_SHIP_BL_SEL), .SELECT_2(P1_DOT_BL_SEL), .DATA_2(P1_DOT_BL_DATA),
    .SELECT_0(P2_CUR_BL_SEL), .DATA_0(controlled_buffer_10_out), .OUT_0(main_19_out_0),
    .OUT_1(main_19_out_1), .OUT_2(main_19_out_2), .OUT_3(main_19_out_3), .OUT_4(main_19_out_4),
    .OUT_6(main_19_out_6), .OUT_7(main_19_out_7), .OUT_8(main_19_out_8), .OUT_9(main_19_out_9),
    .OUT_a(main_19_out_a), .OUT_c(main_19_out_c), .OUT_12(main_19_out_12), .OUT_d(main_19_out_d),
    .OUT_13(main_19_out_13), .OUT_e(main_19_out_e), .OUT_14(main_19_out_14), .OUT_f(main_19_out_f),
    .OUT_15(main_19_out_15), .OUT_10(main_19_out_10), .OUT_16(main_19_out_16), .OUT_18(main_19_out_18),
    .OUT_19(main_19_out_19), .OUT_1a(main_19_out_1a), .OUT_1b(main_19_out_1b), .OUT_1c(main_19_out_1c),
    .OUT_5(main_19_out_5), .OUT_b(main_19_out_b), .OUT_11(main_19_out_11), .OUT_17(main_19_out_17),
    .OUT_1d(main_19_out_1d));
  DotMatrix #(.matrixcols(30), .matrixrows(30), .persist(500)) dotmatrix_11 (
    .col0(main_19_out_0), .col1(main_19_out_1), .col2(main_19_out_2), .col3(main_19_out_3),
    .col4(main_19_out_4), .col5(main_19_out_5), .col6(main_19_out_6), .col7(main_19_out_7),
    .col8(main_19_out_8), .col9(main_19_out_9), .col10(main_19_out_a), .col11(main_19_out_b),
    .col12(main_19_out_c), .col13(main_19_out_d), .col14(main_19_out_e), .col15(main_19_out_f),
    .col16(main_19_out_10), .col17(main_19_out_11), .col18(main_19_out_12), .col19(main_19_out_13),
    .col20(main_19_out_14), .col21(main_19_out_15), .col22(main_19_out_16), .col23(main_19_out_17),
    .col24(main_19_out_18), .col25(main_19_out_19), .col26(main_19_out_1a), .col27(main_19_out_1b),
    .col28(main_19_out_1c), .col29(main_19_out_1d));
  not not_6 (not_6_out, PREP_PHASE_END);
  demuxor_30x30x3_main main_20 (
    .DATA_1(P1_SHIP_ON_EN_TL_DATA), .SELECT_1(P1_SHIP_ON_EN_TL_SEL), .SELECT_2(P2_DOT_TL_SEL),
    .DATA_2(P2_DOT_TL_DATA), .SELECT_0(P2_CUR_TL_SEL), .DATA_0(controlled_buffer_11_out),
    .OUT_0(main_20_out_0), .OUT_1(main_20_out_1), .OUT_2(main_20_out_2), .OUT_3(main_20_out_3),
    .OUT_4(main_20_out_4), .OUT_6(main_20_out_6), .OUT_7(main_20_out_7), .OUT_8(main_20_out_8),
    .OUT_9(main_20_out_9), .OUT_a(main_20_out_a), .OUT_c(main_20_out_c), .OUT_12(main_20_out_12),
    .OUT_d(main_20_out_d), .OUT_13(main_20_out_13), .OUT_e(main_20_out_e), .OUT_14(main_20_out_14),
    .OUT_f(main_20_out_f), .OUT_15(main_20_out_15), .OUT_10(main_20_out_10), .OUT_16(main_20_out_16),
    .OUT_18(main_20_out_18), .OUT_19(main_20_out_19), .OUT_1a(main_20_out_1a), .OUT_1b(main_20_out_1b),
    .OUT_1c(main_20_out_1c), .OUT_5(main_20_out_5), .OUT_b(main_20_out_b), .OUT_11(main_20_out_11),
    .OUT_17(main_20_out_17), .OUT_1d(main_20_out_1d));
  DotMatrix #(.matrixcols(30), .matrixrows(30), .persist(500)) dotmatrix_12 (
    .col0(main_20_out_0), .col1(main_20_out_1), .col2(main_20_out_2), .col3(main_20_out_3),
    .col4(main_20_out_4), .col5(main_20_out_5), .col6(main_20_out_6), .col7(main_20_out_7),
    .col8(main_20_out_8), .col9(main_20_out_9), .col10(main_20_out_a), .col11(main_20_out_b),
    .col12(main_20_out_c), .col13(main_20_out_d), .col14(main_20_out_e), .col15(main_20_out_f),
    .col16(main_20_out_10), .col17(main_20_out_11), .col18(main_20_out_12), .col19(main_20_out_13),
    .col20(main_20_out_14), .col21(main_20_out_15), .col22(main_20_out_16), .col23(main_20_out_17),
    .col24(main_20_out_18), .col25(main_20_out_19), .col26(main_20_out_1a), .col27(main_20_out_1b),
    .col28(main_20_out_1c), .col29(main_20_out_1d));
  and and_15 (and_15_out, PREP_PHASE_END, CURR_PLAYER);
  demuxor_30x30x3_main main_21 (
    .DATA_1(P1_SHIP_ON_EN_BL_DATA), .SELECT_1(P1_SHIP_ON_EN_BL_SEL), .SELECT_2(P2_DOT_BL_SEL),
    .DATA_2(P2_DOT_BL_DATA), .SELECT_0(P2_CUR_BL_SEL), .DATA_0(controlled_buffer_12_out),
    .OUT_0(main_21_out_0), .OUT_1(main_21_out_1), .OUT_2(main_21_out_2), .OUT_3(main_21_out_3),
    .OUT_4(main_21_out_4), .OUT_6(main_21_out_6), .OUT_7(main_21_out_7), .OUT_8(main_21_out_8),
    .OUT_9(main_21_out_9), .OUT_a(main_21_out_a), .OUT_c(main_21_out_c), .OUT_12(main_21_out_12),
    .OUT_d(main_21_out_d), .OUT_13(main_21_out_13), .OUT_e(main_21_out_e), .OUT_14(main_21_out_14),
    .OUT_f(main_21_out_f), .OUT_15(main_21_out_15), .OUT_10(main_21_out_10), .OUT_16(main_21_out_16),
    .OUT_18(main_21_out_18), .OUT_19(main_21_out_19), .OUT_1a(main_21_out_1a), .OUT_1b(main_21_out_1b),
    .OUT_1c(main_21_out_1c), .OUT_5(main_21_out_5), .OUT_b(main_21_out_b), .OUT_11(main_21_out_11),
    .OUT_17(main_21_out_17), .OUT_1d(main_21_out_1d));
  DotMatrix #(.matrixcols(30), .matrixrows(30), .persist(500)) dotmatrix_13 (
    .col0(main_21_out_0), .col1(main_21_out_1), .col2(main_21_out_2), .col3(main_21_out_3),
    .col4(main_21_out_4), .col5(main_21_out_5), .col6(main_21_out_6), .col7(main_21_out_7),
    .col8(main_21_out_8), .col9(main_21_out_9), .col10(main_21_out_a), .col11(main_21_out_b),
    .col12(main_21_out_c), .col13(main_21_out_d), .col14(main_21_out_e), .col15(main_21_out_f),
    .col16(main_21_out_10), .col17(main_21_out_11), .col18(main_21_out_12), .col19(main_21_out_13),
    .col20(main_21_out_14), .col21(main_21_out_15), .col22(main_21_out_16), .col23(main_21_out_17),
    .col24(main_21_out_18), .col25(main_21_out_19), .col26(main_21_out_1a), .col27(main_21_out_1b),
    .col28(main_21_out_1c), .col29(main_21_out_1d));
  and and_16 (and_16_out, PREP_PHASE_END, CURR_PLAYER);
  assign controlled_buffer_9_out = not_5_out ? P2_CUR_TL_DATA : 30'bz;  // Controlled_Buffer controlled_buffer_9
  assign controlled_buffer_10_out = not_6_out ? P2_CUR_BL_DATA : 30'bz;  // Controlled_Buffer controlled_buffer_10
  assign controlled_buffer_11_out = and_15_out ? P2_CUR_TL_DATA : 30'bz;  // Controlled_Buffer controlled_buffer_11
  assign controlled_buffer_12_out = and_16_out ? P2_CUR_BL_DATA : 30'bz;  // Controlled_Buffer controlled_buffer_12
  not_hit_module_main main_22 (
    .nHIT_X(P1_CUR_X), .nHIT_Y(P1_CUR_Y), .nHIT(and_14_out), .CLK(CLK), .TL_DATA(P1_DOT_TL_DATA),
    .TR_DATA(P1_DOT_TR_DATA), .BL_DATA(P1_DOT_BL_DATA), .BR_DATA(P1_DOT_BR_DATA), .TL_SEL(P1_DOT_TL_SEL),
    .TR_SEL(P1_DOT_TR_SEL), .BL_SEL(P1_DOT_BL_SEL), .BR_SEL(P1_DOT_BR_SEL), .ADDED(P2_DOT_ADDED));
  Multiplexer #(.select(2), .enable("false")) multiplexer_6 (
    .in0(P2_RO_ALIVE[0]), .in1(P2_RO_ALIVE[1]), .in2(P2_RO_ALIVE[2]), .in3(P2_RO_ALIVE[3]),
    .out(P2_CURR_SEG_ALIVE), .sel(P2_SEG_SEL));
  Multiplexer #(.width(3), .enable("false")) multiplexer_7 (
    .in0(3'b010), .in1(3'b001), .out(P2_SHIP_DRAW_SEL), .sel(P2_CURR_SEG_ALIVE));
  Multiplexer #(.width(3), .enable("false")) multiplexer_8 (
    .in0(3'b010), .in1(3'b100), .out(P2_SHIP_DRAW_ON_ENEMY_SEL), .sel(P2_CURR_SEG_ALIVE));
  and and_17 (and_17_out, ~PREP_PHASE_END, main_17_confirm);  // AND_Gate
  and and_18 (and_18_out, main_17_confirm, CURR_PLAYER);
  or or_4 (P2_CONF, and_17_out, and_18_out);
  DotMatrix #(.matrixcols(30), .matrixrows(30), .persist(500)) dotmatrix_14 (
    .col0(main_23_out_0), .col1(main_23_out_1), .col2(main_23_out_2), .col3(main_23_out_3),
    .col4(main_23_out_4), .col5(main_23_out_5), .col6(main_23_out_6), .col7(main_23_out_7),
    .col8(main_23_out_8), .col9(main_23_out_9), .col10(main_23_out_a), .col11(main_23_out_b),
    .col12(main_23_out_c), .col13(main_23_out_d), .col14(main_23_out_e), .col15(main_23_out_f),
    .col16(main_23_out_10), .col17(main_23_out_11), .col18(main_23_out_12), .col19(main_23_out_13),
    .col20(main_23_out_14), .col21(main_23_out_15), .col22(main_23_out_16), .col23(main_23_out_17),
    .col24(main_23_out_18), .col25(main_23_out_19), .col26(main_23_out_1a), .col27(main_23_out_1b),
    .col28(main_23_out_1c), .col29(main_23_out_1d));
  demuxor_30x30x3_main main_23 (
    .DATA_1(P2_SHIP_TR_DATA), .SELECT_1(P2_SHIP_TR_SEL), .SELECT_2(P1_DOT_TR_SEL), .DATA_2(P1_DOT_TR_DATA),
    .SELECT_0(P2_CUR_TR_SEL), .DATA_0(controlled_buffer_13_out), .OUT_0(main_23_out_0),
    .OUT_1(main_23_out_1), .OUT_2(main_23_out_2), .OUT_3(main_23_out_3), .OUT_4(main_23_out_4),
    .OUT_6(main_23_out_6), .OUT_7(main_23_out_7), .OUT_8(main_23_out_8), .OUT_9(main_23_out_9),
    .OUT_a(main_23_out_a), .OUT_c(main_23_out_c), .OUT_12(main_23_out_12), .OUT_d(main_23_out_d),
    .OUT_13(main_23_out_13), .OUT_e(main_23_out_e), .OUT_14(main_23_out_14), .OUT_f(main_23_out_f),
    .OUT_15(main_23_out_15), .OUT_10(main_23_out_10), .OUT_16(main_23_out_16), .OUT_18(main_23_out_18),
    .OUT_19(main_23_out_19), .OUT_1a(main_23_out_1a), .OUT_1b(main_23_out_1b), .OUT_1c(main_23_out_1c),
    .OUT_5(main_23_out_5), .OUT_b(main_23_out_b), .OUT_11(main_23_out_11), .OUT_17(main_23_out_17),
    .OUT_1d(main_23_out_1d));
  assign controlled_buffer_13_out = not_7_out ? P2_CUR_TR_DATA : 30'bz;  // Controlled_Buffer controlled_buffer_13
  not not_7 (not_7_out, PREP_PHASE_END);
  DotMatrix #(.matrixcols(30), .matrixrows(30), .persist(500)) dotmatrix_15 (
    .col0(main_24_out_0), .col1(main_24_out_1), .col2(main_24_out_2), .col3(main_24_out_3),
    .col4(main_24_out_4), .col5(main_24_out_5), .col6(main_24_out_6), .col7(main_24_out_7),
    .col8(main_24_out_8), .col9(main_24_out_9), .col10(main_24_out_a), .col11(main_24_out_b),
    .col12(main_24_out_c), .col13(main_24_out_d), .col14(main_24_out_e), .col15(main_24_out_f),
    .col16(main_24_out_10), .col17(main_24_out_11), .col18(main_24_out_12), .col19(main_24_out_13),
    .col20(main_24_out_14), .col21(main_24_out_15), .col22(main_24_out_16), .col23(main_24_out_17),
    .col24(main_24_out_18), .col25(main_24_out_19), .col26(main_24_out_1a), .col27(main_24_out_1b),
    .col28(main_24_out_1c), .col29(main_24_out_1d));
  demuxor_30x30x3_main main_24 (
    .DATA_1(P2_SHIP_BR_DATA), .SELECT_1(P2_SHIP_BR_SEL), .SELECT_2(P1_DOT_BR_SEL), .DATA_2(P1_DOT_BR_DATA),
    .SELECT_0(P2_CUR_BR_SEL), .DATA_0(controlled_buffer_14_out), .OUT_0(main_24_out_0),
    .OUT_1(main_24_out_1), .OUT_2(main_24_out_2), .OUT_3(main_24_out_3), .OUT_4(main_24_out_4),
    .OUT_6(main_24_out_6), .OUT_7(main_24_out_7), .OUT_8(main_24_out_8), .OUT_9(main_24_out_9),
    .OUT_a(main_24_out_a), .OUT_c(main_24_out_c), .OUT_12(main_24_out_12), .OUT_d(main_24_out_d),
    .OUT_13(main_24_out_13), .OUT_e(main_24_out_e), .OUT_14(main_24_out_14), .OUT_f(main_24_out_f),
    .OUT_15(main_24_out_15), .OUT_10(main_24_out_10), .OUT_16(main_24_out_16), .OUT_18(main_24_out_18),
    .OUT_19(main_24_out_19), .OUT_1a(main_24_out_1a), .OUT_1b(main_24_out_1b), .OUT_1c(main_24_out_1c),
    .OUT_5(main_24_out_5), .OUT_b(main_24_out_b), .OUT_11(main_24_out_11), .OUT_17(main_24_out_17),
    .OUT_1d(main_24_out_1d));
  assign controlled_buffer_14_out = not_8_out ? P2_CUR_BR_DATA : 30'bz;  // Controlled_Buffer controlled_buffer_14
  not not_8 (not_8_out, PREP_PHASE_END);
  DotMatrix #(.matrixcols(30), .matrixrows(30), .persist(500)) dotmatrix_16 (
    .col0(main_25_out_0), .col1(main_25_out_1), .col2(main_25_out_2), .col3(main_25_out_3),
    .col4(main_25_out_4), .col5(main_25_out_5), .col6(main_25_out_6), .col7(main_25_out_7),
    .col8(main_25_out_8), .col9(main_25_out_9), .col10(main_25_out_a), .col11(main_25_out_b),
    .col12(main_25_out_c), .col13(main_25_out_d), .col14(main_25_out_e), .col15(main_25_out_f),
    .col16(main_25_out_10), .col17(main_25_out_11), .col18(main_25_out_12), .col19(main_25_out_13),
    .col20(main_25_out_14), .col21(main_25_out_15), .col22(main_25_out_16), .col23(main_25_out_17),
    .col24(main_25_out_18), .col25(main_25_out_19), .col26(main_25_out_1a), .col27(main_25_out_1b),
    .col28(main_25_out_1c), .col29(main_25_out_1d));
  demuxor_30x30x3_main main_25 (
    .DATA_1(P1_SHIP_ON_EN_TR_DATA), .SELECT_1(P1_SHIP_ON_EN_TR_SEL), .SELECT_2(P2_DOT_TR_SEL),
    .DATA_2(P2_DOT_TR_DATA), .SELECT_0(P2_CUR_TR_SEL), .DATA_0(controlled_buffer_15_out),
    .OUT_0(main_25_out_0), .OUT_1(main_25_out_1), .OUT_2(main_25_out_2), .OUT_3(main_25_out_3),
    .OUT_4(main_25_out_4), .OUT_6(main_25_out_6), .OUT_7(main_25_out_7), .OUT_8(main_25_out_8),
    .OUT_9(main_25_out_9), .OUT_a(main_25_out_a), .OUT_c(main_25_out_c), .OUT_12(main_25_out_12),
    .OUT_d(main_25_out_d), .OUT_13(main_25_out_13), .OUT_e(main_25_out_e), .OUT_14(main_25_out_14),
    .OUT_f(main_25_out_f), .OUT_15(main_25_out_15), .OUT_10(main_25_out_10), .OUT_16(main_25_out_16),
    .OUT_18(main_25_out_18), .OUT_19(main_25_out_19), .OUT_1a(main_25_out_1a), .OUT_1b(main_25_out_1b),
    .OUT_1c(main_25_out_1c), .OUT_5(main_25_out_5), .OUT_b(main_25_out_b), .OUT_11(main_25_out_11),
    .OUT_17(main_25_out_17), .OUT_1d(main_25_out_1d));
  assign controlled_buffer_15_out = and_19_out ? P2_CUR_TR_DATA : 30'bz;  // Controlled_Buffer controlled_buffer_15
  and and_19 (and_19_out, PREP_PHASE_END, CURR_PLAYER);
  DotMatrix #(.matrixcols(30), .matrixrows(30), .persist(500)) dotmatrix_17 (
    .col0(main_26_out_0), .col1(main_26_out_1), .col2(main_26_out_2), .col3(main_26_out_3),
    .col4(main_26_out_4), .col5(main_26_out_5), .col6(main_26_out_6), .col7(main_26_out_7),
    .col8(main_26_out_8), .col9(main_26_out_9), .col10(main_26_out_a), .col11(main_26_out_b),
    .col12(main_26_out_c), .col13(main_26_out_d), .col14(main_26_out_e), .col15(main_26_out_f),
    .col16(main_26_out_10), .col17(main_26_out_11), .col18(main_26_out_12), .col19(main_26_out_13),
    .col20(main_26_out_14), .col21(main_26_out_15), .col22(main_26_out_16), .col23(main_26_out_17),
    .col24(main_26_out_18), .col25(main_26_out_19), .col26(main_26_out_1a), .col27(main_26_out_1b),
    .col28(main_26_out_1c), .col29(main_26_out_1d));
  demuxor_30x30x3_main main_26 (
    .DATA_1(P1_SHIP_ON_EN_BR_DATA), .SELECT_1(P1_SHIP_ON_EN_BR_SEL), .SELECT_2(P2_DOT_BR_SEL),
    .DATA_2(P2_DOT_BR_DATA), .SELECT_0(P2_CUR_BR_SEL), .DATA_0(controlled_buffer_16_out),
    .OUT_0(main_26_out_0), .OUT_1(main_26_out_1), .OUT_2(main_26_out_2), .OUT_3(main_26_out_3),
    .OUT_4(main_26_out_4), .OUT_6(main_26_out_6), .OUT_7(main_26_out_7), .OUT_8(main_26_out_8),
    .OUT_9(main_26_out_9), .OUT_a(main_26_out_a), .OUT_c(main_26_out_c), .OUT_12(main_26_out_12),
    .OUT_d(main_26_out_d), .OUT_13(main_26_out_13), .OUT_e(main_26_out_e), .OUT_14(main_26_out_14),
    .OUT_f(main_26_out_f), .OUT_15(main_26_out_15), .OUT_10(main_26_out_10), .OUT_16(main_26_out_16),
    .OUT_18(main_26_out_18), .OUT_19(main_26_out_19), .OUT_1a(main_26_out_1a), .OUT_1b(main_26_out_1b),
    .OUT_1c(main_26_out_1c), .OUT_5(main_26_out_5), .OUT_b(main_26_out_b), .OUT_11(main_26_out_11),
    .OUT_17(main_26_out_17), .OUT_1d(main_26_out_1d));
  assign controlled_buffer_16_out = and_20_out ? P2_CUR_BR_DATA : 30'bz;  // Controlled_Buffer controlled_buffer_16
  and and_20 (and_20_out, PREP_PHASE_END, CURR_PLAYER);
  Comparator #(.width(4), .mode("unsigned")) comparator_6 (
    .a(P2_CURR_SHIP_ADD), .b(4'b0000), .gt(comparator_6_gt));  // open: eq, lt
  ship_xyr_to_screen_xy_main main_27 (
    .INPUT(P2_RO_SHIP_X), .in_2(P2_RO_SHIP_Y), .CONST(P2_RO_ROTATED), .OUT_X_00(main_27_out_x_00),
    .OUT_Y_00(main_27_out_y_00), .OUT_X_01(main_27_out_x_01), .OUT_Y_01(main_27_out_y_01),
    .OUT_X_10(main_27_out_x_10), .OUT_Y_10(main_27_out_y_10), .OUT_X_11(main_27_out_x_11),
    .OUT_Y_11(main_27_out_y_11));
  screen_xy_to_screen_data_main main_28 (
    .SCREEN_X(P2_SHIP_SCR_X), .SCREEN_Y(P2_SHIP_SCR_Y), .DATA_TO_DISPLAY(P2_SHIP_DRAW_SEL),
    .TL_SEL_OUT(P2_SHIP_TL_SEL), .TR_SEL_OUT(P2_SHIP_TR_SEL), .BL_SEL_OUT(P2_SHIP_BL_SEL),
    .BR_SEL_OUT(P2_SHIP_BR_SEL), .TL_DATA_OUT(P2_SHIP_TL_DATA), .TR_DATA_OUT(P2_SHIP_TR_DATA),
    .BL_DATA_OUT(P2_SHIP_BL_DATA), .BR_DATA_OUT(P2_SHIP_BR_DATA), .CLK(CLK), .ENABLE(and_21_out));
  and and_21 (and_21_out, P2_SHIP_DRAW_ENABLE, comparator_6_gt);
  screen_xy_to_screen_data_main main_29 (
    .SCREEN_X(P2_SHIP_SCR_X), .SCREEN_Y(P2_SHIP_SCR_Y), .DATA_TO_DISPLAY(P2_SHIP_DRAW_ON_ENEMY_SEL),
    .TL_SEL_OUT(P2_SHIP_ON_EN_TL_SEL), .TR_SEL_OUT(P2_SHIP_ON_EN_TR_SEL), .BL_SEL_OUT(P2_SHIP_ON_EN_BL_SEL),
    .BR_SEL_OUT(P2_SHIP_ON_EN_BR_SEL), .TL_DATA_OUT(P2_SHIP_ON_EN_TL_DATA),
    .TR_DATA_OUT(P2_SHIP_ON_EN_TR_DATA), .BL_DATA_OUT(P2_SHIP_ON_EN_BL_DATA),
    .BR_DATA_OUT(P2_SHIP_ON_EN_BR_DATA), .CLK(CLK), .ENABLE(and_22_out));
  and and_22 (and_22_out, P2_SHIP_DRAW_ENABLE, comparator_7_gt);
  Comparator #(.width(4), .mode("unsigned")) comparator_7 (
    .a(P2_CURR_SHIP_ADD), .b(4'b0000), .gt(comparator_7_gt));  // open: eq, lt
  and and_23 (P2_ADD_SHIP, P2_CONF, ~PREP_PHASE_END);  // AND_Gate
  and and_24 (P2_CHECK_SHIP, P2_CONF, PREP_PHASE_END);
  Comparator #(.width(2), .mode("unsigned")) comparator_8 (
    .a(P2_SEG_SEL), .b(P2_RO_SHIP_TYPE), .eq(comparator_8_eq), .lt(comparator_8_lt));  // open: gt
  or or_5 (P2_SHIP_DRAW_ENABLE, comparator_8_eq, comparator_8_lt);
  Multiplexer #(.select(2), .width(6), .enable("false")) multiplexer_9 (
    .in0(main_27_out_x_00), .in1(main_27_out_x_01), .in2(main_27_out_x_10), .in3(main_27_out_x_11),
    .out(P2_SHIP_SCR_X), .sel(P2_SEG_SEL));
  Multiplexer #(.select(2), .width(6), .enable("false")) multiplexer_10 (
    .in0(main_27_out_y_00), .in1(main_27_out_y_01), .in2(main_27_out_y_10), .in3(main_27_out_y_11),
    .out(P2_SHIP_SCR_Y), .sel(P2_SEG_SEL));

  // Notes on the sheet:
  //   sunk
  //   alive
  //   sunk
  //   none
  //   STATKI GRACZA 1
  //   1 jak gracze wybiora statki juz
  //   sunk
  //   alive
  //   sunk
  //   none
  //   STATKI GRACZA 2
endmodule
