// Logisim project arrow.circ as structural Verilog: 2 circuits, main circuit main
module main (
  input  \input ,
  output [4:0] output4,
  output [4:0] output5,
  output [4:0] output3,
  output [4:0] output6,
  output [4:0] output2,
  output [4:0] output7,
  output [4:0] output1,
  output [4:0] output8
);

  Multiplexer #(.width(30), .enable("false")) multiplexer_1 (
    .in0(30'h8427dc4), .in1(30'h8ef9084), .out({output2, output3, output4, output5, output6, output7}),
    .sel(\input ));

  assign output1 = {5{1'b0}};
  assign output8 = {5{1'b0}};
endmodule

module sub (
  input  in_1
);

  wire [4:0] main_1_output1, main_1_output2, main_1_output3, main_1_output4, main_1_output5, main_1_output6,
       main_1_output7, main_1_output8;

  DotMatrix #(.matrixcols(8), .matrixrows(5)) dotmatrix_1 (
    .col0(main_1_output8), .col1(main_1_output7), .col2(main_1_output6), .col3(main_1_output5),
    .col4(main_1_output4), .col5(main_1_output3), .col6(main_1_output2), .col7(main_1_output1));
  main main_1 (
    .\input (in_1), .output2(main_1_output2), .output1(main_1_output1), .output3(main_1_output3),
    .output4(main_1_output4), .output5(main_1_output5), .output6(main_1_output6), .output7(main_1_output7),
    .output8(main_1_output8));
endmodule
