// Logisim project bot_0.circ as structural Verilog: 1 circuit, main circuit main
module main (
  input  in_1,
  input  in_2,
  input  in_3,
  input  in_4,
  output CONFIRM,
  output [3:0] X,
  output out_7,
  output [3:0] Y
);

  wire _1ST_SHOT_DONE, and_1_out, CONFIRM_CLOCK, controlled_buffer_1_out, d_ff_1_qn, d_ff_2_q, not_1_out,
       not_2_out, or_1_out, or_2_out, POSITION_CLOCK, SHOOT, SHOOT1, SHOOT2;
  wire [3:0] main_4_output, main_5_output;

  D_Flip_Flop d_ff_1 (
    .clk(out_7), .D(out_7), .Q(_1ST_SHOT_DONE), .Qn(d_ff_1_qn), .reset(or_1_out));  // open: preset, en
  assign controlled_buffer_1_out = d_ff_1_qn ? in_2 : 1'bz;  // Controlled_Buffer controlled_buffer_1
  not not_1 (not_1_out, in_2);
  or or_1 (or_1_out, not_1_out, in_4);
  not not_2 (not_2_out, in_2);
  shooter_main main_1 (
    .in_1(in_1), .in_2(SHOOT), .in_3(in_2), .out_5(POSITION_CLOCK), .out_6(CONFIRM_CLOCK), .out_7(out_7),
    .in_4(in_4));
  Pull_Resistor pull_resistor_1 (.node(controlled_buffer_1_out));
  D_Flip_Flop d_ff_2 (.clk(out_7), .D(out_7), .Q(d_ff_2_q), .reset(or_2_out));  // open: Qn, preset, en
  or or_2 (or_2_out, not_2_out, in_4, SHOOT2);
  and and_1 (and_1_out, d_ff_2_q, in_2, _1ST_SHOT_DONE);
  tick_main main_2 (.in_1(in_1), .in_2(controlled_buffer_1_out), .out_3(SHOOT1));
  tick_main main_3 (.in_1(in_1), .in_2(and_1_out), .out_3(SHOOT2));
  Pull_Resistor pull_resistor_2 (.node(POSITION_CLOCK));
  Pull_Resistor pull_resistor_3 (.node(CONFIRM_CLOCK));
  or or_3 (SHOOT, SHOOT1, SHOOT2);
  random_num_generator_A_main main_4 (.GENERATE(POSITION_CLOCK), .OUTPUT(main_4_output));
  random_num_generator_B_main main_5 (.GENERATE(POSITION_CLOCK), .OUTPUT(main_5_output));
  assign CONFIRM = in_3 ? CONFIRM_CLOCK : 1'bz;  // Controlled_Buffer controlled_buffer_2
  assign X = in_3 ? main_4_output : 4'bz;  // Controlled_Buffer controlled_buffer_3
  assign Y = in_3 ? main_5_output : 4'bz;  // Controlled_Buffer controlled_buffer_4

  // Other names for the same wires on the sheet: CLK = in_1; CLR = in_4; ENABLE = in_3; SHOOT_PHASE = in_2;
  //   SHOT_DONE = out_7
endmodule
