// Logisim project bots.circ as structural Verilog: 1 circuit, main circuit main
module main (
  input  CURR_PLAYER,
  input  PREP_PHASE_END,
  input  CHECKING,
  input  WIN,
  input  CLR,
  input  HIT,
  input  CLK,
  input  [3:0] SHIPS_NUMBER,
  output ROTATED,
  output CONFIRM,
  output [3:0] X,
  output [3:0] Y
);

  wire _1ST_SHOT_DONE, _10SHIPS, and_1_out, and_2_out, and_4_out, BOOT_PHASE, CLK_t, comparator_1_eq,
       comparator_1_gt, controlled_buffer_4_out, controlled_buffer_7_out, counter_2_carry, counter_3_carry,
       d_ff_1_q, d_ff_2_q, d_ff_3_qn, demultiplexer_1_out0, demultiplexer_1_out1, demultiplexer_1_out2,
       not_1_out, not_3_out, not_4_out, not_5_out, not_6_out, or_1_out, or_3_out, or_4_out, POSITION_CLOCK,
       pull_resistor_3_node, pull_resistor_4_node, random_1_out, ROTATION_CLOCK, SHOOT, SHOOT1, SHOOT2,
       SHOOT_PHASE, SHOT_DONE;
  wire [4:0] counter_1_q, counter_3_q;

  Clock clock_1 (.out(CLK_t));
  not not_1 (not_1_out, PREP_PHASE_END);
  not not_2 (not_1_out, PREP_PHASE_END);
  not not_3 (not_3_out, _10SHIPS);
  and and_1 (and_1_out, BOOT_PHASE, CLK_t);
  and and_2 (and_2_out, CURR_PLAYER, ~BOOT_PHASE, PREP_PHASE_END);  // AND_Gate
  and and_3 (BOOT_PHASE, not_1_out, not_3_out);
  Comparator #(.width(4), .mode("unsigned")) comparator_1 (
    .a(SHIPS_NUMBER), .b(4'b1010), .gt(comparator_1_gt), .eq(comparator_1_eq));  // open: lt
  Demultiplexer #(.select(5)) demultiplexer_1 (
    .out0(demultiplexer_1_out0), .out1(demultiplexer_1_out1), .out2(demultiplexer_1_out2), .in(1'b1),
    .sel(counter_1_q));  // open: out3, out4, out5, out6, out7, out8, out9, out10, out11, out12, out13, out14, out15, out16, out17, out18, out19, out20, out21, out22, out23, out24, out25, out26, out27, out28, out29, out30, out31, en
  Counter #(.width(5), .max('h1f)) counter_1 (
    .Q(counter_1_q), .clk(and_1_out), .clr(CLR));  // open: load, D, count, carry
  S_R_Flip_Flop s_r_ff_1 (
    .S(and_2_out), .clk(or_1_out), .R(SHOT_DONE), .Q(SHOOT_PHASE));  // open: Qn, preset, reset, en
  or or_1 (or_1_out, and_2_out, SHOT_DONE);
  or or_2 (_10SHIPS, comparator_1_gt, comparator_1_eq);
  Counter #(.width(4), .max('hf)) counter_2 (
    .carry(counter_2_carry), .clk(controlled_buffer_4_out), .clr(or_3_out));  // open: load, D, count, Q
  D_Flip_Flop d_ff_1 (.clk(SHOOT), .D(SHOOT), .Q(d_ff_1_q), .reset(or_3_out));  // open: Qn, preset, en
  Pull_Resistor pull_resistor_1 (.node(SHOOT));
  not not_4 (not_4_out, SHOOT_PHASE);
  assign ROTATION_CLOCK = and_1_out ? demultiplexer_1_out0 : 1'bz;  // Controlled_Buffer controlled_buffer_1
  assign POSITION_CLOCK = and_1_out ? demultiplexer_1_out1 : 1'bz;  // Controlled_Buffer controlled_buffer_2
  assign CONFIRM = and_1_out ? demultiplexer_1_out2 : 1'bz;  // Controlled_Buffer controlled_buffer_3
  Counter #(.width(5), .max('h1f)) counter_3 (
    .Q(counter_3_q), .carry(counter_3_carry), .clk(counter_2_carry), .clr(or_3_out));  // open: load, D, count
  assign controlled_buffer_4_out = d_ff_1_q ? CLK_t : 1'bz;  // Controlled_Buffer controlled_buffer_4
  Pull_Resistor pull_resistor_2 (.node(controlled_buffer_4_out));
  or or_3 (or_3_out, not_4_out, counter_3_carry);
  Pull_Resistor pull_resistor_3 (.node(pull_resistor_3_node));
  Pull_Resistor pull_resistor_4 (.node(pull_resistor_4_node));
  Demultiplexer #(.select(5)) demultiplexer_2 (
    .out1(pull_resistor_3_node), .out3(pull_resistor_4_node), .out31(SHOT_DONE), .in(1'b1),
    .sel(counter_3_q), .en(d_ff_1_q));  // open: out0, out2, out4, out5, out6, out7, out8, out9, out10, out11, out12, out13, out14, out15, out16, out17, out18, out19, out20, out21, out22, out23, out24, out25, out26, out27, out28, out29, out30
  assign POSITION_CLOCK = d_ff_1_q ? pull_resistor_3_node : 1'bz;  // Controlled_Buffer controlled_buffer_5
  assign CONFIRM = d_ff_1_q ? pull_resistor_4_node : 1'bz;  // Controlled_Buffer controlled_buffer_6
  Pull_Resistor pull_resistor_5 (.node(SHOT_DONE));
  assign controlled_buffer_7_out = d_ff_3_qn ? SHOOT_PHASE : 1'bz;  // Controlled_Buffer controlled_buffer_7
  not not_5 (not_5_out, SHOOT_PHASE);
  D_Flip_Flop d_ff_2 (.clk(SHOT_DONE), .D(SHOT_DONE), .Q(d_ff_2_q), .reset(or_4_out));  // open: Qn, preset, en
  or or_4 (or_4_out, not_6_out, SHOOT2);
  not not_6 (not_6_out, SHOOT_PHASE);
  D_Flip_Flop d_ff_3 (
    .clk(SHOT_DONE), .D(SHOT_DONE), .Q(_1ST_SHOT_DONE), .Qn(d_ff_3_qn), .reset(not_5_out));  // open: preset, en
  and and_4 (and_4_out, d_ff_2_q, SHOOT_PHASE, _1ST_SHOT_DONE);
  Pull_Resistor pull_resistor_6 (.node(controlled_buffer_7_out));
  tick_main main_1 (.in_1(CLK_t), .in_2(and_4_out), .out_3(SHOOT2));
  tick_main main_2 (.in_1(CLK_t), .in_2(controlled_buffer_7_out), .out_3(SHOOT1));
  Pull_Resistor pull_resistor_7 (.node(POSITION_CLOCK));
  or or_5 (SHOOT, SHOOT1, SHOOT2);
  Random #(.width(1)) random_1 (.clk(ROTATION_CLOCK), .next(ROTATION_CLOCK), .out(random_1_out));  // open: clr
  Pull_Resistor pull_resistor_8 (.node(ROTATION_CLOCK));
  Counter #(.width(1), .max('h1)) counter_4 (
    .Q(ROTATED), .clk(random_1_out), .clr(CLR));  // open: load, D, count, carry
  Pull_Resistor pull_resistor_9 (.node(CONFIRM));
  random_num_generator_A_main main_3 (.GENERATE(POSITION_CLOCK), .OUTPUT(X));
  random_num_generator_B_main main_4 (.GENERATE(POSITION_CLOCK), .OUTPUT(Y));

  // Other names for the same wires on the sheet: CONFIRM_CLOCK = CONFIRM; SHIP_NUMBER[3:0] = SHIPS_NUMBER
endmodule
