// Logisim project cursor_module.circ as structural Verilog: 1 circuit, main circuit main
module main (
  input  CLK,
  input  [6:0] KEYBOARD_OUT,
  input  KEYBOARD_RST,
  output [29:0] TL_DATA,
  output [29:0] TR_DATA,
  output [29:0] BL_DATA,
  output [3:0] CUR_X,
  output [3:0] CUR_Y,
  output ROTATED,
  output [29:0] BR_DATA,
  output [4:0] TL_SEL,
  output [4:0] TR_SEL,
  output [4:0] BL_SEL,
  output [4:0] BR_SEL,
  output CONFIRM
);

  wire DOWN, LEFT, main_2_rotate_pressed, or_1_out, or_2_out, RIGHT, UP;
  wire [5:0] main_1_out_x_00, main_1_out_y_00;

  ship_xyr_to_screen_xy_main main_1 (
    .in_1(CUR_X), .in_2(CUR_Y), .in_3(1'b0), .OUT_X_00(main_1_out_x_00), .OUT_Y_00(main_1_out_y_00));  // open: OUT_X_01, OUT_Y_01, OUT_X_10, OUT_Y_10, OUT_X_11, OUT_Y_11
  KeyboardInputAWSD_main main_2 (
    .Up_pressed(UP), .Down_pressed(DOWN), .Left_pressed(LEFT), .Keyboard_out(KEYBOARD_OUT),
    .Keyboard_rst(KEYBOARD_RST), .Right_pressed(RIGHT), .Confirm_pressed(CONFIRM),
    .Rotate_pressed(main_2_rotate_pressed));
  screen_xy_to_screen_data_main main_3 (
    .SCREEN_X(main_1_out_x_00), .SCREEN_Y(main_1_out_y_00), .DATA_TO_DISPLAY(3'b000), .TL_SEL_OUT(TL_SEL),
    .TR_SEL_OUT(TR_SEL), .BL_SEL_OUT(BL_SEL), .BR_SEL_OUT(BR_SEL), .TL_DATA_OUT(TL_DATA),
    .TR_DATA_OUT(TR_DATA), .BL_DATA_OUT(BL_DATA), .BR_DATA_OUT(BR_DATA), .CLK(CLK), .ENABLE(1'b1));
  Counter #(.width(1), .max('h1)) counter_1 (
    .Q(ROTATED), .clk(main_2_rotate_pressed));  // open: load, D, count, carry, clr
  Counter #(.width(4), .max('hb)) counter_2 (.load(LEFT), .Q(CUR_X), .clk(or_1_out));  // open: D, count, carry, clr
  or or_1 (or_1_out, LEFT, RIGHT);
  Counter #(.width(4), .max('hb)) counter_3 (.load(UP), .Q(CUR_Y), .clk(or_2_out));  // open: D, count, carry, clr
  or or_2 (or_2_out, UP, DOWN);
endmodule
