// Logisim project demo_gora_dol.circ as structural Verilog: 1 circuit, main circuit main
module main (
  input  [31:0] in_1
);

  wire du_out, gura_out, or_1_out;
  wire [4:0] adder_1_out, bit_extender_1_out, controlled_buffer_1_out, multiplier_1_out, subtractor_1_out;
  wire [9:0] register_1_q;
  wire [31:0] shifter_1_out;

  Button gura (.out(gura_out));
  Button du (.out(du_out));
  Register #(.width(10)) register_1 (
    .D({controlled_buffer_1_out, register_1_q[4:0]}), .Q(register_1_q), .clk(or_1_out));  // open: en, clr
  or or_1 (or_1_out, gura_out, du_out);
  Adder #(.width(5)) adder_1 (.a(register_1_q[9:5]), .b(5'b00001), .out(adder_1_out));  // open: cin, cout
  Subtractor #(.width(5)) subtractor_1 (
    .a(register_1_q[9:5]), .b(5'b00001), .out(subtractor_1_out));  // open: bin, bout
  assign controlled_buffer_1_out = gura_out ? adder_1_out : 5'bz;  // Controlled_Buffer controlled_buffer_1
  assign controlled_buffer_1_out = du_out ? subtractor_1_out : 5'bz;  // Controlled_Buffer controlled_buffer_2
  Bit_Extender #(.in_width(5), .out_width(5)) bit_extender_1 (.in(multiplier_1_out), .out(bit_extender_1_out));
  Multiplier #(.width(5)) multiplier_1 (
    .a(register_1_q[9:5]), .b(5'b00010), .out(multiplier_1_out));  // open: cin, cout
  Shifter #(.width(32)) shifter_1 (.in(in_1), .\dist (bit_extender_1_out), .out(shifter_1_out));
  DotMatrix #(.matrixrows(32), .dotshape("circle")) dotmatrix_1 (
    .col0(shifter_1_out), .col1(shifter_1_out), .col2(shifter_1_out), .col3(shifter_1_out),
    .col4(shifter_1_out));

  // Notes on the sheet:
  //   pozycja
  //   x
  //   y
endmodule
