// Logisim project demuxor_30x30x3.circ as structural Verilog: 1 circuit, main circuit main
module main (
  input  [4:0] SELECT_0,
  input  [4:0] SELECT_1,
  input  [4:0] SELECT_2,
  input  [29:0] DATA_0,
  input  [29:0] DATA_1,
  input  [29:0] DATA_2,
  output [29:0] OUT_0,
  output [29:0] OUT_6,
  output [29:0] OUT_c,
  output [29:0] OUT_12,
  output [29:0] OUT_18,
  output [29:0] OUT_1,
  output [29:0] OUT_7,
  output [29:0] OUT_d,
  output [29:0] OUT_13,
  output [29:0] OUT_19,
  output [29:0] OUT_2,
  output [29:0] OUT_8,
  output [29:0] OUT_e,
  output [29:0] OUT_14,
  output [29:0] OUT_1a,
  output [29:0] OUT_3,
  output [29:0] OUT_9,
  output [29:0] OUT_f,
  output [29:0] OUT_15,
  output [29:0] OUT_1b,
  output [29:0] OUT_4,
  output [29:0] OUT_a,
  output [29:0] OUT_10,
  output [29:0] OUT_16,
  output [29:0] OUT_1c,
  output [29:0] OUT_5,
  output [29:0] OUT_b,
  output [29:0] OUT_11,
  output [29:0] OUT_17,
  output [29:0] OUT_1d
);

  wire [29:0] _00, _0a, _0b, _0c, _0d, _0e, _0f, _01, _01a, _1a, _01b, _1b, _01c, _1c, _01d, _1d, _1e, _1f,
       _02, _2a, _2b, _2c, _2d, _2e, _2f, _03, _04, _05, _06, _07, _08, _09, _010, _10, _011, _11, _11a,
       _11b, _11c, _11d, _012, _12, _013, _13, _014, _14, _015, _15, _016, _16, _017, _17, _018, _18, _019,
       _19, _20, _21, _21a, _21b, _21c, _21d, _22, _23, _24, _25, _26, _27, _28, _29, _110, _111, _112, _113,
       _114, _115, _116, _117, _118, _119, _210, _211, _212, _213, _214, _215, _216, _217, _218, _219;

  Pull_Resistor pull_resistor_1 (.node(SELECT_0));
  assign OUT_0 = _00 | _10 | _20;  // OR_Gate or_1, 30 bits wide
  assign OUT_1 = _01 | _11 | _21;  // OR_Gate or_2, 30 bits wide
  assign OUT_2 = _02 | _12 | _22;  // OR_Gate or_3, 30 bits wide
  assign OUT_3 = _03 | _13 | _23;  // OR_Gate or_4, 30 bits wide
  assign OUT_4 = _04 | _14 | _24;  // OR_Gate or_5, 30 bits wide
  assign OUT_5 = _05 | _15 | _25;  // OR_Gate or_6, 30 bits wide
  Demultiplexer #(.select(5), .width(30), .enable("false")) demultiplexer_1 (
    .out0(_00), .out1(_01), .out2(_02), .out3(_03), .out4(_04), .out5(_05), .out6(_06), .out7(_07),
    .out8(_08), .out9(_09), .out10(_0a), .out11(_0b), .out12(_0c), .out13(_0d), .out14(_0e), .out15(_0f),
    .out16(_010), .out17(_011), .out18(_012), .out19(_013), .out20(_014), .out21(_015), .out22(_016),
    .out23(_017), .out24(_018), .out25(_019), .out26(_01a), .out27(_01b), .out28(_01c), .out29(_01d),
    .in(DATA_0), .sel(SELECT_0));  // open: out30, out31
  Pull_Resistor pull_resistor_2 (.node(DATA_0));
  assign OUT_6 = _06 | _16 | _26;  // OR_Gate or_7, 30 bits wide
  assign OUT_7 = _07 | _17 | _27;  // OR_Gate or_8, 30 bits wide
  assign OUT_8 = _08 | _18 | _28;  // OR_Gate or_9, 30 bits wide
  assign OUT_9 = _09 | _19 | _29;  // OR_Gate or_10, 30 bits wide
  assign OUT_a = _0a | _1a | _2a;  // OR_Gate or_11, 30 bits wide
  assign OUT_b = _0b | _1b | _2b;  // OR_Gate or_12, 30 bits wide
  Pull_Resistor pull_resistor_3 (.node(SELECT_1));
  Demultiplexer #(.select(5), .width(30), .enable("false")) demultiplexer_2 (
    .out0(_10), .out1(_11), .out2(_12), .out3(_13), .out4(_14), .out5(_15), .out6(_16), .out7(_17),
    .out8(_18), .out9(_19), .out10(_1a), .out11(_1b), .out12(_1c), .out13(_1d), .out14(_1e), .out15(_1f),
    .out16(_110), .out17(_111), .out18(_112), .out19(_113), .out20(_114), .out21(_115), .out22(_116),
    .out23(_117), .out24(_118), .out25(_119), .out26(_11a), .out27(_11b), .out28(_11c), .out29(_11d),
    .in(DATA_1), .sel(SELECT_1));  // open: out30, out31
  Pull_Resistor pull_resistor_4 (.node(DATA_1));
  assign OUT_c = _0c | _1c | _2c;  // OR_Gate or_13, 30 bits wide
  assign OUT_d = _0d | _1d | _2d;  // OR_Gate or_14, 30 bits wide
  assign OUT_e = _0e | _1e | _2e;  // OR_Gate or_15, 30 bits wide
  assign OUT_f = _0f | _1f | _2f;  // OR_Gate or_16, 30 bits wide
  assign OUT_10 = _010 | _110 | _210;  // OR_Gate or_17, 30 bits wide
  assign OUT_11 = _011 | _111 | _211;  // OR_Gate or_18, 30 bits wide
  Pull_Resistor pull_resistor_5 (.node(SELECT_2));
  assign OUT_12 = _012 | _112 | _212;  // OR_Gate or_19, 30 bits wide
  assign OUT_13 = _013 | _113 | _213;  // OR_Gate or_20, 30 bits wide
  assign OUT_14 = _014 | _114 | _214;  // OR_Gate or_21, 30 bits wide
  assign OUT_15 = _015 | _115 | _215;  // OR_Gate or_22, 30 bits wide
  assign OUT_16 = _016 | _116 | _216;  // OR_Gate or_23, 30 bits wide
  assign OUT_17 = _017 | _117 | _217;  // OR_Gate or_24, 30 bits wide
  Demultiplexer #(.select(5), .width(30), .enable("false")) demultiplexer_3 (
    .out0(_20), .out1(_21), .out2(_22), .out3(_23), .out4(_24), .out5(_25), .out6(_26), .out7(_27),
    .out8(_28), .out9(_29), .out10(_2a), .out11(_2b), .out12(_2c), .out13(_2d), .out14(_2e), .out15(_2f),
    .out16(_210), .out17(_211), .out18(_212), .out19(_213), .out20(_214), .out21(_215), .out22(_216),
    .out23(_217), .out24(_218), .out25(_219), .out26(_21a), .out27(_21b), .out28(_21c), .out29(_21d),
    .in(DATA_2), .sel(SELECT_2));  // open: out30, out31
  Pull_Resistor pull_resistor_6 (.node(DATA_2));
  assign OUT_18 = _018 | _118 | _218;  // OR_Gate or_25, 30 bits wide
  assign OUT_19 = _019 | _119 | _219;  // OR_Gate or_26, 30 bits wide
  assign OUT_1a = _01a | _11a | _21a;  // OR_Gate or_27, 30 bits wide
  assign OUT_1b = _01b | _11b | _21b;  // OR_Gate or_28, 30 bits wide
  assign OUT_1c = _01c | _11c | _21c;  // OR_Gate or_29, 30 bits wide
  assign OUT_1d = _01d | _11d | _21d;  // OR_Gate or_30, 30 bits wide

  // Notes on the sheet:
  //   last 2 data lanes - unused
  //   last 2 data lanes - unused
  //   last 2 data lanes - unused
endmodule
