// Logisim project drawing_select.circ as structural Verilog: 1 circuit, main circuit main
module main (
  input  [2:0] SHIP_SELECT,
  input  CLK,
  input  [4:0] in_3,
  input  [4:0] in_4,
  input  [4:0] in_5,
  input  [4:0] in_6,
  input  [4:0] in_7,
  output [4:0] DATA
);

  wire [2:0] counter_1_q;
  wire [4:0] rom_1_data, rom_2_data, rom_3_data, rom_4_data, rom_5_data, rom_6_data, rom_7_data, rom_8_data;

  Counter #(.width(3), .max('h4)) counter_1 (.Q(counter_1_q), .clk(CLK));  // open: load, D, count, carry, clr
  ROM #(.addrWidth(3), .dataWidth(5)) rom_1 (.addr(counter_1_q), .data(rom_1_data));  // open: sel
  ROM #(.addrWidth(3), .dataWidth(5)) rom_2 (.addr(counter_1_q), .data(rom_2_data));  // open: sel
  ROM #(.addrWidth(3), .dataWidth(5)) rom_3 (.addr(counter_1_q), .data(rom_3_data));  // open: sel
  ROM #(.addrWidth(3), .dataWidth(5)) rom_4 (.addr(counter_1_q), .data(rom_4_data));  // open: sel
  ROM #(.addrWidth(3), .dataWidth(5)) rom_5 (.addr(counter_1_q), .data(rom_5_data));  // open: sel
  ROM #(.addrWidth(3), .dataWidth(5)) rom_6 (.addr(counter_1_q), .data(rom_6_data));  // open: sel
  ROM #(.addrWidth(3), .dataWidth(5)) rom_7 (.addr(counter_1_q), .data(rom_7_data));  // open: sel
  ROM #(.addrWidth(3), .dataWidth(5)) rom_8 (.addr(counter_1_q), .data(rom_8_data));  // open: sel
  Multiplexer #(.select(3), .width(5), .enable("false")) multiplexer_1 (
    .in0(rom_1_data), .in1(rom_2_data), .in2(rom_3_data), .in3(rom_4_data), .in4(rom_5_data),
    .in5(rom_6_data), .in6(rom_7_data), .in7(rom_8_data), .out(DATA), .sel(SHIP_SELECT));
  DotMatrix #(.matrixrows(5)) dotmatrix_1 (.col0(in_3), .col1(in_4), .col2(in_5), .col3(in_6), .col4(in_7));
  // Probe on in_3
  // Probe on in_4
  // Probe on in_5
  // Probe on in_6
  // Probe on in_7

  // Notes on the sheet:
  //   cursor
  //   ship
  //   sunk ship
  //   not hit
  //   contents of rom_1 (hex, n*v repeats v):
  //   1b 11 0 11 1b
  //   contents of rom_2 (hex, n*v repeats v):
  //   0 e a e
  //   contents of rom_3 (hex, n*v repeats v):
  //   0 a 4 a
  //   contents of rom_4 (hex, n*v repeats v):
  //   0 0 4
endmodule
