// Logisim project logic.circ as structural Verilog: 1 circuit, main circuit main
module main (
  input  in_1,
  output [31:0] out_2,
  output [31:0] out_3,
  output [31:0] out_4,
  output [31:0] out_5,
  output [31:0] out_6,
  output [31:0] out_7,
  output [31:0] out_8,
  output [31:0] out_9,
  output [31:0] out_10,
  output [31:0] out_11,
  output [31:0] out_12,
  output [31:0] out_13,
  output [31:0] out_14,
  output [31:0] out_15,
  output [31:0] out_16,
  output [31:0] out_17,
  output [31:0] out_18,
  output [31:0] out_19,
  output [31:0] out_20,
  output [31:0] out_21,
  output [31:0] out_22,
  output [31:0] out_23,
  output [31:0] out_24,
  output [31:0] out_25,
  output [31:0] out_26,
  output [31:0] out_27,
  output [31:0] out_28,
  output [31:0] out_29,
  output [31:0] out_30,
  output [31:0] out_31,
  output [31:0] out_32,
  output [31:0] out_33,
  output [31:0] out_34,
  output [31:0] out_35,
  output [31:0] out_36,
  output [31:0] out_37,
  output [31:0] out_38,
  output [31:0] out_39,
  output [31:0] out_40,
  output [31:0] out_41,
  output [31:0] out_42,
  output [31:0] out_43,
  output [31:0] out_44,
  output [31:0] out_45,
  output [31:0] out_46,
  output [31:0] out_47,
  output [31:0] out_48,
  output [31:0] out_49,
  output [31:0] out_50,
  output [31:0] out_51,
  output [31:0] out_52,
  output [31:0] out_53,
  output [31:0] out_54,
  output [31:0] out_55,
  output [31:0] out_56,
  output [31:0] out_57,
  output [31:0] out_58,
  output [31:0] out_59,
  output [31:0] out_60,
  output [31:0] out_61,
  output [31:0] out_62,
  output [31:0] out_63,
  output [31:0] out_64,
  output [31:0] out_65,
  output [31:0] out_66,
  output [31:0] out_67,
  output [31:0] out_68,
  output [31:0] out_69,
  output [31:0] out_70,
  output [31:0] out_71,
  output [31:0] out_72,
  output [31:0] out_73,
  output [31:0] out_74,
  output [31:0] out_75,
  output [31:0] out_76,
  output [31:0] out_77,
  output [31:0] out_78,
  output [31:0] out_79,
  output [31:0] out_80,
  output [31:0] out_81,
  output [31:0] out_82,
  output [31:0] out_83,
  output [31:0] out_84,
  output [31:0] out_85,
  output [31:0] out_86,
  output [31:0] out_87,
  output [31:0] out_88,
  output [31:0] out_89,
  output [31:0] out_90,
  output [31:0] out_91,
  output [31:0] out_92,
  output [31:0] out_93,
  output [31:0] out_94,
  output [31:0] out_95,
  output [31:0] out_96,
  output [31:0] out_97,
  output [31:0] out_98,
  output [31:0] out_99,
  output [31:0] out_100,
  output [31:0] out_101,
  output [31:0] out_102,
  output [31:0] out_103,
  output [31:0] out_104,
  output [31:0] out_105,
  output [31:0] out_106,
  output [31:0] out_107,
  output [31:0] out_108,
  output [31:0] out_109,
  output [31:0] out_110,
  output [31:0] out_111,
  output [31:0] out_112,
  output [31:0] out_113,
  output [31:0] out_114,
  output [31:0] out_115,
  output [31:0] out_116,
  output [31:0] out_117,
  output [31:0] out_118,
  output [31:0] out_119,
  output [31:0] out_120,
  output [31:0] out_121,
  output [31:0] out_122,
  output [31:0] out_123,
  output [31:0] out_124,
  output [31:0] out_125,
  output [31:0] out_126,
  output [31:0] out_127,
  output [31:0] out_128,
  output [31:0] out_129
);

  wire main_1_f_2_clk_in;
  wire [1:0] main_1_curr_disp;
  wire [4:0] COL;
  wire [6:0] counter_1_q;
  wire [31:0] LB, LT, main_1_mem_out, RB, rom_1_data, RT;

  Counter #(.width(7), .max('h7f)) counter_1 (
    .Q(counter_1_q), .clk(main_1_f_2_clk_in));  // open: load, D, count, carry, clr
  ROM #(.addrWidth(7), .dataWidth(32)) rom_1 (.addr(counter_1_q), .data(rom_1_data));  // open: sel
  screen_driver_main main_1 (
    .clk(in_1), .curr_disp(main_1_curr_disp), .curr_col(COL), .mem_in(rom_1_data), .mem_out(main_1_mem_out),
    .f_2_clk_in(main_1_f_2_clk_in));
  Demultiplexer #(.select(2), .width(32)) demultiplexer_1 (
    .out0(LT), .out1(RT), .out2(LB), .out3(RB), .in(main_1_mem_out), .sel(main_1_curr_disp));  // open: en
  Demultiplexer #(.select(5), .width(32)) demultiplexer_2 (
    .out0(out_2), .out1(out_3), .out2(out_4), .out3(out_5), .out4(out_6), .out5(out_7), .out6(out_8),
    .out7(out_9), .out8(out_10), .out9(out_11), .out10(out_12), .out11(out_13), .out12(out_14),
    .out13(out_15), .out14(out_16), .out15(out_17), .out16(out_18), .out17(out_19), .out18(out_20),
    .out19(out_21), .out20(out_22), .out21(out_23), .out22(out_24), .out23(out_25), .out24(out_26),
    .out25(out_27), .out26(out_28), .out27(out_29), .out28(out_30), .out29(out_31), .out30(out_32),
    .out31(out_33), .in(LT), .sel(COL));  // open: en
  Demultiplexer #(.select(5), .width(32)) demultiplexer_3 (
    .out0(out_66), .out1(out_67), .out2(out_68), .out3(out_69), .out4(out_70), .out5(out_71), .out6(out_72),
    .out7(out_73), .out8(out_74), .out9(out_75), .out10(out_76), .out11(out_77), .out12(out_78),
    .out13(out_79), .out14(out_80), .out15(out_81), .out16(out_82), .out17(out_83), .out18(out_84),
    .out19(out_85), .out20(out_86), .out21(out_87), .out22(out_88), .out23(out_89), .out24(out_90),
    .out25(out_91), .out26(out_92), .out27(out_93), .out28(out_94), .out29(out_95), .out30(out_96),
    .out31(out_97), .in(LB), .sel(COL));  // open: en
  Demultiplexer #(.select(5), .width(32)) demultiplexer_4 (
    .out0(out_34), .out1(out_35), .out2(out_36), .out3(out_37), .out4(out_38), .out5(out_39), .out6(out_40),
    .out7(out_41), .out8(out_42), .out9(out_43), .out10(out_44), .out11(out_45), .out12(out_46),
    .out13(out_47), .out14(out_48), .out15(out_49), .out16(out_50), .out17(out_51), .out18(out_52),
    .out19(out_53), .out20(out_54), .out21(out_55), .out22(out_56), .out23(out_57), .out24(out_58),
    .out25(out_59), .out26(out_60), .out27(out_61), .out28(out_62), .out29(out_63), .out30(out_64),
    .out31(out_65), .in(RT), .sel(COL));  // open: en
  Demultiplexer #(.select(5), .width(32)) demultiplexer_5 (
    .out0(out_98), .out1(out_99), .out2(out_100), .out3(out_101), .out4(out_102), .out5(out_103),
    .out6(out_104), .out7(out_105), .out8(out_106), .out9(out_107), .out10(out_108), .out11(out_109),
    .out12(out_110), .out13(out_111), .out14(out_112), .out15(out_113), .out16(out_114), .out17(out_115),
    .out18(out_116), .out19(out_117), .out20(out_118), .out21(out_119), .out22(out_120), .out23(out_121),
    .out24(out_122), .out25(out_123), .out26(out_124), .out27(out_125), .out28(out_126), .out29(out_127),
    .out30(out_128), .out31(out_129), .in(RB), .sel(COL));  // open: en

  // Other names for the same wires on the sheet: CLK = in_1

  // Notes on the sheet:
  //   contents of rom_1 (hex, n*v repeats v):
  //   7004146 51c71c2 70011c7 1fffffff 10410410 70410410 d0410410 70410410 10410410 1fffffff 10410410
  //   f0410410 f0410410 70410410 10410410 1fffffff 10410410 f0410410 b0410410 b0410410 10410410 1fffffff
  //   10410410 f0410410 b0410410 50410410 10410410 1fffffff 10410410 f0410410 f0410410 b0410410 10410410
  //   1fffffff 10410410 f0410410 d0410410 90410410 10410410 1fffffff 10410410 f0410410 b0410410 70410410
  //   10410410 1fffffff 10410410 f0410410 50410410 f0410410 10410410 1fffffff 10410410 b0410410 f0410410
  //   b0410410 10410410 1fffffff 10410410 70410410 30410410 f0410410 10410410 1fffffff 4710518 1c310718
  //   1031c51c ffffffff 5*41041041 ffffffff 5*41041041 ffffffff 5*41041041 ffffffff 5*41041041 ffffffff
  //   5*41041041 ffffffff 5*41041041 ffffffff 5*41041041 ffffffff 5*41041041 ffffffff 5*41041041 ffffffff
  //   5*41041041 ffffffff
endmodule
