// Logisim project main.circ as structural Verilog: 1 circuit, main circuit main
module main (
  input  in_1
);

  wire main_2_out_2, main_2_out_3, main_2_out_4, main_2_out_5, main_2_out_6, main_2_out_7, main_2_out_8,
       main_2_out_9, main_2_out_10, main_2_out_11, main_2_out_12, main_2_out_13, main_2_out_14,
       main_2_out_15, main_2_out_16, main_2_out_17, main_2_out_18, main_2_out_19, main_2_out_20,
       main_2_out_21, main_2_out_22, main_2_out_23, main_2_out_24, main_2_out_25, main_2_out_26,
       main_2_out_27, main_2_out_28, main_2_out_29, main_2_out_30, main_2_out_31, main_2_out_32,
       main_2_out_33, main_3_out_2, main_3_out_3, main_3_out_4, main_3_out_5, main_3_out_6, main_3_out_7,
       main_3_out_8, main_3_out_9, main_3_out_10, main_3_out_11, main_3_out_12, main_3_out_13, main_3_out_14,
       main_3_out_15, main_3_out_16, main_3_out_17, main_3_out_18, main_3_out_19, main_3_out_20,
       main_3_out_21, main_3_out_22, main_3_out_23, main_3_out_24, main_3_out_25, main_3_out_26,
       main_3_out_27, main_3_out_28, main_3_out_29, main_3_out_30, main_3_out_31, main_3_out_32,
       main_3_out_33, main_4_out_2, main_4_out_3, main_4_out_4, main_4_out_5, main_4_out_6, main_4_out_7,
       main_4_out_8, main_4_out_9, main_4_out_10, main_4_out_11, main_4_out_12, main_4_out_13, main_4_out_14,
       main_4_out_15, main_4_out_16, main_4_out_17, main_4_out_18, main_4_out_19, main_4_out_20,
       main_4_out_21, main_4_out_22, main_4_out_23, main_4_out_24, main_4_out_25, main_4_out_26,
       main_4_out_27, main_4_out_28, main_4_out_29, main_4_out_30, main_4_out_31, main_4_out_32,
       main_4_out_33, main_5_out_2, main_5_out_3, main_5_out_4, main_5_out_5, main_5_out_6, main_5_out_7,
       main_5_out_8, main_5_out_9, main_5_out_10, main_5_out_11, main_5_out_12, main_5_out_13, main_5_out_14,
       main_5_out_15, main_5_out_16, main_5_out_17, main_5_out_18, main_5_out_19, main_5_out_20,
       main_5_out_21, main_5_out_22, main_5_out_23, main_5_out_24, main_5_out_25, main_5_out_26,
       main_5_out_27, main_5_out_28, main_5_out_29, main_5_out_30, main_5_out_31, main_5_out_32,
       main_5_out_33;
  wire [4:0] main_1_out_7, main_1_out_8, main_1_out_9, main_1_out_10, main_1_out_11, main_1_out_13,
       main_1_out_14;
  wire [29:0] main_1_out_20, main_1_out_21, main_1_out_22, main_1_out_23, main_1_out_24, main_1_out_25,
       main_1_out_26, main_1_out_27, main_1_out_28, main_1_out_29, main_1_out_30, main_1_out_31,
       main_1_out_32, main_1_out_33, main_1_out_34, main_1_out_35, main_1_out_36, main_1_out_37,
       main_1_out_38, main_1_out_39, main_1_out_40, main_1_out_41, main_1_out_42, main_1_out_43,
       main_1_out_44, main_1_out_45, main_1_out_46, main_1_out_47, main_1_out_48, main_1_out_49,
       main_1_out_50, main_1_out_51, main_1_out_52, main_1_out_53, main_1_out_54, main_1_out_55,
       main_1_out_56, main_1_out_57, main_1_out_58, main_1_out_59, main_1_out_60, main_1_out_61,
       main_1_out_62, main_1_out_63, main_1_out_64, main_1_out_65, main_1_out_66, main_1_out_67,
       main_1_out_68, main_1_out_69, main_1_out_70, main_1_out_71, main_1_out_72, main_1_out_73,
       main_1_out_74, main_1_out_75, main_1_out_76, main_1_out_77, main_1_out_78, main_1_out_79,
       main_1_out_80, main_1_out_81, main_1_out_82, main_1_out_83, main_1_out_84, main_1_out_85,
       main_1_out_86, main_1_out_87, main_1_out_88, main_1_out_89, main_1_out_90, main_1_out_91,
       main_1_out_92, main_1_out_93, main_1_out_94, main_1_out_95, main_1_out_96, main_1_out_97,
       main_1_out_98, main_1_out_99, main_1_out_100, main_1_out_101, main_1_out_102, main_1_out_103,
       main_1_out_104, main_1_out_105, main_1_out_106, main_1_out_107, main_1_out_108, main_1_out_109,
       main_1_out_110, main_1_out_111, main_1_out_112, main_1_out_113, main_1_out_114, main_1_out_115,
       main_1_out_116, main_1_out_117, main_1_out_118, main_1_out_119, main_1_out_120, main_1_out_121,
       main_1_out_122, main_1_out_123, main_1_out_124, main_1_out_125, main_1_out_126, main_1_out_127,
       main_1_out_128, main_1_out_129, main_1_out_130, main_1_out_131, main_1_out_132, main_1_out_133,
       main_1_out_134, main_1_out_135, main_1_out_137, main_1_out_139, main_1_out_140, main_1_out_141,
       main_1_out_142, main_1_out_143, main_1_out_144, main_1_out_145, main_1_out_146, main_1_out_147,
       main_1_out_148, main_1_out_149, main_1_out_150, main_1_out_151, main_1_out_152, main_1_out_153,
       main_1_out_154, main_1_out_155, main_1_out_156, main_1_out_157, main_1_out_158, main_1_out_159,
       main_1_out_160, main_1_out_161, main_1_out_162, main_1_out_163, main_1_out_164, main_1_out_165,
       main_1_out_166, main_1_out_167, main_1_out_168, main_1_out_169, main_1_out_170, main_1_out_171,
       main_1_out_172, main_1_out_173, main_1_out_174, main_1_out_175, main_1_out_176, main_1_out_177,
       main_1_out_178, main_1_out_179, main_1_out_180, main_1_out_181, main_1_out_182, main_1_out_183,
       main_1_out_184, main_1_out_185, main_1_out_186, main_1_out_187, main_1_out_188, main_1_out_189,
       main_1_out_190, main_1_out_191, main_1_out_192, main_1_out_193, main_1_out_194, main_1_out_195,
       main_1_out_196, main_1_out_197, main_1_out_198, main_1_out_199, main_1_out_200, main_1_out_201,
       main_1_out_202, main_1_out_203, main_1_out_204, main_1_out_205, main_1_out_206, main_1_out_207,
       main_1_out_208, main_1_out_209, main_1_out_210, main_1_out_211, main_1_out_212, main_1_out_213,
       main_1_out_214, main_1_out_215, main_1_out_216, main_1_out_217, main_1_out_218, main_1_out_219,
       main_1_out_220, main_1_out_221, main_1_out_222, main_1_out_223, main_1_out_224, main_1_out_225,
       main_1_out_226, main_1_out_227, main_1_out_228, main_1_out_229, main_1_out_230, main_1_out_231,
       main_1_out_232, main_1_out_233, main_1_out_234, main_1_out_235, main_1_out_236, main_1_out_237,
       main_1_out_238, main_1_out_239, main_1_out_240, main_1_out_241, main_1_out_242, main_1_out_243,
       main_1_out_244, main_1_out_245, main_1_out_246, main_1_out_247, main_1_out_248, main_1_out_249,
       main_1_out_250, main_1_out_251, main_1_out_252, main_1_out_253, main_1_out_254, main_1_out_255,
       main_1_out_257, main_1_out_259, main_1_out_260, main_1_out_261, main_1_out_262, main_1_out_263,
       main_1_out_264, main_1_out_265, main_1_out_266, main_1_out_267, main_1_out_268, main_1_out_269,
       main_1_out_270, main_1_out_271, main_1_out_272, main_1_out_273, main_1_out_274, main_1_out_275,
       main_1_out_276, main_1_out_277, main_1_out_278, main_1_out_279, main_1_out_280, main_1_out_281,
       main_1_out_282, main_1_out_283, main_1_out_284, main_1_out_285, main_1_out_286, main_1_out_287,
       main_1_out_288, main_1_out_289, main_1_out_290, main_1_out_291, main_1_out_292, main_1_out_293,
       main_1_out_294, main_1_out_295, main_1_out_296, main_1_out_297, main_1_out_298, main_1_out_299,
       main_1_out_300, main_1_out_301, main_1_out_302, main_1_out_303, main_1_out_304, main_1_out_305,
       main_1_out_306, main_1_out_307, main_1_out_308, main_1_out_309, main_1_out_310, main_1_out_311,
       main_1_out_312, main_1_out_313, main_1_out_314, main_1_out_315, main_1_out_316, main_1_out_317,
       main_1_out_318, main_1_out_319, main_1_out_320, main_1_out_321, main_1_out_322, main_1_out_323,
       main_1_out_324, main_1_out_325, main_1_out_326, main_1_out_327, main_1_out_328, main_1_out_329,
       main_1_out_330, main_1_out_331, main_1_out_332, main_1_out_333, main_1_out_334, main_1_out_335,
       main_1_out_336, main_1_out_337, main_1_out_338, main_1_out_339, main_1_out_340, main_1_out_341,
       main_1_out_342, main_1_out_343, main_1_out_344, main_1_out_345, main_1_out_346, main_1_out_347,
       main_1_out_348, main_1_out_349, main_1_out_350, main_1_out_351, main_1_out_352, main_1_out_353,
       main_1_out_354, main_1_out_355, main_1_out_356, main_1_out_357, main_1_out_358, main_1_out_359,
       main_1_out_360, main_1_out_361, main_1_out_362, main_1_out_363, main_1_out_364, main_1_out_365,
       main_1_out_366, main_1_out_367, main_1_out_368, main_1_out_369, main_1_out_370, main_1_out_371,
       main_1_out_372, main_1_out_373, main_1_out_374, main_1_out_375, main_1_out_377, main_1_out_379,
       main_1_out_380, main_1_out_381, main_1_out_382, main_1_out_383, main_1_out_384, main_1_out_385,
       main_1_out_386, main_1_out_387, main_1_out_388, main_1_out_389, main_1_out_390, main_1_out_391,
       main_1_out_392, main_1_out_393, main_1_out_394, main_1_out_395, main_1_out_396, main_1_out_397,
       main_1_out_398, main_1_out_399, main_1_out_400, main_1_out_401, main_1_out_402, main_1_out_403,
       main_1_out_404, main_1_out_405, main_1_out_406, main_1_out_407, main_1_out_408, main_1_out_409,
       main_1_out_410, main_1_out_411, main_1_out_412, main_1_out_413, main_1_out_414, main_1_out_415,
       main_1_out_416, main_1_out_417, main_1_out_418, main_1_out_419, main_1_out_420, main_1_out_421,
       main_1_out_422, main_1_out_423, main_1_out_424, main_1_out_425, main_1_out_426, main_1_out_427,
       main_1_out_428, main_1_out_429, main_1_out_430, main_1_out_431, main_1_out_432, main_1_out_433,
       main_1_out_434, main_1_out_435, main_1_out_436, main_1_out_437, main_1_out_438, main_1_out_439,
       main_1_out_440, main_1_out_441, main_1_out_442, main_1_out_443, main_1_out_444, main_1_out_445,
       main_1_out_446, main_1_out_447, main_1_out_448, main_1_out_449, main_1_out_450, main_1_out_451,
       main_1_out_452, main_1_out_453, main_1_out_454, main_1_out_455, main_1_out_456, main_1_out_457,
       main_1_out_458, main_1_out_459, main_1_out_460, main_1_out_461, main_1_out_462, main_1_out_463,
       main_1_out_464, main_1_out_465, main_1_out_466, main_1_out_467, main_1_out_468, main_1_out_469,
       main_1_out_470, main_1_out_471, main_1_out_472, main_1_out_473, main_1_out_474, main_1_out_475,
       main_1_out_476, main_1_out_477, main_1_out_478, main_1_out_479, main_1_out_480, main_1_out_481,
       main_1_out_482, main_1_out_483, main_1_out_484, main_1_out_485, main_1_out_486, main_1_out_487,
       main_1_out_488, main_1_out_489, main_1_out_490, main_1_out_491, main_1_out_492, main_1_out_493,
       main_1_out_494, main_1_out_495, main_1_out_497, main_1_out_499;

  app_main main_1 (
    .out_132(main_1_out_132), .out_128(main_1_out_128), .out_124(main_1_out_124), .out_120(main_1_out_120),
    .out_116(main_1_out_116), .out_112(main_1_out_112), .out_108(main_1_out_108), .out_104(main_1_out_104),
    .out_100(main_1_out_100), .out_96(main_1_out_96), .out_92(main_1_out_92), .out_88(main_1_out_88),
    .out_84(main_1_out_84), .out_80(main_1_out_80), .out_76(main_1_out_76), .out_72(main_1_out_72),
    .out_68(main_1_out_68), .out_64(main_1_out_64), .out_60(main_1_out_60), .out_56(main_1_out_56),
    .out_52(main_1_out_52), .out_48(main_1_out_48), .out_44(main_1_out_44), .out_40(main_1_out_40),
    .out_36(main_1_out_36), .out_32(main_1_out_32), .out_28(main_1_out_28), .out_24(main_1_out_24),
    .out_20(main_1_out_20), .out_21(main_1_out_21), .out_25(main_1_out_25), .out_29(main_1_out_29),
    .out_33(main_1_out_33), .out_37(main_1_out_37), .out_41(main_1_out_41), .out_45(main_1_out_45),
    .out_49(main_1_out_49), .out_53(main_1_out_53), .out_57(main_1_out_57), .out_61(main_1_out_61),
    .out_65(main_1_out_65), .out_69(main_1_out_69), .out_73(main_1_out_73), .out_77(main_1_out_77),
    .out_81(main_1_out_81), .out_85(main_1_out_85), .out_89(main_1_out_89), .out_93(main_1_out_93),
    .out_97(main_1_out_97), .out_101(main_1_out_101), .out_105(main_1_out_105), .out_109(main_1_out_109),
    .out_113(main_1_out_113), .out_117(main_1_out_117), .out_121(main_1_out_121), .out_125(main_1_out_125),
    .out_129(main_1_out_129), .out_133(main_1_out_133), .out_137(main_1_out_137), .out_142(main_1_out_142),
    .out_146(main_1_out_146), .out_150(main_1_out_150), .out_154(main_1_out_154), .out_158(main_1_out_158),
    .out_162(main_1_out_162), .out_166(main_1_out_166), .out_170(main_1_out_170), .out_174(main_1_out_174),
    .out_178(main_1_out_178), .out_182(main_1_out_182), .out_186(main_1_out_186), .out_190(main_1_out_190),
    .out_194(main_1_out_194), .out_198(main_1_out_198), .out_202(main_1_out_202), .out_206(main_1_out_206),
    .out_210(main_1_out_210), .out_214(main_1_out_214), .out_218(main_1_out_218), .out_222(main_1_out_222),
    .out_226(main_1_out_226), .out_230(main_1_out_230), .out_234(main_1_out_234), .out_238(main_1_out_238),
    .out_242(main_1_out_242), .out_246(main_1_out_246), .out_250(main_1_out_250), .out_254(main_1_out_254),
    .out_143(main_1_out_143), .out_147(main_1_out_147), .out_151(main_1_out_151), .out_155(main_1_out_155),
    .out_159(main_1_out_159), .out_163(main_1_out_163), .out_167(main_1_out_167), .out_171(main_1_out_171),
    .out_175(main_1_out_175), .out_179(main_1_out_179), .out_183(main_1_out_183), .out_187(main_1_out_187),
    .out_191(main_1_out_191), .out_195(main_1_out_195), .out_199(main_1_out_199), .out_203(main_1_out_203),
    .out_207(main_1_out_207), .out_211(main_1_out_211), .out_215(main_1_out_215), .out_219(main_1_out_219),
    .out_223(main_1_out_223), .out_227(main_1_out_227), .out_231(main_1_out_231), .out_235(main_1_out_235),
    .out_239(main_1_out_239), .out_243(main_1_out_243), .out_247(main_1_out_247), .out_251(main_1_out_251),
    .out_255(main_1_out_255), .out_259(main_1_out_259), .out_22(main_1_out_22), .out_26(main_1_out_26),
    .out_30(main_1_out_30), .out_34(main_1_out_34), .out_38(main_1_out_38), .out_42(main_1_out_42),
    .out_46(main_1_out_46), .out_50(main_1_out_50), .out_54(main_1_out_54), .out_58(main_1_out_58),
    .out_62(main_1_out_62), .out_66(main_1_out_66), .out_70(main_1_out_70), .out_74(main_1_out_74),
    .out_78(main_1_out_78), .out_82(main_1_out_82), .out_86(main_1_out_86), .out_90(main_1_out_90),
    .out_94(main_1_out_94), .out_98(main_1_out_98), .out_102(main_1_out_102), .out_106(main_1_out_106),
    .out_110(main_1_out_110), .out_114(main_1_out_114), .out_118(main_1_out_118), .out_122(main_1_out_122),
    .out_126(main_1_out_126), .out_130(main_1_out_130), .out_134(main_1_out_134), .out_23(main_1_out_23),
    .out_27(main_1_out_27), .out_31(main_1_out_31), .out_35(main_1_out_35), .out_39(main_1_out_39),
    .out_43(main_1_out_43), .out_47(main_1_out_47), .out_51(main_1_out_51), .out_55(main_1_out_55),
    .out_59(main_1_out_59), .out_63(main_1_out_63), .out_67(main_1_out_67), .out_71(main_1_out_71),
    .out_75(main_1_out_75), .out_79(main_1_out_79), .out_83(main_1_out_83), .out_87(main_1_out_87),
    .out_91(main_1_out_91), .out_95(main_1_out_95), .out_99(main_1_out_99), .out_103(main_1_out_103),
    .out_107(main_1_out_107), .out_111(main_1_out_111), .out_115(main_1_out_115), .out_119(main_1_out_119),
    .out_123(main_1_out_123), .out_127(main_1_out_127), .out_131(main_1_out_131), .out_135(main_1_out_135),
    .out_139(main_1_out_139), .out_140(main_1_out_140), .out_144(main_1_out_144), .out_148(main_1_out_148),
    .out_152(main_1_out_152), .out_156(main_1_out_156), .out_160(main_1_out_160), .out_164(main_1_out_164),
    .out_168(main_1_out_168), .out_172(main_1_out_172), .out_176(main_1_out_176), .out_180(main_1_out_180),
    .out_184(main_1_out_184), .out_188(main_1_out_188), .out_192(main_1_out_192), .out_196(main_1_out_196),
    .out_200(main_1_out_200), .out_204(main_1_out_204), .out_208(main_1_out_208), .out_212(main_1_out_212),
    .out_216(main_1_out_216), .out_220(main_1_out_220), .out_224(main_1_out_224), .out_228(main_1_out_228),
    .out_232(main_1_out_232), .out_236(main_1_out_236), .out_240(main_1_out_240), .out_244(main_1_out_244),
    .out_248(main_1_out_248), .out_252(main_1_out_252), .out_141(main_1_out_141), .out_145(main_1_out_145),
    .out_149(main_1_out_149), .out_153(main_1_out_153), .out_157(main_1_out_157), .out_161(main_1_out_161),
    .out_165(main_1_out_165), .out_169(main_1_out_169), .out_173(main_1_out_173), .out_177(main_1_out_177),
    .out_181(main_1_out_181), .out_185(main_1_out_185), .out_189(main_1_out_189), .out_193(main_1_out_193),
    .out_197(main_1_out_197), .out_201(main_1_out_201), .out_205(main_1_out_205), .out_209(main_1_out_209),
    .out_213(main_1_out_213), .out_217(main_1_out_217), .out_221(main_1_out_221), .out_225(main_1_out_225),
    .out_229(main_1_out_229), .out_233(main_1_out_233), .out_237(main_1_out_237), .out_241(main_1_out_241),
    .out_245(main_1_out_245), .out_249(main_1_out_249), .out_253(main_1_out_253), .out_257(main_1_out_257),
    .out_262(main_1_out_262), .out_266(main_1_out_266), .out_270(main_1_out_270), .out_274(main_1_out_274),
    .out_278(main_1_out_278), .out_282(main_1_out_282), .out_286(main_1_out_286), .out_290(main_1_out_290),
    .out_294(main_1_out_294), .out_298(main_1_out_298), .out_302(main_1_out_302), .out_306(main_1_out_306),
    .out_310(main_1_out_310), .out_314(main_1_out_314), .out_318(main_1_out_318), .out_322(main_1_out_322),
    .out_326(main_1_out_326), .out_330(main_1_out_330), .out_334(main_1_out_334), .out_338(main_1_out_338),
    .out_342(main_1_out_342), .out_346(main_1_out_346), .out_350(main_1_out_350), .out_354(main_1_out_354),
    .out_358(main_1_out_358), .out_362(main_1_out_362), .out_366(main_1_out_366), .out_370(main_1_out_370),
    .out_374(main_1_out_374), .out_263(main_1_out_263), .out_267(main_1_out_267), .out_271(main_1_out_271),
    .out_275(main_1_out_275), .out_279(main_1_out_279), .out_283(main_1_out_283), .out_287(main_1_out_287),
    .out_291(main_1_out_291), .out_295(main_1_out_295), .out_299(main_1_out_299), .out_303(main_1_out_303),
    .out_307(main_1_out_307), .out_311(main_1_out_311), .out_315(main_1_out_315), .out_319(main_1_out_319),
    .out_323(main_1_out_323), .out_327(main_1_out_327), .out_331(main_1_out_331), .out_335(main_1_out_335),
    .out_339(main_1_out_339), .out_343(main_1_out_343), .out_347(main_1_out_347), .out_351(main_1_out_351),
    .out_355(main_1_out_355), .out_359(main_1_out_359), .out_363(main_1_out_363), .out_367(main_1_out_367),
    .out_371(main_1_out_371), .out_375(main_1_out_375), .out_379(main_1_out_379), .out_382(main_1_out_382),
    .out_386(main_1_out_386), .out_390(main_1_out_390), .out_394(main_1_out_394), .out_398(main_1_out_398),
    .out_402(main_1_out_402), .out_406(main_1_out_406), .out_410(main_1_out_410), .out_414(main_1_out_414),
    .out_418(main_1_out_418), .out_422(main_1_out_422), .out_426(main_1_out_426), .out_430(main_1_out_430),
    .out_434(main_1_out_434), .out_438(main_1_out_438), .out_442(main_1_out_442), .out_446(main_1_out_446),
    .out_450(main_1_out_450), .out_454(main_1_out_454), .out_458(main_1_out_458), .out_462(main_1_out_462),
    .out_466(main_1_out_466), .out_470(main_1_out_470), .out_474(main_1_out_474), .out_478(main_1_out_478),
    .out_482(main_1_out_482), .out_486(main_1_out_486), .out_490(main_1_out_490), .out_494(main_1_out_494),
    .out_383(main_1_out_383), .out_387(main_1_out_387), .out_391(main_1_out_391), .out_395(main_1_out_395),
    .out_399(main_1_out_399), .out_403(main_1_out_403), .out_407(main_1_out_407), .out_411(main_1_out_411),
    .out_415(main_1_out_415), .out_419(main_1_out_419), .out_423(main_1_out_423), .out_427(main_1_out_427),
    .out_431(main_1_out_431), .out_435(main_1_out_435), .out_439(main_1_out_439), .out_443(main_1_out_443),
    .out_447(main_1_out_447), .out_451(main_1_out_451), .out_455(main_1_out_455), .out_459(main_1_out_459),
    .out_463(main_1_out_463), .out_467(main_1_out_467), .out_471(main_1_out_471), .out_475(main_1_out_475),
    .out_479(main_1_out_479), .out_483(main_1_out_483), .out_487(main_1_out_487), .out_491(main_1_out_491),
    .out_495(main_1_out_495), .out_499(main_1_out_499), .out_260(main_1_out_260), .out_264(main_1_out_264),
    .out_268(main_1_out_268), .out_272(main_1_out_272), .out_276(main_1_out_276), .out_280(main_1_out_280),
    .out_284(main_1_out_284), .out_288(main_1_out_288), .out_292(main_1_out_292), .out_296(main_1_out_296),
    .out_300(main_1_out_300), .out_304(main_1_out_304), .out_308(main_1_out_308), .out_312(main_1_out_312),
    .out_316(main_1_out_316), .out_320(main_1_out_320), .out_324(main_1_out_324), .out_328(main_1_out_328),
    .out_332(main_1_out_332), .out_336(main_1_out_336), .out_340(main_1_out_340), .out_344(main_1_out_344),
    .out_348(main_1_out_348), .out_352(main_1_out_352), .out_356(main_1_out_356), .out_360(main_1_out_360),
    .out_364(main_1_out_364), .out_368(main_1_out_368), .out_372(main_1_out_372), .out_261(main_1_out_261),
    .out_265(main_1_out_265), .out_269(main_1_out_269), .out_273(main_1_out_273), .out_277(main_1_out_277),
    .out_281(main_1_out_281), .out_285(main_1_out_285), .out_289(main_1_out_289), .out_293(main_1_out_293),
    .out_297(main_1_out_297), .out_301(main_1_out_301), .out_305(main_1_out_305), .out_309(main_1_out_309),
    .out_313(main_1_out_313), .out_317(main_1_out_317), .out_321(main_1_out_321), .out_325(main_1_out_325),
    .out_329(main_1_out_329), .out_333(main_1_out_333), .out_337(main_1_out_337), .out_341(main_1_out_341),
    .out_345(main_1_out_345), .out_349(main_1_out_349), .out_353(main_1_out_353), .out_357(main_1_out_357),
    .out_361(main_1_out_361), .out_365(main_1_out_365), .out_369(main_1_out_369), .out_373(main_1_out_373),
    .out_377(main_1_out_377), .out_380(main_1_out_380), .out_384(main_1_out_384), .out_388(main_1_out_388),
    .out_392(main_1_out_392), .out_396(main_1_out_396), .out_400(main_1_out_400), .out_404(main_1_out_404),
    .out_408(main_1_out_408), .out_412(main_1_out_412), .out_416(main_1_out_416), .out_420(main_1_out_420),
    .out_424(main_1_out_424), .out_428(main_1_out_428), .out_432(main_1_out_432), .out_436(main_1_out_436),
    .out_440(main_1_out_440), .out_444(main_1_out_444), .out_448(main_1_out_448), .out_452(main_1_out_452),
    .out_456(main_1_out_456), .out_460(main_1_out_460), .out_464(main_1_out_464), .out_468(main_1_out_468),
    .out_472(main_1_out_472), .out_476(main_1_out_476), .out_480(main_1_out_480), .out_484(main_1_out_484),
    .out_488(main_1_out_488), .out_492(main_1_out_492), .out_381(main_1_out_381), .out_385(main_1_out_385),
    .out_389(main_1_out_389), .out_393(main_1_out_393), .out_397(main_1_out_397), .out_401(main_1_out_401),
    .out_405(main_1_out_405), .out_409(main_1_out_409), .out_413(main_1_out_413), .out_417(main_1_out_417),
    .out_421(main_1_out_421), .out_425(main_1_out_425), .out_429(main_1_out_429), .out_433(main_1_out_433),
    .out_437(main_1_out_437), .out_441(main_1_out_441), .out_445(main_1_out_445), .out_449(main_1_out_449),
    .out_453(main_1_out_453), .out_457(main_1_out_457), .out_461(main_1_out_461), .out_465(main_1_out_465),
    .out_469(main_1_out_469), .out_473(main_1_out_473), .out_477(main_1_out_477), .out_481(main_1_out_481),
    .out_485(main_1_out_485), .out_489(main_1_out_489), .out_493(main_1_out_493), .out_497(main_1_out_497),
    .out_14(main_1_out_14), .out_13(main_1_out_13), .out_11(main_1_out_11), .out_10(main_1_out_10),
    .out_9(main_1_out_9), .out_8(main_1_out_8), .out_7(main_1_out_7));  // open: out_136, out_258, out_18, in_2, in_3, out_19, in_4, in_5, out_138, out_256, out_378, out_498, out_376, out_496, out_6, HUMAN, CURR, TOP1, TOP2, TOP3
  DotMatrix #(.matrixcols(30), .matrixrows(30), .persist(500)) dotmatrix_1 (
    .col0(main_1_out_132), .col1(main_1_out_128), .col2(main_1_out_124), .col3(main_1_out_120),
    .col4(main_1_out_116), .col5(main_1_out_112), .col6(main_1_out_108), .col7(main_1_out_104),
    .col8(main_1_out_100), .col9(main_1_out_96), .col10(main_1_out_92), .col11(main_1_out_88),
    .col12(main_1_out_84), .col13(main_1_out_80), .col14(main_1_out_76), .col15(main_1_out_72),
    .col16(main_1_out_68), .col17(main_1_out_64), .col18(main_1_out_60), .col19(main_1_out_56),
    .col20(main_1_out_52), .col21(main_1_out_48), .col22(main_1_out_44), .col23(main_1_out_40),
    .col24(main_1_out_36), .col25(main_1_out_32), .col26(main_1_out_28), .col27(main_1_out_24),
    .col28(main_1_out_20), .col29(main_1_out_137));
  DotMatrix #(.matrixcols(30), .matrixrows(30), .persist(500)) dotmatrix_2 (
    .col0(main_1_out_254), .col1(main_1_out_250), .col2(main_1_out_246), .col3(main_1_out_242),
    .col4(main_1_out_238), .col5(main_1_out_234), .col6(main_1_out_230), .col7(main_1_out_226),
    .col8(main_1_out_222), .col9(main_1_out_218), .col10(main_1_out_214), .col11(main_1_out_210),
    .col12(main_1_out_206), .col13(main_1_out_202), .col14(main_1_out_198), .col15(main_1_out_194),
    .col16(main_1_out_190), .col17(main_1_out_186), .col18(main_1_out_182), .col19(main_1_out_178),
    .col20(main_1_out_174), .col21(main_1_out_170), .col22(main_1_out_166), .col23(main_1_out_162),
    .col24(main_1_out_158), .col25(main_1_out_154), .col26(main_1_out_150), .col27(main_1_out_146),
    .col28(main_1_out_142), .col29(main_1_out_259));
  DotMatrix #(.matrixcols(30), .matrixrows(30), .persist(500)) dotmatrix_3 (
    .col0(main_1_out_374), .col1(main_1_out_370), .col2(main_1_out_366), .col3(main_1_out_362),
    .col4(main_1_out_358), .col5(main_1_out_354), .col6(main_1_out_350), .col7(main_1_out_346),
    .col8(main_1_out_342), .col9(main_1_out_338), .col10(main_1_out_334), .col11(main_1_out_330),
    .col12(main_1_out_326), .col13(main_1_out_322), .col14(main_1_out_318), .col15(main_1_out_314),
    .col16(main_1_out_310), .col17(main_1_out_306), .col18(main_1_out_302), .col19(main_1_out_298),
    .col20(main_1_out_294), .col21(main_1_out_290), .col22(main_1_out_286), .col23(main_1_out_282),
    .col24(main_1_out_278), .col25(main_1_out_274), .col26(main_1_out_270), .col27(main_1_out_266),
    .col28(main_1_out_262), .col29(main_1_out_379));
  DotMatrix #(.matrixcols(30), .matrixrows(30), .persist(500)) dotmatrix_4 (
    .col0(main_1_out_494), .col1(main_1_out_490), .col2(main_1_out_486), .col3(main_1_out_482),
    .col4(main_1_out_478), .col5(main_1_out_474), .col6(main_1_out_470), .col7(main_1_out_466),
    .col8(main_1_out_462), .col9(main_1_out_458), .col10(main_1_out_454), .col11(main_1_out_450),
    .col12(main_1_out_446), .col13(main_1_out_442), .col14(main_1_out_438), .col15(main_1_out_434),
    .col16(main_1_out_430), .col17(main_1_out_426), .col18(main_1_out_422), .col19(main_1_out_418),
    .col20(main_1_out_414), .col21(main_1_out_410), .col22(main_1_out_406), .col23(main_1_out_402),
    .col24(main_1_out_398), .col25(main_1_out_394), .col26(main_1_out_390), .col27(main_1_out_386),
    .col28(main_1_out_382), .col29(main_1_out_499));
  DotMatrix #(.matrixcols(30), .matrixrows(30), .persist(500)) dotmatrix_5 (
    .col0(main_1_out_133), .col1(main_1_out_129), .col2(main_1_out_125), .col3(main_1_out_121),
    .col4(main_1_out_117), .col5(main_1_out_113), .col6(main_1_out_109), .col7(main_1_out_105),
    .col8(main_1_out_101), .col9(main_1_out_97), .col10(main_1_out_93), .col11(main_1_out_89),
    .col12(main_1_out_85), .col13(main_1_out_81), .col14(main_1_out_77), .col15(main_1_out_73),
    .col16(main_1_out_69), .col17(main_1_out_65), .col18(main_1_out_61), .col19(main_1_out_57),
    .col20(main_1_out_53), .col21(main_1_out_49), .col22(main_1_out_45), .col23(main_1_out_41),
    .col24(main_1_out_37), .col25(main_1_out_33), .col26(main_1_out_29), .col27(main_1_out_25),
    .col28(main_1_out_21));  // open: col29
  DotMatrix #(.matrixcols(30), .matrixrows(30), .persist(500)) dotmatrix_6 (
    .col0(main_1_out_255), .col1(main_1_out_251), .col2(main_1_out_247), .col3(main_1_out_243),
    .col4(main_1_out_239), .col5(main_1_out_235), .col6(main_1_out_231), .col7(main_1_out_227),
    .col8(main_1_out_223), .col9(main_1_out_219), .col10(main_1_out_215), .col11(main_1_out_211),
    .col12(main_1_out_207), .col13(main_1_out_203), .col14(main_1_out_199), .col15(main_1_out_195),
    .col16(main_1_out_191), .col17(main_1_out_187), .col18(main_1_out_183), .col19(main_1_out_179),
    .col20(main_1_out_175), .col21(main_1_out_171), .col22(main_1_out_167), .col23(main_1_out_163),
    .col24(main_1_out_159), .col25(main_1_out_155), .col26(main_1_out_151), .col27(main_1_out_147),
    .col28(main_1_out_143));  // open: col29
  DotMatrix #(.matrixcols(30), .matrixrows(30), .persist(500)) dotmatrix_7 (
    .col0(main_1_out_375), .col1(main_1_out_371), .col2(main_1_out_367), .col3(main_1_out_363),
    .col4(main_1_out_359), .col5(main_1_out_355), .col6(main_1_out_351), .col7(main_1_out_347),
    .col8(main_1_out_343), .col9(main_1_out_339), .col10(main_1_out_335), .col11(main_1_out_331),
    .col12(main_1_out_327), .col13(main_1_out_323), .col14(main_1_out_319), .col15(main_1_out_315),
    .col16(main_1_out_311), .col17(main_1_out_307), .col18(main_1_out_303), .col19(main_1_out_299),
    .col20(main_1_out_295), .col21(main_1_out_291), .col22(main_1_out_287), .col23(main_1_out_283),
    .col24(main_1_out_279), .col25(main_1_out_275), .col26(main_1_out_271), .col27(main_1_out_267),
    .col28(main_1_out_263));  // open: col29
  DotMatrix #(.matrixcols(30), .matrixrows(30), .persist(500)) dotmatrix_8 (
    .col0(main_1_out_495), .col1(main_1_out_491), .col2(main_1_out_487), .col3(main_1_out_483),
    .col4(main_1_out_479), .col5(main_1_out_475), .col6(main_1_out_471), .col7(main_1_out_467),
    .col8(main_1_out_463), .col9(main_1_out_459), .col10(main_1_out_455), .col11(main_1_out_451),
    .col12(main_1_out_447), .col13(main_1_out_443), .col14(main_1_out_439), .col15(main_1_out_435),
    .col16(main_1_out_431), .col17(main_1_out_427), .col18(main_1_out_423), .col19(main_1_out_419),
    .col20(main_1_out_415), .col21(main_1_out_411), .col22(main_1_out_407), .col23(main_1_out_403),
    .col24(main_1_out_399), .col25(main_1_out_395), .col26(main_1_out_391), .col27(main_1_out_387),
    .col28(main_1_out_383));  // open: col29
  _7_Segment_Display u_7_segment_display_1 (
    .g(main_2_out_10), .f(main_2_out_11), .a(main_2_out_12), .b(main_2_out_13), .e(main_2_out_26),
    .d(main_2_out_27), .c(main_2_out_28), .dp(main_2_out_29));
  secs_to_score_main main_2 (
    .out_10(main_2_out_10), .out_11(main_2_out_11), .out_12(main_2_out_12), .out_13(main_2_out_13),
    .out_26(main_2_out_26), .out_27(main_2_out_27), .out_28(main_2_out_28), .out_29(main_2_out_29),
    .out_14(main_2_out_14), .out_15(main_2_out_15), .out_16(main_2_out_16), .out_17(main_2_out_17),
    .out_30(main_2_out_30), .out_31(main_2_out_31), .out_32(main_2_out_32), .out_33(main_2_out_33),
    .out_2(main_2_out_2), .out_3(main_2_out_3), .out_4(main_2_out_4), .out_5(main_2_out_5),
    .out_18(main_2_out_18), .out_19(main_2_out_19), .out_20(main_2_out_20), .out_21(main_2_out_21),
    .out_6(main_2_out_6), .out_7(main_2_out_7), .out_8(main_2_out_8), .out_9(main_2_out_9),
    .out_22(main_2_out_22), .out_23(main_2_out_23), .out_24(main_2_out_24), .out_25(main_2_out_25));  // open: SECS_IPT
  _7_Segment_Display u_7_segment_display_2 (
    .g(main_2_out_14), .f(main_2_out_15), .a(main_2_out_16), .b(main_2_out_17), .e(main_2_out_30),
    .d(main_2_out_31), .c(main_2_out_32), .dp(main_2_out_33));
  secs_to_score_main main_3 (
    .out_10(main_3_out_10), .out_11(main_3_out_11), .out_12(main_3_out_12), .out_13(main_3_out_13),
    .out_26(main_3_out_26), .out_27(main_3_out_27), .out_28(main_3_out_28), .out_29(main_3_out_29),
    .out_14(main_3_out_14), .out_15(main_3_out_15), .out_16(main_3_out_16), .out_17(main_3_out_17),
    .out_30(main_3_out_30), .out_31(main_3_out_31), .out_32(main_3_out_32), .out_33(main_3_out_33),
    .out_2(main_3_out_2), .out_3(main_3_out_3), .out_4(main_3_out_4), .out_5(main_3_out_5),
    .out_18(main_3_out_18), .out_19(main_3_out_19), .out_20(main_3_out_20), .out_21(main_3_out_21),
    .out_6(main_3_out_6), .out_7(main_3_out_7), .out_8(main_3_out_8), .out_9(main_3_out_9),
    .out_22(main_3_out_22), .out_23(main_3_out_23), .out_24(main_3_out_24), .out_25(main_3_out_25));  // open: SECS_IPT
  _7_Segment_Display u_7_segment_display_3 (
    .g(main_3_out_10), .f(main_3_out_11), .a(main_3_out_12), .b(main_3_out_13), .e(main_3_out_26),
    .d(main_3_out_27), .c(main_3_out_28), .dp(main_3_out_29));
  _7_Segment_Display u_7_segment_display_4 (
    .g(main_3_out_14), .f(main_3_out_15), .a(main_3_out_16), .b(main_3_out_17), .e(main_3_out_30),
    .d(main_3_out_31), .c(main_3_out_32), .dp(main_3_out_33));
  secs_to_score_main main_4 (
    .out_10(main_4_out_10), .out_11(main_4_out_11), .out_12(main_4_out_12), .out_13(main_4_out_13),
    .out_26(main_4_out_26), .out_27(main_4_out_27), .out_28(main_4_out_28), .out_29(main_4_out_29),
    .out_14(main_4_out_14), .out_15(main_4_out_15), .out_16(main_4_out_16), .out_17(main_4_out_17),
    .out_30(main_4_out_30), .out_31(main_4_out_31), .out_32(main_4_out_32), .out_33(main_4_out_33),
    .out_2(main_4_out_2), .out_3(main_4_out_3), .out_4(main_4_out_4), .out_5(main_4_out_5),
    .out_18(main_4_out_18), .out_19(main_4_out_19), .out_20(main_4_out_20), .out_21(main_4_out_21),
    .out_6(main_4_out_6), .out_7(main_4_out_7), .out_8(main_4_out_8), .out_9(main_4_out_9),
    .out_22(main_4_out_22), .out_23(main_4_out_23), .out_24(main_4_out_24), .out_25(main_4_out_25));  // open: SECS_IPT
  _7_Segment_Display u_7_segment_display_5 (
    .g(main_4_out_10), .f(main_4_out_11), .a(main_4_out_12), .b(main_4_out_13), .e(main_4_out_26),
    .d(main_4_out_27), .c(main_4_out_28), .dp(main_4_out_29));
  _7_Segment_Display u_7_segment_display_6 (
    .g(main_4_out_14), .f(main_4_out_15), .a(main_4_out_16), .b(main_4_out_17), .e(main_4_out_30),
    .d(main_4_out_31), .c(main_4_out_32), .dp(main_4_out_33));
  _7_Segment_Display u_7_segment_display_7 (
    .g(main_5_out_14), .f(main_5_out_15), .a(main_5_out_16), .b(main_5_out_17), .e(main_5_out_30),
    .d(main_5_out_31), .c(main_5_out_32), .dp(main_5_out_33));
  _7_Segment_Display u_7_segment_display_8 (
    .g(main_5_out_10), .f(main_5_out_11), .a(main_5_out_12), .b(main_5_out_13), .e(main_5_out_26),
    .d(main_5_out_27), .c(main_5_out_28), .dp(main_5_out_29));
  secs_to_score_main main_5 (
    .out_10(main_5_out_10), .out_11(main_5_out_11), .out_12(main_5_out_12), .out_13(main_5_out_13),
    .out_26(main_5_out_26), .out_27(main_5_out_27), .out_28(main_5_out_28), .out_29(main_5_out_29),
    .out_14(main_5_out_14), .out_15(main_5_out_15), .out_16(main_5_out_16), .out_17(main_5_out_17),
    .out_30(main_5_out_30), .out_31(main_5_out_31), .out_32(main_5_out_32), .out_33(main_5_out_33),
    .out_2(main_5_out_2), .out_3(main_5_out_3), .out_4(main_5_out_4), .out_5(main_5_out_5),
    .out_18(main_5_out_18), .out_19(main_5_out_19), .out_20(main_5_out_20), .out_21(main_5_out_21),
    .out_6(main_5_out_6), .out_7(main_5_out_7), .out_8(main_5_out_8), .out_9(main_5_out_9),
    .out_22(main_5_out_22), .out_23(main_5_out_23), .out_24(main_5_out_24), .out_25(main_5_out_25));  // open: SECS_IPT
  DotMatrix #(.matrixcols(8), .matrixrows(5)) dotmatrix_9 (
    .col0(main_1_out_7), .col1(main_1_out_8), .col2(main_1_out_9), .col3(main_1_out_10),
    .col4(main_1_out_11), .col5(main_1_out_13), .col6(main_1_out_14));  // open: col7
  _7_Segment_Display u_7_segment_display_9 (
    .g(main_2_out_6), .f(main_2_out_7), .a(main_2_out_8), .b(main_2_out_9), .e(main_2_out_22),
    .d(main_2_out_23), .c(main_2_out_24), .dp(main_2_out_25));
  _7_Segment_Display u_7_segment_display_10 (
    .g(main_2_out_2), .f(main_2_out_3), .a(main_2_out_4), .b(main_2_out_5), .e(main_2_out_18),
    .d(main_2_out_19), .c(main_2_out_20), .dp(main_2_out_21));
  _7_Segment_Display u_7_segment_display_11 (
    .g(main_3_out_2), .f(main_3_out_3), .a(main_3_out_4), .b(main_3_out_5), .e(main_3_out_18),
    .d(main_3_out_19), .c(main_3_out_20), .dp(main_3_out_21));
  _7_Segment_Display u_7_segment_display_12 (
    .g(main_3_out_6), .f(main_3_out_7), .a(main_3_out_8), .b(main_3_out_9), .e(main_3_out_22),
    .d(main_3_out_23), .c(main_3_out_24), .dp(main_3_out_25));
  _7_Segment_Display u_7_segment_display_13 (
    .g(main_4_out_2), .f(main_4_out_3), .a(main_4_out_4), .b(main_4_out_5), .e(main_4_out_18),
    .d(main_4_out_19), .c(main_4_out_20), .dp(main_4_out_21));
  _7_Segment_Display u_7_segment_display_14 (
    .g(main_4_out_6), .f(main_4_out_7), .a(main_4_out_8), .b(main_4_out_9), .e(main_4_out_22),
    .d(main_4_out_23), .c(main_4_out_24), .dp(main_4_out_25));
  _7_Segment_Display u_7_segment_display_15 (
    .g(main_5_out_6), .f(main_5_out_7), .a(main_5_out_8), .b(main_5_out_9), .e(main_5_out_22),
    .d(main_5_out_23), .c(main_5_out_24), .dp(main_5_out_25));
  _7_Segment_Display u_7_segment_display_16 (
    .g(main_5_out_2), .f(main_5_out_3), .a(main_5_out_4), .b(main_5_out_5), .e(main_5_out_18),
    .d(main_5_out_19), .c(main_5_out_20), .dp(main_5_out_21));
  DotMatrix #(.matrixcols(30), .matrixrows(30), .persist(500)) dotmatrix_10 (
    .col0(main_1_out_134), .col1(main_1_out_130), .col2(main_1_out_126), .col3(main_1_out_122),
    .col4(main_1_out_118), .col5(main_1_out_114), .col6(main_1_out_110), .col7(main_1_out_106),
    .col8(main_1_out_102), .col9(main_1_out_98), .col10(main_1_out_94), .col11(main_1_out_90),
    .col12(main_1_out_86), .col13(main_1_out_82), .col14(main_1_out_78), .col15(main_1_out_74),
    .col16(main_1_out_70), .col17(main_1_out_66), .col18(main_1_out_62), .col19(main_1_out_58),
    .col20(main_1_out_54), .col21(main_1_out_50), .col22(main_1_out_46), .col23(main_1_out_42),
    .col24(main_1_out_38), .col25(main_1_out_34), .col26(main_1_out_30), .col27(main_1_out_26),
    .col28(main_1_out_22), .col29(main_1_out_139));
  DotMatrix #(.matrixcols(30), .matrixrows(30), .persist(500)) dotmatrix_11 (
    .col0(main_1_out_252), .col1(main_1_out_248), .col2(main_1_out_244), .col3(main_1_out_240),
    .col4(main_1_out_236), .col5(main_1_out_232), .col6(main_1_out_228), .col7(main_1_out_224),
    .col8(main_1_out_220), .col9(main_1_out_216), .col10(main_1_out_212), .col11(main_1_out_208),
    .col12(main_1_out_204), .col13(main_1_out_200), .col14(main_1_out_196), .col15(main_1_out_192),
    .col16(main_1_out_188), .col17(main_1_out_184), .col18(main_1_out_180), .col19(main_1_out_176),
    .col20(main_1_out_172), .col21(main_1_out_168), .col22(main_1_out_164), .col23(main_1_out_160),
    .col24(main_1_out_156), .col25(main_1_out_152), .col26(main_1_out_148), .col27(main_1_out_144),
    .col28(main_1_out_140), .col29(main_1_out_257));
  DotMatrix #(.matrixcols(30), .matrixrows(30), .persist(500)) dotmatrix_12 (
    .col0(main_1_out_372), .col1(main_1_out_368), .col2(main_1_out_364), .col3(main_1_out_360),
    .col4(main_1_out_356), .col5(main_1_out_352), .col6(main_1_out_348), .col7(main_1_out_344),
    .col8(main_1_out_340), .col9(main_1_out_336), .col10(main_1_out_332), .col11(main_1_out_328),
    .col12(main_1_out_324), .col13(main_1_out_320), .col14(main_1_out_316), .col15(main_1_out_312),
    .col16(main_1_out_308), .col17(main_1_out_304), .col18(main_1_out_300), .col19(main_1_out_296),
    .col20(main_1_out_292), .col21(main_1_out_288), .col22(main_1_out_284), .col23(main_1_out_280),
    .col24(main_1_out_276), .col25(main_1_out_272), .col26(main_1_out_268), .col27(main_1_out_264),
    .col28(main_1_out_260), .col29(main_1_out_261));
  DotMatrix #(.matrixcols(30), .matrixrows(30), .persist(500)) dotmatrix_13 (
    .col0(main_1_out_492), .col1(main_1_out_488), .col2(main_1_out_484), .col3(main_1_out_480),
    .col4(main_1_out_476), .col5(main_1_out_472), .col6(main_1_out_468), .col7(main_1_out_464),
    .col8(main_1_out_460), .col9(main_1_out_456), .col10(main_1_out_452), .col11(main_1_out_448),
    .col12(main_1_out_444), .col13(main_1_out_440), .col14(main_1_out_436), .col15(main_1_out_432),
    .col16(main_1_out_428), .col17(main_1_out_424), .col18(main_1_out_420), .col19(main_1_out_416),
    .col20(main_1_out_412), .col21(main_1_out_408), .col22(main_1_out_404), .col23(main_1_out_400),
    .col24(main_1_out_396), .col25(main_1_out_392), .col26(main_1_out_388), .col27(main_1_out_384),
    .col28(main_1_out_380), .col29(main_1_out_493));
  DotMatrix #(.matrixcols(30), .matrixrows(30), .persist(500)) dotmatrix_14 (
    .col0(main_1_out_135), .col1(main_1_out_131), .col2(main_1_out_127), .col3(main_1_out_123),
    .col4(main_1_out_119), .col5(main_1_out_115), .col6(main_1_out_111), .col7(main_1_out_107),
    .col8(main_1_out_103), .col9(main_1_out_99), .col10(main_1_out_95), .col11(main_1_out_91),
    .col12(main_1_out_87), .col13(main_1_out_83), .col14(main_1_out_79), .col15(main_1_out_75),
    .col16(main_1_out_71), .col17(main_1_out_67), .col18(main_1_out_63), .col19(main_1_out_59),
    .col20(main_1_out_55), .col21(main_1_out_51), .col22(main_1_out_47), .col23(main_1_out_43),
    .col24(main_1_out_39), .col25(main_1_out_35), .col26(main_1_out_31), .col27(main_1_out_27),
    .col28(main_1_out_23));  // open: col29
  DotMatrix #(.matrixcols(30), .matrixrows(30), .persist(500)) dotmatrix_15 (
    .col0(main_1_out_253), .col1(main_1_out_249), .col2(main_1_out_245), .col3(main_1_out_241),
    .col4(main_1_out_237), .col5(main_1_out_233), .col6(main_1_out_229), .col7(main_1_out_225),
    .col8(main_1_out_221), .col9(main_1_out_217), .col10(main_1_out_213), .col11(main_1_out_209),
    .col12(main_1_out_205), .col13(main_1_out_201), .col14(main_1_out_197), .col15(main_1_out_193),
    .col16(main_1_out_189), .col17(main_1_out_185), .col18(main_1_out_181), .col19(main_1_out_177),
    .col20(main_1_out_173), .col21(main_1_out_169), .col22(main_1_out_165), .col23(main_1_out_161),
    .col24(main_1_out_157), .col25(main_1_out_153), .col26(main_1_out_149), .col27(main_1_out_145),
    .col28(main_1_out_141));  // open: col29
  DotMatrix #(.matrixcols(30), .matrixrows(30), .persist(500)) dotmatrix_16 (
    .col0(main_1_out_377), .col1(main_1_out_373), .col2(main_1_out_369), .col3(main_1_out_365),
    .col4(main_1_out_361), .col5(main_1_out_357), .col6(main_1_out_353), .col7(main_1_out_349),
    .col8(main_1_out_345), .col9(main_1_out_341), .col10(main_1_out_337), .col11(main_1_out_333),
    .col12(main_1_out_329), .col13(main_1_out_325), .col14(main_1_out_321), .col15(main_1_out_317),
    .col16(main_1_out_313), .col17(main_1_out_309), .col18(main_1_out_305), .col19(main_1_out_301),
    .col20(main_1_out_297), .col21(main_1_out_293), .col22(main_1_out_289), .col23(main_1_out_285),
    .col24(main_1_out_281), .col25(main_1_out_277), .col26(main_1_out_273), .col27(main_1_out_269),
    .col28(main_1_out_265));  // open: col29
  DotMatrix #(.matrixcols(30), .matrixrows(30), .persist(500)) dotmatrix_17 (
    .col0(main_1_out_497), .col1(main_1_out_489), .col2(main_1_out_485), .col3(main_1_out_481),
    .col4(main_1_out_477), .col5(main_1_out_473), .col6(main_1_out_469), .col7(main_1_out_465),
    .col8(main_1_out_461), .col9(main_1_out_457), .col10(main_1_out_453), .col11(main_1_out_449),
    .col12(main_1_out_445), .col13(main_1_out_441), .col14(main_1_out_437), .col15(main_1_out_433),
    .col16(main_1_out_429), .col17(main_1_out_425), .col18(main_1_out_421), .col19(main_1_out_417),
    .col20(main_1_out_413), .col21(main_1_out_409), .col22(main_1_out_405), .col23(main_1_out_401),
    .col24(main_1_out_397), .col25(main_1_out_393), .col26(main_1_out_389), .col27(main_1_out_385),
    .col28(main_1_out_381));  // open: col29
  Button button_1 ();  // open: out
  Keyboard keyboard_1 ();  // open: clk, re, clr, avail, data
  Keyboard keyboard_2 ();  // open: clk, re, clr, avail, data

  // Notes on the sheet:
  //   JAK GRAĆ?
  //   Sterowanie kursorem
  //   A - ruch w lewo
  //   W - ruch w górę
  //   S - ruch w dół
  //   D - ruch w prawo
  //   R - obrót statku
  //   ENTER - przycisk potwierdzający dodanie statku / sprawdzenie pozycji
  //   Gra automatycznie rozpoczyna się.
  //   Po zakończeniu gry, gdy "GAME TIME" pokazuje 00:00,
  //    aby uruchomić kolejną grę, należy przycisnąć przycisk "RESET".
  //   Aby uruchomić grę przeciwko komputerowi, należy ustawić logiczne 1 na wejściu "BOT?".
  //   Zmiana tego wejścia w trakcie gry powoduje jedynie to, że bot
  //    przestaje wykonywać ruchy - grę może kontynuować inny gracz.
  //   USTAWIENIA:
  //   Częstotliwość zegara: 4.1k Hz.
  //   W celu prawidłowego wyświetlania czasu rozgrywki, w module
  //   "timer.circ" należy ustawić odpowiednią wartość maksymalną countera odpowiadającą
  //   częstotliwości zegara pokazaną w aplikacji (prawy górny róg).
  //   W przypadku, gdy kliknięcie w klawiaturę/przyciski okazuje się trudne, przez
  //   automatyczne wybieranie całego modułu "app.circ" przez symulator,
  //   należy "pociągnąć" połączenia do odpowiednich elementów IO, znajdujących się poza układem.
  //   Przed grą należy odpowiednio oddalić ekran tak, aby wszystkie pola były widoczne.
endmodule
