// Logisim project map_generator.circ as structural Verilog: 1 circuit, main circuit main
module main (
  input  in_1,
  input  BOOT_PHASE,
  input  CLK,
  input  [3:0] SHIPS_NUMBER,
  output [3:0] out_5,
  output [3:0] out_6,
  output ROTATED,
  output out_8,
  output out_9
);

  wire and_1_out, comparator_1_eq, comparator_1_gt, demultiplexer_1_out0, demultiplexer_1_out1,
       demultiplexer_1_out2, POSITION_CLOCK, random_1_out, ROTATION_CLOCK;
  wire [3:0] main_1_output, main_2_output;
  wire [4:0] counter_1_q;

  and and_1 (and_1_out, BOOT_PHASE, CLK);
  Comparator #(.width(4), .mode("unsigned")) comparator_1 (
    .a(SHIPS_NUMBER), .b(4'b1010), .gt(comparator_1_gt), .eq(comparator_1_eq));  // open: lt
  or or_1 (out_9, comparator_1_gt, comparator_1_eq);
  Demultiplexer #(.select(5)) demultiplexer_1 (
    .out0(demultiplexer_1_out0), .out1(demultiplexer_1_out1), .out2(demultiplexer_1_out2), .in(1'b1),
    .sel(counter_1_q));  // open: out3, out4, out5, out6, out7, out8, out9, out10, out11, out12, out13, out14, out15, out16, out17, out18, out19, out20, out21, out22, out23, out24, out25, out26, out27, out28, out29, out30, out31, en
  Counter #(.width(5), .max('h1f)) counter_1 (
    .Q(counter_1_q), .clk(and_1_out), .clr(in_1));  // open: load, D, count, carry
  assign ROTATION_CLOCK = BOOT_PHASE ? demultiplexer_1_out0 : 1'bz;  // Controlled_Buffer controlled_buffer_1
  assign POSITION_CLOCK = BOOT_PHASE ? demultiplexer_1_out1 : 1'bz;  // Controlled_Buffer controlled_buffer_2
  assign out_8 = BOOT_PHASE ? demultiplexer_1_out2 : 1'bz;  // Controlled_Buffer controlled_buffer_3
  Pull_Resistor pull_resistor_1 (.node(ROTATION_CLOCK));
  Random #(.width(1)) random_1 (.clk(ROTATION_CLOCK), .next(ROTATION_CLOCK), .out(random_1_out));  // open: clr
  Pull_Resistor pull_resistor_2 (.node(POSITION_CLOCK));
  Counter #(.width(1), .max('h1)) counter_2 (
    .Q(ROTATED), .clk(random_1_out), .clr(in_1));  // open: load, D, count, carry
  random_num_generator_A_main main_1 (.GENERATE(POSITION_CLOCK), .OUTPUT(main_1_output));
  assign out_5 = BOOT_PHASE ? main_1_output : 4'bz;  // Controlled_Buffer controlled_buffer_4
  random_num_generator_B_main main_2 (.GENERATE(POSITION_CLOCK), .OUTPUT(main_2_output));
  assign out_6 = BOOT_PHASE ? main_2_output : 4'bz;  // Controlled_Buffer controlled_buffer_5

  // Other names for the same wires on the sheet: _10SHIPS = out_9; CLR = in_1; CONFIRM_CLOCK = out_8;
  //   SHIP_NUMBER[3:0] = SHIPS_NUMBER
endmodule
