// Logisim project memory_management.circ as structural Verilog: 1 circuit, main circuit main
// 2
module main (
  input  [3:0] X,
  input  in_2,
  input  [3:0] Y,
  input  ROTATED,
  input  CLK,
  input  SHOW_NEXT_SHIP,
  input  CONFIRM,
  input  [3:0] CHECK_X,
  input  [3:0] CHECK_Y,
  input  CHECK,
  input  SINK_IF_HIT,
  output [3:0] CURR_SHIP_ADD,
  output WIN,
  output HIT,
  output CHECKING,
  output [14:0] RAM_OUT,
  output ALREADY_HIT
);

  wire _0HIT, _0HIT_t, _1HIT, _1HIT_t, _2HIT, _2HIT_t, _3HIT, _3HIT_t, ALIVE0, ALIVE1, ALIVE2, ALIVE3,
       and_1_out, and_2_out, and_3_out, and_4_out, and_5_out, and_6_out, and_7_out, and_13_out, and_14_out,
       and_15_out, and_16_out, and_17_out, and_18_out, and_23_out, and_24_out, and_25_out, and_26_out,
       and_27_out, and_28_out, and_29_out, and_30_out, and_31_out, and_32_out, and_33_out, and_34_out,
       and_35_out, and_36_out, and_37_out, CHECK_FRAME_END, CHECK_OCCUPIED_RST, CHECK_t, CLK_t, COLL_CHECK,
       comparator_1_eq, comparator_2_eq, comparator_3_eq, comparator_4_eq, comparator_5_eq, comparator_6_eq,
       comparator_7_eq, comparator_8_eq, comparator_9_eq, comparator_10_eq, comparator_11_eq,
       comparator_12_eq, comparator_13_eq, comparator_14_eq, comparator_15_eq, comparator_16_eq,
       comparator_18_lt, comparator_19_eq, comparator_20_eq, comparator_21_eq, CONFIRM_t, counter_5_carry,
       d_ff_9_q, HORI_HIT, main_1_out_of_range, main_2_p3, main_4_p5, main_4_p6, main_5_p5, main_6_colliding,
       MEM_NOT_CHANGING, multiplexer_2_out, multiplexer_3_out, multiplexer_4_out, multiplexer_5_out,
       multiplexer_6_out, not_1_out, not_2_out, not_3_out, not_4_out, not_5_out, not_6_out, not_7_out,
       not_8_out, not_9_out, or_1_out, or_2_out, or_3_out, or_4_out, or_5_out, or_6_out, or_7_out, or_8_out,
       or_9_out, or_10_out, OVERWRITE, ROTATED_CHECK, SAVE, SAVE_CURR_RAM_STATE, VERT_HIT;
  wire [1:0] counter_5_q, SHIP_TYPE, TYPE_CHECK;
  wire [2:0] counter_2_q;
  wire [3:0] adder_1_out, adder_2_out, adder_3_out, adder_4_out, adder_5_out, adder_6_out, and_8_out,
       controlled_buffer_11_out, controlled_buffer_13_out, CURR_SHIP_CHECK, CURR_SHIP_COLL,
       CURRENT_SHIP_SHOW, MEM_SELECT, multiplexer_1_out;
  wire [4:0] hits_counter_q;
  wire [7:0] HORI_CHECK, register_1_q, VERT_CHECK;
  wire [14:0] RAM_OUT_t, SHIP_DATA;

  Clock clock_1 (.out(CLK_t));
  Multiplexer #(.select(2), .width(4), .enable("false")) multiplexer_1 (
    .in0(4'b0001), .in1(4'b0011), .in2(4'b0111), .in3(4'b1111), .out(multiplexer_1_out), .sel(SHIP_TYPE));
  assign RAM_OUT_t = SAVE ? SHIP_DATA : 15'bz;  // Controlled_Buffer controlled_buffer_1
  not not_1 (not_1_out, SAVE);
  D_Flip_Flop d_ff_1 (.clk(CHECK), .D(CHECK), .Q(CHECK_t), .reset(CHECK_t));  // open: Qn, preset, en
  Register #(.width(15)) register_1 (
    .D(RAM_OUT_t), .Q({ALIVE3, ALIVE2, ALIVE1, ALIVE0, ROTATED_CHECK, TYPE_CHECK, register_1_q}),
    .clk(SAVE_CURR_RAM_STATE));  // open: en, clr
  Comparator #(.width(2), .mode("unsigned")) comparator_1 (
    .a(TYPE_CHECK), .b(2'b00), .eq(comparator_1_eq));  // open: gt, lt
  Comparator #(.width(2), .mode("unsigned")) comparator_2 (
    .a(TYPE_CHECK), .b(2'b01), .eq(comparator_2_eq));  // open: gt, lt
  Comparator #(.width(2), .mode("unsigned")) comparator_3 (
    .a(TYPE_CHECK), .b(2'b10), .eq(comparator_3_eq));  // open: gt, lt
  Comparator #(.width(2), .mode("unsigned")) comparator_4 (
    .a(TYPE_CHECK), .b(2'b11), .eq(comparator_4_eq));  // open: gt, lt
  and and_1 (and_1_out, ~ALIVE0, _0HIT_t);  // AND_Gate
  and and_2 (and_2_out, ~ALIVE1, _1HIT_t);  // AND_Gate
  and and_3 (and_3_out, ~ALIVE2, _2HIT_t);  // AND_Gate
  and and_4 (and_4_out, ~ALIVE3, _3HIT_t);  // AND_Gate
  // Probe on RAM_OUT_t
  RAM #(.addrWidth(4), .dataWidth(15)) ram_1 (
    .addr(MEM_SELECT), .data(RAM_OUT_t), .clk(CLK_t), .ld(not_1_out), .clr(in_2));  // open: sel
  Demultiplexer #(.width(8), .enable("false")) demultiplexer_1 (
    .out0(HORI_CHECK), .out1(VERT_CHECK), .in(register_1_q), .sel(ROTATED_CHECK));
  and and_5 (and_5_out, HORI_HIT, ~ROTATED_CHECK);  // AND_Gate
  or or_1 (or_1_out, and_5_out, and_6_out);
  and and_6 (and_6_out, ROTATED_CHECK, VERT_HIT);
  and and_7 (and_7_out, comparator_1_eq, and_1_out);
  or or_2 (or_2_out, and_1_out, and_2_out);
  and and_8 (and_8_out[0], ALIVE0, ~_0HIT);  // AND_Gate
  and and_9 (and_8_out[1], ALIVE1, ~_1HIT);  // AND_Gate
  and and_10 (and_8_out[2], ALIVE2, ~_2HIT);  // AND_Gate
  and and_11 (and_8_out[3], ALIVE3, ~_3HIT);  // AND_Gate
  and and_12 (OVERWRITE, SINK_IF_HIT, or_1_out);
  and and_13 (and_13_out, comparator_2_eq, or_2_out);
  and and_14 (and_14_out, comparator_3_eq, or_3_out);
  or or_3 (or_3_out, or_2_out, and_3_out);
  or or_4 (or_4_out, or_3_out, and_4_out);
  assign SHIP_DATA = not_2_out ? {multiplexer_1_out, ROTATED, SHIP_TYPE, Y, X} : 15'bz;  // Controlled_Buffer controlled_buffer_2
  not not_2 (not_2_out, CHECKING);
  assign SHIP_DATA = CHECKING ? {and_8_out, ROTATED_CHECK, TYPE_CHECK, register_1_q} : 15'bz;  // Controlled_Buffer controlled_buffer_3
  and and_15 (and_15_out, comparator_4_eq, or_4_out);
  not not_3 (not_3_out, CHECKING);
  assign RAM_OUT = not_3_out ? RAM_OUT_t : 15'bz;  // Controlled_Buffer controlled_buffer_4
  D_Flip_Flop d_ff_2 (.clk(CHECK_t), .D(CHECK_t), .Q(CHECKING), .reset(CHECK_OCCUPIED_RST));  // open: Qn, preset, en
  and and_16 (and_16_out, MEM_NOT_CHANGING, or_5_out);
  or or_5 (or_5_out, and_7_out, and_13_out, and_14_out, and_15_out);
  ship_out_of_map_main main_1 (.SHIP_DATA_A(SHIP_DATA), .out_of_range(main_1_out_of_range));
  D_Flip_Flop d_ff_3 (.clk(and_16_out), .D(and_16_out), .Q(ALREADY_HIT), .reset(or_6_out));  // open: Qn, preset, en
  or or_6 (or_6_out, CHECK_t, in_2);
  Comparator #(.width(4), .mode("unsigned")) comparator_5 (
    .a(CHECK_X), .b(VERT_CHECK[3:0]), .eq(comparator_5_eq));  // open: gt, lt
  Adder #(.width(4)) adder_1 (.a(VERT_CHECK[7:4]), .b(4'b0001), .out(adder_1_out));  // open: cin, cout
  Adder #(.width(4)) adder_2 (.a(VERT_CHECK[7:4]), .b(4'b0010), .out(adder_2_out));  // open: cin, cout
  Adder #(.width(4)) adder_3 (.a(VERT_CHECK[7:4]), .b(4'b0011), .out(adder_3_out));  // open: cin, cout
  Comparator #(.width(4), .mode("unsigned")) comparator_6 (
    .a(CHECK_Y), .b(HORI_CHECK[7:4]), .eq(comparator_6_eq));  // open: gt, lt
  Adder #(.width(4)) adder_4 (.a(HORI_CHECK[3:0]), .b(4'b0001), .out(adder_4_out));  // open: cin, cout
  Adder #(.width(4)) adder_5 (.a(HORI_CHECK[3:0]), .b(4'b0010), .out(adder_5_out));  // open: cin, cout
  Adder #(.width(4)) adder_6 (.a(HORI_CHECK[3:0]), .b(4'b0011), .out(adder_6_out));  // open: cin, cout
  Counter #(.width(4), .max('hf), .trigger("falling")) counter_1 (
    .Q(CURR_SHIP_ADD), .clk(and_17_out), .clr(in_2));  // open: load, D, count, carry
  and and_17 (and_17_out, ~main_1_out_of_range, CONFIRM_t);  // AND_Gate
  not not_4 (not_4_out, CHECKING);
  Comparator #(.width(4), .mode("unsigned")) comparator_7 (
    .a(CHECK_Y), .b(VERT_CHECK[7:4]), .eq(comparator_7_eq));  // open: gt, lt
  Comparator #(.width(4), .mode("unsigned")) comparator_8 (
    .a(CHECK_Y), .b(adder_1_out), .eq(comparator_8_eq));  // open: gt, lt
  Comparator #(.width(4), .mode("unsigned")) comparator_9 (
    .a(CHECK_Y), .b(adder_2_out), .eq(comparator_9_eq));  // open: gt, lt
  Comparator #(.width(4), .mode("unsigned")) comparator_10 (
    .a(CHECK_Y), .b(adder_3_out), .eq(comparator_10_eq));  // open: gt, lt
  Multiplexer #(.enable("false")) multiplexer_2 (
    .in0(comparator_5_eq), .in1(comparator_6_eq), .out(multiplexer_2_out), .sel(not_5_out));
  not not_5 (not_5_out, ROTATED_CHECK);
  Comparator #(.width(4), .mode("unsigned")) comparator_11 (
    .a(CHECK_X), .b(HORI_CHECK[3:0]), .eq(comparator_11_eq));  // open: gt, lt
  Comparator #(.width(4), .mode("unsigned")) comparator_12 (
    .a(CHECK_X), .b(adder_4_out), .eq(comparator_12_eq));  // open: gt, lt
  Comparator #(.width(4), .mode("unsigned")) comparator_13 (
    .a(CHECK_X), .b(adder_5_out), .eq(comparator_13_eq));  // open: gt, lt
  Comparator #(.width(4), .mode("unsigned")) comparator_14 (
    .a(CHECK_X), .b(adder_6_out), .eq(comparator_14_eq));  // open: gt, lt
  assign SAVE = not_4_out ? and_17_out : 1'bz;  // Controlled_Buffer controlled_buffer_5
  assign SAVE = CHECKING ? OVERWRITE : 1'bz;  // Controlled_Buffer controlled_buffer_6
  Multiplexer #(.enable("false")) multiplexer_3 (
    .in0(comparator_7_eq), .in1(comparator_11_eq), .out(multiplexer_3_out), .sel(not_5_out));
  Multiplexer #(.enable("false")) multiplexer_4 (
    .in0(comparator_8_eq), .in1(comparator_12_eq), .out(multiplexer_4_out), .sel(not_5_out));
  Multiplexer #(.enable("false")) multiplexer_5 (
    .in0(comparator_9_eq), .in1(comparator_13_eq), .out(multiplexer_5_out), .sel(not_5_out));
  // _4bit_greater_or_equal_than_and_less_than__main main_2: pin names not known; wires that end beside it: CURR_SHIP_ADD, 4'b0000, main_2_p3
  // _4bit_greater_or_equal_than_and_less_than__main main_3: pin names not known; wires that end beside it: 4'b0100, CURR_SHIP_ADD
  // _4bit_greater_or_equal_than_and_less_than__main main_4: pin names not known; wires that end beside it: 4'b0100, 4'b0111, CURR_SHIP_ADD, 4'b0111, main_4_p5, main_4_p6
  // _4bit_greater_or_equal_than_and_less_than__main main_5: pin names not known; wires that end beside it: 4'b1001, CURR_SHIP_ADD, 4'b1001, 4'b1010, main_5_p5
  Multiplexer #(.enable("false")) multiplexer_6 (
    .in0(comparator_10_eq), .in1(comparator_14_eq), .out(multiplexer_6_out), .sel(not_5_out));
  Counter #(.width(3), .max('h6), .trigger("falling")) counter_2 (
    .Q(counter_2_q), .carry(CHECK_FRAME_END), .clk(and_18_out));  // open: load, D, count, clr
  and and_18 (and_18_out, CLK_t, CHECKING);
  and and_19 (_0HIT_t, multiplexer_2_out, multiplexer_3_out);
  and and_20 (_1HIT_t, multiplexer_2_out, multiplexer_4_out);
  and and_21 (_2HIT_t, multiplexer_2_out, multiplexer_5_out);
  and and_22 (_3HIT_t, multiplexer_2_out, multiplexer_6_out);
  Pull_Resistor pull_resistor_1 (.node(SHIP_TYPE));
  assign SHIP_TYPE = main_2_p3 ? 2'b00 : 2'bz;  // Controlled_Buffer controlled_buffer_7
  Pull_Resistor pull_resistor_2 (.node(SHIP_TYPE));
  assign SHIP_TYPE = main_4_p5 ? 2'b01 : 2'bz;  // Controlled_Buffer controlled_buffer_8
  Pull_Resistor pull_resistor_3 (.node(SHIP_TYPE));
  assign SHIP_TYPE = main_4_p6 ? 2'b10 : 2'bz;  // Controlled_Buffer controlled_buffer_9
  Pull_Resistor pull_resistor_4 (.node(SHIP_TYPE));
  assign SHIP_TYPE = main_5_p5 ? 2'b11 : 2'bz;  // Controlled_Buffer controlled_buffer_10
  Counter #(.width(4), .max('ha), .trigger("falling")) counter_3 (
    .Q(CURR_SHIP_CHECK), .carry(CHECK_OCCUPIED_RST), .clk(CHECK_FRAME_END), .clr(CHECK_OCCUPIED_RST));  // open: load, D, count
  Comparator #(.width(3), .mode("unsigned")) comparator_15 (
    .a(counter_2_q), .b(3'b001), .eq(comparator_15_eq));  // open: gt, lt
  D_Flip_Flop d_ff_4 (
    .clk(comparator_15_eq), .D(comparator_15_eq), .Q(SAVE_CURR_RAM_STATE), .reset(comparator_16_eq));  // open: Qn, preset, en
  Comparator #(.width(3), .mode("unsigned")) comparator_16 (
    .a(counter_2_q), .b(3'b010), .gt(MEM_NOT_CHANGING), .eq(comparator_16_eq));  // open: lt
  and and_23 (and_23_out, comparator_7_eq, ALIVE0);
  and and_24 (and_24_out, comparator_8_eq, ALIVE1);
  and and_25 (and_25_out, comparator_9_eq, ALIVE2);
  and and_26 (and_26_out, comparator_10_eq, ALIVE3);
  not not_6 (not_6_out, ROTATED_CHECK);
  and and_27 (and_27_out, comparator_11_eq, ALIVE0);
  and and_28 (and_28_out, comparator_12_eq, ALIVE1);
  and and_29 (and_29_out, comparator_13_eq, ALIVE2);
  and and_30 (and_30_out, comparator_14_eq, ALIVE3);
  Counter #(.width(5), .max('h1f)) hits_counter (
    .Q(hits_counter_q), .clk(OVERWRITE), .clr(in_2));  // open: load, D, count, carry
  D_Flip_Flop d_ff_5 (.clk(OVERWRITE), .D(OVERWRITE), .Q(HIT), .reset(or_7_out));  // open: Qn, preset, en
  or or_7 (or_7_out, CHECK_t, in_2);
  Multiplexer #(.enable("false")) multiplexer_7 (.in0(and_23_out), .in1(and_27_out), .out(_0HIT), .sel(not_6_out));
  Multiplexer #(.enable("false")) multiplexer_8 (.in0(and_24_out), .in1(and_28_out), .out(_1HIT), .sel(not_6_out));
  Comparator #(.width(5), .mode("unsigned")) comparator_17 (
    .a(hits_counter_q), .b(5'b10100), .eq(WIN));  // open: gt, lt
  Multiplexer #(.enable("false")) multiplexer_9 (.in0(and_25_out), .in1(and_29_out), .out(_2HIT), .sel(not_6_out));
  Multiplexer #(.enable("false")) multiplexer_10 (.in0(and_26_out), .in1(and_30_out), .out(_3HIT), .sel(not_6_out));
  Comparator #(.width(4), .mode("unsigned")) comparator_18 (
    .a(CURR_SHIP_ADD), .b(4'b1010), .lt(comparator_18_lt));  // open: gt, eq
  ships_colliding_main main_6 (.SHIP_DATA_A(SHIP_DATA), .SHIP_DATA_B(RAM_OUT_t), .COLLIDING(main_6_colliding));
  and and_31 (and_31_out, comparator_18_lt, CONFIRM);
  and and_32 (and_32_out, CLK_t, COLL_CHECK);
  D_Flip_Flop d_ff_6 (.clk(and_31_out), .D(and_31_out), .Q(COLL_CHECK), .reset(or_10_out));  // open: Qn, preset, en
  Comparator #(.width(15), .mode("unsigned")) comparator_19 (
    .a(RAM_OUT_t), .b({15{1'b0}}), .eq(comparator_19_eq));  // open: gt, lt
  and and_33 (and_33_out, MEM_NOT_CHANGING, ROTATED_CHECK, comparator_5_eq, or_8_out);
  or or_8 (or_8_out, and_23_out, and_24_out, and_25_out, and_26_out);
  and and_34 (and_34_out, MEM_NOT_CHANGING, ~ROTATED_CHECK, comparator_6_eq, or_9_out);  // AND_Gate
  or or_9 (or_9_out, and_27_out, and_28_out, and_29_out, and_30_out);
  Comparator #(.width(4), .mode("unsigned")) comparator_20 (
    .a(CURR_SHIP_ADD), .b(CURR_SHIP_COLL), .eq(comparator_20_eq));  // open: gt, lt
  Counter #(.width(4), .max('hf)) counter_4 (
    .Q(CURR_SHIP_COLL), .clk(and_32_out), .clr(or_10_out));  // open: load, D, count, carry
  or or_10 (or_10_out, and_36_out, and_35_out);
  and and_35 (and_35_out, COLL_CHECK, main_6_colliding, ~comparator_19_eq);  // AND_Gate
  D_Flip_Flop d_ff_7 (.clk(and_33_out), .D(and_33_out), .Q(VERT_HIT), .reset(CHECK_FRAME_END));  // open: Qn, preset, en
  D_Flip_Flop d_ff_8 (.clk(and_34_out), .D(and_34_out), .Q(HORI_HIT), .reset(CHECK_FRAME_END));  // open: Qn, preset, en
  DotMatrix #(.matrixcols(1), .matrixrows(1), .persist(10)) dotmatrix_1 (.col0(and_36_out));
  and and_36 (and_36_out, comparator_20_eq, COLL_CHECK);
  and and_37 (and_37_out, CLK_t, d_ff_9_q);
  D_Flip_Flop d_ff_9 (.clk(and_36_out), .D(and_36_out), .Q(d_ff_9_q), .reset(counter_5_carry));  // open: Qn, preset, en
  Comparator #(.width(4), .mode("unsigned")) comparator_21 (
    .a(CURRENT_SHIP_SHOW), .b(CURR_SHIP_ADD), .eq(comparator_21_eq));  // open: gt, lt
  Counter #(.width(2), .max('h2)) counter_5 (
    .Q(counter_5_q), .carry(counter_5_carry), .clk(and_37_out), .clr(counter_5_carry));  // open: load, D, count
  Counter #(.width(4), .max('hf), .trigger("falling")) counter_6 (
    .Q(CURRENT_SHIP_SHOW), .clk(SHOW_NEXT_SHIP), .clr(comparator_21_eq));  // open: load, D, count, carry
  Comparator #(.width(2), .mode("unsigned")) comparator_22 (
    .a(counter_5_q), .b(2'b00), .gt(CONFIRM_t));  // open: eq, lt
  assign controlled_buffer_11_out = not_7_out ? CURRENT_SHIP_SHOW : 4'bz;  // Controlled_Buffer controlled_buffer_11
  not not_7 (not_7_out, CONFIRM_t);
  assign controlled_buffer_11_out = CONFIRM_t ? CURR_SHIP_ADD : 4'bz;  // Controlled_Buffer controlled_buffer_12
  assign controlled_buffer_13_out = not_8_out ? controlled_buffer_11_out : 4'bz;  // Controlled_Buffer controlled_buffer_13
  not not_8 (not_8_out, COLL_CHECK);
  assign MEM_SELECT = not_9_out ? controlled_buffer_13_out : 4'bz;  // Controlled_Buffer controlled_buffer_14
  not not_9 (not_9_out, CHECKING);
  assign controlled_buffer_13_out = COLL_CHECK ? CURR_SHIP_COLL : 4'bz;  // Controlled_Buffer controlled_buffer_15
  assign MEM_SELECT = CHECKING ? CURR_SHIP_CHECK : 4'bz;  // Controlled_Buffer controlled_buffer_16

  // Other names for the same wires on the sheet: SHIP_X[3:0] = X; SHIP_Y[3:0] = Y; IS_ROTATED = ROTATED;
  //   CURRENT_SHIP[3:0] = CURR_SHIP_ADD; RST = in_2

  // Notes on the sheet:
  //   nieobrocony statek jest poziomy a obrocony pionowy
  //   najpierw ram out powinien sie zmienic a potem powinno dopiero sie zapisac a jest odwrotnie i takie opoznienie jakby jest
  //   na czerwono ma byc jak jest sprawdzane
  //   _HIT jest do sprawdzania czy w ogole trafilo w jakakolwiek czesc statku 'pelnego'
  //   jak jest 20 overwritow(zatopionych) to znaczy ze win
  //   HIT jest do nadpisywania zycia
endmodule
