// Logisim project not_hit_ram_storage.circ as structural Verilog: 1 circuit, main circuit main
module main (
  input  IF_1__save_input,
  input  CLR,
  input  [3:0] X,
  input  [3:0] Y,
  input  CLK,
  output out_6,
  output [7:0] out_7,
  output [3:0] X_2,
  output [3:0] Y_2,
  output [7:0] out_10,
  output [7:0] out_11,
  output [7:0] out_12,
  output [7:0] out_13,
  output [7:0] out_14,
  output [7:0] out_15
);

  wire and_1_out, and_2_out, CLK_t, comparator_1_eq, comparator_2_lt, comparator_3_gt, comparator_3_lt,
       controlled_buffer_2_out, controlled_buffer_3_out, controlled_buffer_5_out, controlled_buffer_9_out,
       controlled_buffer_12_out, counter_1_carry, counter_3_carry, d_ff_3_q, d_ff_3_qn, IS_DATA_GOOD,
       main_1_out_3, main_2_out_3, main_3_out_3, main_4_out_3, main_5_out_3, main_6_out_3, MEM_END, nHIT,
       NO_SUCC_RESET, not_1_out, not_3_out, not_4_out, not_5_out, not_hit___0, not_hit___1, or_2_out,
       or_3_out, or_4_out, pull_resistor_1_node, pull_resistor_5_node, pull_resistor_9_node,
       pull_resistor_10_node, SAVE_N_DATA, SAVE_N_DATA1, SAVE_N_DATA2, SAVE_N_DATA3, SECOND_WRITE_DONE;
  wire [7:0] ADDRESS, STABLE_COUNTER_q;

  Clock clock_1 (.out(CLK_t));
  Pull_Resistor pull_resistor_1 (.node(pull_resistor_1_node));
  assign pull_resistor_1_node = nHIT ? CLK_t : 1'bz;  // Controlled_Buffer controlled_buffer_1
  assign controlled_buffer_2_out = not_1_out ? nHIT : 1'bz;  // Controlled_Buffer controlled_buffer_2
  not not_1 (not_1_out, out_6);
  tick_main main_1 (.in_1(CLK_t), .in_2(nHIT), .out_3(main_1_out_3));
  or or_1 (SAVE_N_DATA, SAVE_N_DATA1, SAVE_N_DATA2, SAVE_N_DATA3);
  Counter #(.width(2), .max('h2)) counter_1 (
    .carry(counter_1_carry), .clk(pull_resistor_1_node));  // open: load, D, count, Q, clr
  Register register_1 (.D({Y, X}), .Q(out_7), .clk(controlled_buffer_2_out), .clr(CLR));  // open: en
  Pull_Resistor pull_resistor_2 (.node(controlled_buffer_2_out));
  Counter #(.width(1), .max('h1), .ongoal("stay")) counter_2 (
    .carry(out_6), .clk(controlled_buffer_3_out), .clr(or_2_out));  // open: load, D, count, Q
  assign controlled_buffer_3_out = SECOND_WRITE_DONE ? main_1_out_3 : 1'bz;  // Controlled_Buffer controlled_buffer_3
  Pull_Resistor pull_resistor_3 (.node(controlled_buffer_3_out));
  or or_2 (or_2_out, NO_SUCC_RESET, SAVE_N_DATA3);
  D_Flip_Flop d_ff_1 (
    .clk(IF_1__save_input), .D(IF_1__save_input), .Q(nHIT), .reset(main_2_out_3));  // open: Qn, preset, en
  tick_main main_2 (.in_1(CLK_t), .in_2(counter_1_carry), .out_3(main_2_out_3));
  Counter #(.width(2), .max('h2), .ongoal("stay")) count_form_0 (
    .carry(not_hit___1), .clk(SAVE_N_DATA), .clr(CLR));  // open: load, D, count, Q
  Counter #(.width(1), .max('h1), .ongoal("stay")) count_form_0_2 (
    .carry(not_hit___0), .clk(SAVE_N_DATA), .clr(CLR));  // open: load, D, count, Q
  Pull_Resistor pull_resistor_4 (.node(SAVE_N_DATA));
  Comparator comparator_1 (.a(out_7), .b(out_10), .eq(comparator_1_eq));  // open: gt, lt
  Register register_2 (.D(out_7), .Q(out_11), .clk(SAVE_N_DATA), .clr(CLR));  // open: en
  Pull_Resistor pull_resistor_5 (.node(pull_resistor_5_node));
  assign pull_resistor_5_node = out_6 ? comparator_1_eq : 1'bz;  // Controlled_Buffer controlled_buffer_4
  Counter #(.max('h90)) STABLE_COUNTER (
    .Q(STABLE_COUNTER_q), .clk(controlled_buffer_5_out), .clr(CLR));  // open: load, D, count, carry
  assign controlled_buffer_5_out = not_hit___0 ? SAVE_N_DATA : 1'bz;  // Controlled_Buffer controlled_buffer_5
  Counter #(.width(1), .max('h1), .ongoal("stay")) counter_3 (
    .carry(counter_3_carry), .clk(pull_resistor_5_node), .clr(NO_SUCC_RESET));  // open: load, D, count, Q
  not not_2 (IS_DATA_GOOD, counter_3_carry);
  Comparator comparator_2 (.a(STABLE_COUNTER_q), .b(ADDRESS), .eq(MEM_END), .lt(comparator_2_lt));  // open: gt
  not not_3 (not_3_out, IS_DATA_GOOD);
  tick_main main_3 (.in_1(CLK_t), .in_2(MEM_END), .out_3(main_3_out_3));
  tick_main main_4 (.in_1(CLK_t), .in_2(MEM_END), .out_3(main_4_out_3));
  tick_main main_5 (.in_1(CLK_t), .in_2(MEM_END), .out_3(main_5_out_3));
  RAM #(.bus("separate")) ram_1 (
    .addr(ADDRESS), .din(out_11), .data(out_10), .str(MEM_END), .clk(CLK_t), .ld(1'b1), .clr(CLR));  // open: sel
  assign {Y_2, X_2} = not_hit___0 ? out_10 : 8'bz;  // Controlled_Buffer controlled_buffer_6
  and and_1 (and_1_out, not_3_out, main_3_out_3);
  and and_2 (and_2_out, IS_DATA_GOOD, main_4_out_3);
  or or_3 (or_3_out, main_5_out_3, comparator_2_lt, CLR, nHIT, SAVE_N_DATA);
  Pull_Resistor pull_resistor_6 (.node(NO_SUCC_RESET));
  assign NO_SUCC_RESET = out_6 ? and_1_out : 1'bz;  // Controlled_Buffer controlled_buffer_7
  assign SAVE_N_DATA3 = out_6 ? and_2_out : 1'bz;  // Controlled_Buffer controlled_buffer_8
  Pull_Resistor pull_resistor_7 (.node(SAVE_N_DATA3));
  Counter #(.max('h90)) UNSTABLE_COUNTER (.Q(ADDRESS), .clk(CLK_t), .clr(or_3_out));  // open: load, D, count, carry
  Counter counter_4 (.clk(NO_SUCC_RESET));  // open: load, D, count, Q, carry, clr
  Counter counter_5 (.clk(SAVE_N_DATA3));  // open: load, D, count, Q, carry, clr
  assign controlled_buffer_9_out = not_hit___0 ? nHIT : 1'bz;  // Controlled_Buffer controlled_buffer_9
  Pull_Resistor pull_resistor_8 (.node(controlled_buffer_9_out));
  not not_4 (not_4_out, not_hit___0);
  Pull_Resistor pull_resistor_9 (.node(pull_resistor_9_node));
  assign pull_resistor_9_node = not_4_out ? nHIT : 1'bz;  // Controlled_Buffer controlled_buffer_10
  not not_5 (not_5_out, SAVE_N_DATA);
  Pull_Resistor pull_resistor_10 (.node(pull_resistor_10_node));
  assign pull_resistor_10_node = not_5_out ? controlled_buffer_9_out : 1'bz;  // Controlled_Buffer controlled_buffer_11
  D_Flip_Flop d_ff_2 (.clk(CLK_t), .D(pull_resistor_9_node), .Q(SAVE_N_DATA1));  // open: Qn, preset, en, reset
  tick_main main_6 (.in_1(CLK_t), .in_2(pull_resistor_10_node), .out_3(main_6_out_3));
  or or_4 (or_4_out, comparator_3_gt, comparator_3_lt);
  Comparator comparator_3 (.a(out_7), .b(out_10), .gt(comparator_3_gt), .lt(comparator_3_lt));  // open: eq
  assign controlled_buffer_12_out = main_6_out_3 ? or_4_out : 1'bz;  // Controlled_Buffer controlled_buffer_12
  Pull_Resistor pull_resistor_11 (.node(controlled_buffer_12_out));
  D_Flip_Flop d_ff_3 (
    .clk(controlled_buffer_12_out), .D(controlled_buffer_12_out), .Q(d_ff_3_q), .Qn(d_ff_3_qn));  // open: preset, en, reset
  D_Flip_Flop d_ff_4 (.clk(CLK_t), .D(d_ff_3_q), .Q(SECOND_WRITE_DONE));  // open: Qn, preset, en, reset
  Pull_Resistor pull_resistor_12 (.node(SAVE_N_DATA2));
  assign SAVE_N_DATA2 = d_ff_3_qn ? controlled_buffer_12_out : 1'bz;  // Controlled_Buffer controlled_buffer_13

  assign out_12 = out_10;
  assign out_13 = out_7;
  assign out_14 = out_7;
  assign out_15 = out_10;

  // Other names for the same wires on the sheet: CHECKED_DATA[7:0] = out_11; CURRENT_MEM_OUT[7:0] = out_10;
  //   DATA_TO_CHECK[7:0] = out_7; CHECKING = out_6; nHIT_REGISTER = out_6; STORE = MEM_END

  // Notes on the sheet:
  //   FITRST DATA SAVER
  //   SECOND DATA SAVER
endmodule
