// Logisim project random_num_generator_B.circ as structural Verilog: 1 circuit, main circuit main
module main (
  input  GENERATE,
  output [3:0] OUTPUT
);

  wire [1:0] random_5_out;
  wire [3:0] rom_1_data, rom_2_data, rom_3_data, rom_4_data;
  wire [4:0] random_1_out, random_2_out, random_3_out, random_4_out;

  Random #(.width(5), .seed(4)) random_1 (.clk(GENERATE), .next(GENERATE), .out(random_1_out));  // open: clr
  Random #(.width(5), .seed(1)) random_2 (.clk(GENERATE), .next(GENERATE), .out(random_2_out));  // open: clr
  Random #(.width(5), .seed(6)) random_3 (.clk(GENERATE), .next(GENERATE), .out(random_3_out));  // open: clr
  Random #(.width(5), .seed(7)) random_4 (.clk(GENERATE), .next(GENERATE), .out(random_4_out));  // open: clr
  ROM #(.addrWidth(5), .dataWidth(4)) rom_1 (.addr(random_1_out), .data(rom_1_data));  // open: sel
  ROM #(.addrWidth(5), .dataWidth(4)) rom_2 (.addr(random_2_out), .data(rom_2_data));  // open: sel
  ROM #(.addrWidth(5), .dataWidth(4)) rom_3 (.addr(random_3_out), .data(rom_3_data));  // open: sel
  ROM #(.addrWidth(5), .dataWidth(4)) rom_4 (.addr(random_4_out), .data(rom_4_data));  // open: sel
  Multiplexer #(.select(2), .width(4)) multiplexer_1 (
    .in0(rom_1_data), .in1(rom_2_data), .in2(rom_3_data), .in3(rom_4_data), .out(OUTPUT), .sel(random_5_out));  // open: en
  Random #(.width(2), .seed(6)) random_5 (.clk(GENERATE), .next(GENERATE), .out(random_5_out));  // open: clr

  // Notes on the sheet:
  //   contents of rom_1 (hex, n*v repeats v):
  //   0 1 2 3 4 5 6 7 8 9 0 1 2 3 4 5 6 7 8 9 0 1 2 3 4 5 6 7 8 9 0 1
  //   contents of rom_2 (hex, n*v repeats v):
  //   0 1 2 3 4 5 6 7 8 9 0 1 2 3 4 5 6 7 8 9 0 1 2 3 4 5 6 7 8 9 0 1
  //   contents of rom_3 (hex, n*v repeats v):
  //   0 1 2 3 4 5 6 7 8 9 0 1 2 3 4 5 6 7 8 9 0 1 2 3 4 5 6 7 8 9 0 1
  //   contents of rom_4 (hex, n*v repeats v):
  //   0 1 2 3 4 5 6 7 8 9 0 1 2 3 4 5 6 7 8 9 0 1 2 3 4 5 6 7 8 9 0 1
endmodule
