// Logisim project screen_driver.circ as structural Verilog: 1 circuit, main circuit main
module main (
  input  clk,
  input  [31:0] mem_in,
  output [1:0] curr_disp,
  output [4:0] curr_col,
  output f_2_clk_in,
  output [31:0] mem_out
);

  wire comparator_1_eq, not_1_out;
  wire [5:0] counter_2_q;

  Counter #(.width(1), .max('h1)) counter_1 (.carry(f_2_clk_in), .clk(clk));  // open: load, D, count, Q, clr
  Counter #(.width(6), .max('h3f)) counter_2 (
    .Q(counter_2_q), .clk(f_2_clk_in), .clr(comparator_1_eq));  // open: load, D, count, carry
  Counter #(.width(5), .max('h1f)) counter_3 (.Q(curr_col), .clk(f_2_clk_in));  // open: load, D, count, carry, clr
  Counter #(.width(2), .max('h3)) counter_4 (.Q(curr_disp), .clk(comparator_1_eq));  // open: load, D, count, carry, clr
  Comparator #(.width(6)) comparator_1 (.a(counter_2_q), .b(6'b100000), .eq(comparator_1_eq));  // open: gt, lt
  assign mem_out = f_2_clk_in ? {32{1'b0}} : 32'bz;  // Controlled_Buffer controlled_buffer_1
  not not_1 (not_1_out, f_2_clk_in);
  assign mem_out = not_1_out ? mem_in : 32'bz;  // Controlled_Buffer controlled_buffer_2
endmodule
