// Logisim project screen_xy_to_screen_data.circ as structural Verilog: 1 circuit, main circuit main
module main (
  input  [5:0] SCREEN_X,
  input  [5:0] SCREEN_Y,
  input  [2:0] DATA_TO_DISPLAY,
  input  CLK,
  input  ENABLE,
  output [4:0] TL_SEL_OUT,
  output [4:0] TR_SEL_OUT,
  output [4:0] BL_SEL_OUT,
  output [4:0] BR_SEL_OUT,
  output [29:0] TL_DATA_OUT,
  output [29:0] TR_DATA_OUT,
  output [29:0] BL_DATA_OUT,
  output [29:0] BR_DATA_OUT
);

  wire not_1_out, SCREEN_SELECT_X, SCREEN_SELECT_Y;
  wire [4:0] adder_1_out, adder_3_out, main_1_data, multiplexer_2_out, SCREEN_BIT_X, Y_BIT_SHIFT;
  wire [5:0] counter_1_q;
  wire [5:5] adder_2_out;
  wire [29:0] bit_extender_1_out, pull_resistor_1_node, shifter_1_out, shifter_2_out;

  Comparator #(.width(6), .mode("unsigned")) comparator_1 (
    .a(SCREEN_Y), .b(6'b011001), .gt(SCREEN_SELECT_Y));  // open: eq, lt
  Adder #(.width(5)) adder_1 (.a(SCREEN_Y[4:0]), .b(5'b00010), .out(adder_1_out));  // open: cin, cout
  drawing_select_main main_1 (.DATA(main_1_data), .SHIP_SELECT(DATA_TO_DISPLAY), .CLK(CLK));
  Multiplexer #(.width(5), .enable("false")) multiplexer_1 (
    .in0(SCREEN_Y[4:0]), .in1(adder_1_out), .out(Y_BIT_SHIFT), .sel(SCREEN_SELECT_Y));
  assign bit_extender_1_out = {{25{1'b0}}, main_1_data};  // Bit_Extender bit_extender_1
  Counter #(.width(6), .max('h4)) counter_1 (.Q(counter_1_q), .clk(CLK));  // open: load, D, count, carry, clr
  Shifter #(.width(30)) shifter_1 (.in(bit_extender_1_out), .\dist (5'b11001), .out(shifter_1_out));
  not not_1 (not_1_out, CLK);
  Shifter #(.width(30), .shift("lr")) shifter_2 (.in(shifter_1_out), .\dist (Y_BIT_SHIFT), .out(shifter_2_out));
  Adder #(.width(6)) adder_2 (.a(SCREEN_X), .b(counter_1_q), .out({adder_2_out[5], SCREEN_BIT_X}));  // open: cin, cout
  Adder #(.width(5)) adder_3 (.a(SCREEN_BIT_X), .b(5'b00010), .out(adder_3_out));  // open: cin, cout
  Pull_Resistor pull_resistor_1 (.node(pull_resistor_1_node));
  assign pull_resistor_1_node = not_1_out ? shifter_2_out : 30'bz;  // Controlled_Buffer controlled_buffer_1
  Demultiplexer #(.select(2), .width(30), .disabled(0)) demultiplexer_1 (
    .out0(TL_DATA_OUT), .out1(TR_DATA_OUT), .out2(BL_DATA_OUT), .out3(BR_DATA_OUT),
    .in(pull_resistor_1_node), .sel({SCREEN_SELECT_Y, SCREEN_SELECT_X}), .en(ENABLE));
  Comparator #(.width(6), .mode("unsigned")) comparator_2 (
    .a({adder_2_out[5], SCREEN_BIT_X}), .b(6'b011101), .gt(SCREEN_SELECT_X));  // open: eq, lt
  Multiplexer #(.width(5), .enable("false")) multiplexer_2 (
    .in0(SCREEN_BIT_X), .in1(adder_3_out), .out(multiplexer_2_out), .sel(SCREEN_SELECT_X));
  Demultiplexer #(.select(2), .width(5), .disabled(0)) demultiplexer_2 (
    .out0(TL_SEL_OUT), .out1(TR_SEL_OUT), .out2(BL_SEL_OUT), .out3(BR_SEL_OUT), .in(multiplexer_2_out),
    .sel({SCREEN_SELECT_Y, SCREEN_SELECT_X}), .en(ENABLE));

  // Other names for the same wires on the sheet: BL_DATA[29:0] = BL_DATA_OUT; BL_SEL[4:0] = BL_SEL_OUT;
  //   BR_DATA[29:0] = BR_DATA_OUT; BR_SEL[4:0] = BR_SEL_OUT; SCREEN_BIT_Y[4:0] = SCREEN_Y[4:0];
  //   TL_DATA[29:0] = TL_DATA_OUT; TL_SEL[4:0] = TL_SEL_OUT; TR_DATA[29:0] = TR_DATA_OUT; TR_SEL[4:0] = TR_SEL_OUT

  // Notes on the sheet:
  //   OUTPUT:
  //   ASSUMING FIELD SIZE IS 5x5!!!
  //   ASSUMING SCREEN SIZE IS 4x(30x30)!!!
  //   input: {6x x_screen, 6x x_screen, 3x data_select_to_display}
  //   output: {4x {30x screen data }, 4x {5xselect} }
endmodule
