// Logisim project secs_to_score.circ as structural Verilog: 1 circuit, main circuit main
module main (
  input  [9:0] SECS_IPT,
  output out_2,
  output out_3,
  output out_4,
  output out_5,
  output out_6,
  output out_7,
  output out_8,
  output out_9,
  output out_10,
  output out_11,
  output out_12,
  output out_13,
  output out_14,
  output out_15,
  output out_16,
  output out_17,
  output out_18,
  output out_19,
  output out_20,
  output out_21,
  output out_22,
  output out_23,
  output out_24,
  output out_25,
  output out_26,
  output out_27,
  output out_28,
  output out_29,
  output out_30,
  output out_31,
  output out_32,
  output out_33
);

  wire [3:0] FULL_MINS_ONES, FULL_MINS_TENS, FULL_SECS_ONES, FULL_SECS_TENS;
  wire [9:0] divider_2_out, divider_3_out, FULL_MINS, FULL_SECS, multiplier_1_out, multiplier_2_out,
       multiplier_3_out, subtractor_1_out, subtractor_3_out;

  // Probe on SECS_IPT
  Pull_Resistor pull_resistor_1 (.node(SECS_IPT));
  // Probe on FULL_MINS
  Divider #(.width(10)) divider_1 (.a(SECS_IPT), .b(10'h3c), .out(FULL_MINS));  // open: upper, rem
  // Probe on divider_2_out
  Divider #(.width(10)) divider_2 (.a(FULL_MINS), .b(10'ha), .out(divider_2_out));  // open: upper, rem
  _7seg_disp_driver_main main_1 (
    .in_1(FULL_MINS_TENS), .out_2(out_10), .out_3(out_11), .out_4(out_12), .out_5(out_13), .out_6(out_26),
    .out_7(out_27), .out_8(out_28), .out_9(out_29));
  Bit_Extender #(.in_width(10), .out_width(4)) bit_extender_1 (.in(divider_2_out), .out(FULL_MINS_TENS));
  Multiplier #(.width(10)) multiplier_1 (.a(divider_2_out), .b(10'ha), .out(multiplier_1_out));  // open: cin, cout
  // Probe on subtractor_1_out
  Subtractor #(.width(10)) subtractor_1 (
    .a(FULL_MINS), .b(multiplier_1_out), .out(subtractor_1_out));  // open: bin, bout
  Bit_Extender #(.in_width(10), .out_width(4)) bit_extender_2 (.in(subtractor_1_out), .out(FULL_MINS_ONES));
  _7seg_disp_driver_main main_2 (
    .in_1(FULL_MINS_ONES), .out_2(out_14), .out_3(out_15), .out_4(out_16), .out_5(out_17), .out_6(out_30),
    .out_7(out_31), .out_8(out_32), .out_9(out_33));
  Multiplier #(.width(10)) multiplier_2 (.a(FULL_MINS), .b(10'h3c), .out(multiplier_2_out));  // open: cin, cout
  Divider #(.width(10)) divider_3 (.a(FULL_SECS), .b(10'ha), .out(divider_3_out));  // open: upper, rem
  _7seg_disp_driver_main main_3 (
    .in_1(FULL_SECS_TENS), .out_2(out_2), .out_3(out_3), .out_4(out_4), .out_5(out_5), .out_6(out_18),
    .out_7(out_19), .out_8(out_20), .out_9(out_21));
  // Probe on FULL_SECS
  Subtractor #(.width(10)) subtractor_2 (.a(SECS_IPT), .b(multiplier_2_out), .out(FULL_SECS));  // open: bin, bout
  // Probe on divider_3_out
  Bit_Extender #(.in_width(10), .out_width(4)) bit_extender_3 (.in(divider_3_out), .out(FULL_SECS_TENS));
  Multiplier #(.width(10)) multiplier_3 (.a(divider_3_out), .b(10'ha), .out(multiplier_3_out));  // open: cin, cout
  // Probe on subtractor_3_out
  Subtractor #(.width(10)) subtractor_3 (
    .a(FULL_SECS), .b(multiplier_3_out), .out(subtractor_3_out));  // open: bin, bout
  Bit_Extender #(.in_width(10), .out_width(4)) bit_extender_4 (.in(subtractor_3_out), .out(FULL_SECS_ONES));
  _7seg_disp_driver_main main_4 (
    .in_1(FULL_SECS_ONES), .out_2(out_6), .out_3(out_7), .out_4(out_8), .out_5(out_9), .out_6(out_22),
    .out_7(out_23), .out_8(out_24), .out_9(out_25));
endmodule
