// Logisim project ship_data_to_all_ship_xy.circ as structural Verilog: 1 circuit, main circuit main
module main (
  input  [14:0] INPUT,
  output [3:0] OUT_X_00,
  output [3:0] OUT_Y_00,
  output [3:0] OUT_X_01,
  output [3:0] OUT_Y_01,
  output [3:0] OUT_X_10,
  output [3:0] OUT_Y_10,
  output [3:0] OUT_X_11,
  output [3:0] OUT_Y_11
);

  wire comparator_1_gt, comparator_2_gt, comparator_3_gt;
  wire [3:0] adder_1_out, adder_2_out, adder_3_out, adder_4_out, adder_5_out, adder_6_out, SCREEN_SHIP_X_01,
       SCREEN_SHIP_X_10, SCREEN_SHIP_X_11, SCREEN_SHIP_Y_01, SCREEN_SHIP_Y_10, SCREEN_SHIP_Y_11;

  Adder #(.width(4)) adder_1 (.a(INPUT[3:0]), .b(4'b0001), .out(adder_1_out));  // open: cin, cout
  Adder #(.width(4)) adder_2 (.a(4'b0001), .b(INPUT[7:4]), .out(adder_2_out));  // open: cin, cout
  Adder #(.width(4)) adder_3 (.a(adder_1_out), .b(4'b0001), .out(adder_3_out));  // open: cin, cout
  Adder #(.width(4)) adder_4 (.a(4'b0001), .b(adder_2_out), .out(adder_4_out));  // open: cin, cout
  Adder #(.width(4)) adder_5 (.a(adder_3_out), .b(4'b0001), .out(adder_5_out));  // open: cin, cout
  Adder #(.width(4)) adder_6 (.a(4'b0001), .b(adder_4_out), .out(adder_6_out));  // open: cin, cout
  Multiplexer #(.width(4), .enable("false")) multiplexer_1 (
    .in0(adder_1_out), .in1(INPUT[3:0]), .out(SCREEN_SHIP_X_01), .sel(INPUT[10]));
  Multiplexer #(.width(4), .enable("false")) multiplexer_2 (
    .in0(INPUT[7:4]), .in1(adder_2_out), .out(SCREEN_SHIP_Y_01), .sel(INPUT[10]));
  Multiplexer #(.width(4), .enable("false")) multiplexer_3 (
    .in0(adder_3_out), .in1(INPUT[3:0]), .out(SCREEN_SHIP_X_10), .sel(INPUT[10]));
  Multiplexer #(.width(4), .enable("false")) multiplexer_4 (
    .in0(INPUT[7:4]), .in1(adder_4_out), .out(SCREEN_SHIP_Y_10), .sel(INPUT[10]));
  Multiplexer #(.width(4), .enable("false")) multiplexer_5 (
    .in0(adder_5_out), .in1(INPUT[3:0]), .out(SCREEN_SHIP_X_11), .sel(INPUT[10]));
  Multiplexer #(.width(4), .enable("false")) multiplexer_6 (
    .in0(INPUT[7:4]), .in1(adder_6_out), .out(SCREEN_SHIP_Y_11), .sel(INPUT[10]));
  // Probe on SCREEN_SHIP_X_01
  // Probe on INPUT[3:0]
  // Probe on SCREEN_SHIP_X_11
  // Probe on SCREEN_SHIP_X_10
  // Probe on SCREEN_SHIP_Y_01
  // Probe on INPUT[7:4]
  // Probe on SCREEN_SHIP_Y_11
  // Probe on SCREEN_SHIP_Y_10
  Comparator #(.width(2), .mode("unsigned")) comparator_1 (
    .a(INPUT[9:8]), .b(2'b00), .gt(comparator_1_gt));  // open: eq, lt
  Comparator #(.width(2), .mode("unsigned")) comparator_2 (
    .a(INPUT[9:8]), .b(2'b01), .gt(comparator_2_gt));  // open: eq, lt
  Comparator #(.width(2), .mode("unsigned")) comparator_3 (
    .a(INPUT[9:8]), .b(2'b10), .gt(comparator_3_gt));  // open: eq, lt
  assign OUT_X_01 = comparator_1_gt ? SCREEN_SHIP_X_01 : 4'bz;  // Controlled_Buffer controlled_buffer_1
  assign OUT_Y_01 = comparator_1_gt ? SCREEN_SHIP_Y_01 : 4'bz;  // Controlled_Buffer controlled_buffer_2
  assign OUT_X_10 = comparator_2_gt ? SCREEN_SHIP_X_10 : 4'bz;  // Controlled_Buffer controlled_buffer_3
  assign OUT_Y_10 = comparator_2_gt ? SCREEN_SHIP_Y_10 : 4'bz;  // Controlled_Buffer controlled_buffer_4
  assign OUT_X_11 = comparator_3_gt ? SCREEN_SHIP_X_11 : 4'bz;  // Controlled_Buffer controlled_buffer_5
  assign OUT_Y_11 = comparator_3_gt ? SCREEN_SHIP_Y_11 : 4'bz;  // Controlled_Buffer controlled_buffer_6

  assign OUT_X_00 = INPUT[3:0];
  assign OUT_Y_00 = INPUT[7:4];

  // Other names for the same wires on the sheet: SCREEN_SHIP_X_00[3:0] = INPUT[3:0]; SHIP_X[3:0] = INPUT[3:0];
  //   SCREEN_SHIP_Y_00[3:0] = INPUT[7:4]; SHIP_Y[3:0] = INPUT[7:4]; SHIP_TYPE[1:0] = INPUT[9:8]; ROTATED = INPUT[10]

  // Notes on the sheet:
  //   nieobrocony statek jest poziomy!!!
  //   in: 15x ship_data => out: {4x {4x ship_x, 4x ship_y}}
  //   OUTPUT
  //   X(dec)
  //   Y (dec)
  //   0,0 zawsze takie same; reszta zalezna od rotated?; dla statkow ktore nie maja wszystich koordynatow wyswietlane jest xxxx (nieustalone)
endmodule
