// Logisim project ship_data_to_screen_data.circ as structural Verilog: 1 circuit, main circuit main
module main (
  input  [3:0] in_1,
  input  [3:0] in_2,
  input  in_3,
  input  in_4,
  input  in_5,
  input  [3:0] in_6,
  input  [3:0] in_7,
  input  in_8,
  input  in_9
);

  wire CLK, ROTATED;
  wire [3:0] ALIVE;
  wire [9:4] SHIP_DATA;

  memory_management_main main_1 (
    .X(in_1), .Y(in_2), .ROTATED(in_3), .RAM_OUT({ALIVE, ROTATED, SHIP_DATA, SHIP_DATA[7:4]}),
    .CHECK_X(in_6), .CHECK_Y(in_7), .SINK_IF_HIT(in_8), .CONFIRM(in_4), .CHECK(in_9), .CLK(CLK),
    .SHOW_NEXT_SHIP(in_5));
  Clock clock_1 (.out(CLK));

  // Other names for the same wires on the sheet: SHIP_DATA (some bits) = {ALIVE, ROTATED, SHIP_DATA[7:4]};
  //   SHIP_X[3:0] = SHIP_DATA[7:4]; SHIP_TYPE[1:0] = SHIP_DATA[9:8]

  // Notes on the sheet:
  //   ship data => {4x ship_x, 4x ship_y, 2x ship_type, 1x rotated, 4x alive}
  //   dostaje 15-bit info o statku i chce na wyjsciu dac 4x 32 (czy tam mniej jak mialo byc) na ekran
endmodule
