// Logisim project ship_out_of_map.circ as structural Verilog: 1 circuit, main circuit main
module main (
  input  [14:0] SHIP_DATA_A,
  output out_of_range
);

  wire comparator_1_eq, comparator_2_eq, comparator_3_eq, comparator_4_eq, comparator_5_eq, comparator_6_eq,
       comparator_7_eq, comparator_8_eq, or_1_out, or_2_out, or_3_out, or_4_out, or_6_out, or_7_out,
       or_8_out, or_9_out, pull_resistor_1_node, pull_resistor_3_node, pull_resistor_5_node,
       pull_resistor_7_node, pull_resistor_9_node, pull_resistor_11_node, pull_resistor_13_node,
       pull_resistor_15_node, X_OOR, Y_OOR;
  wire [3:0] X0, X1, X2, X3, Y0, Y1, Y2, Y3;

  ship_data_to_all_ship_xy_main main_1 (
    .OUT_X_00(X0), .OUT_Y_00(Y0), .OUT_X_01(X1), .OUT_Y_01(Y1), .OUT_X_10(X2), .OUT_Y_10(Y2), .OUT_X_11(X3),
    .OUT_Y_11(Y3), .INPUT(SHIP_DATA_A));
  Pull_Resistor pull_resistor_1 (.node(pull_resistor_1_node));
  Comparator #(.width(4), .mode("unsigned")) comparator_1 (
    .a(X0), .b(4'b1100), .gt(pull_resistor_1_node), .eq(comparator_1_eq));  // open: lt
  or or_1 (or_1_out, pull_resistor_1_node, comparator_1_eq);
  Pull_Resistor pull_resistor_2 (.node(comparator_1_eq));
  Pull_Resistor pull_resistor_3 (.node(pull_resistor_3_node));
  Comparator #(.width(4), .mode("unsigned")) comparator_2 (
    .a(X1), .b(4'b1100), .gt(pull_resistor_3_node), .eq(comparator_2_eq));  // open: lt
  or or_2 (or_2_out, pull_resistor_3_node, comparator_2_eq);
  Pull_Resistor pull_resistor_4 (.node(comparator_2_eq));
  Pull_Resistor pull_resistor_5 (.node(pull_resistor_5_node));
  or or_3 (or_3_out, pull_resistor_5_node, comparator_3_eq);
  Comparator #(.width(4), .mode("unsigned")) comparator_3 (
    .a(X2), .b(4'b1100), .gt(pull_resistor_5_node), .eq(comparator_3_eq));  // open: lt
  Pull_Resistor pull_resistor_6 (.node(comparator_3_eq));
  Pull_Resistor pull_resistor_7 (.node(pull_resistor_7_node));
  Comparator #(.width(4), .mode("unsigned")) comparator_4 (
    .a(X3), .b(4'b1100), .gt(pull_resistor_7_node), .eq(comparator_4_eq));  // open: lt
  or or_4 (or_4_out, pull_resistor_7_node, comparator_4_eq);
  Pull_Resistor pull_resistor_8 (.node(comparator_4_eq));
  or or_5 (X_OOR, or_1_out, or_2_out, or_3_out, or_4_out);
  Pull_Resistor pull_resistor_9 (.node(pull_resistor_9_node));
  Comparator #(.width(4), .mode("unsigned")) comparator_5 (
    .a(Y0), .b(4'b1100), .gt(pull_resistor_9_node), .eq(comparator_5_eq));  // open: lt
  Pull_Resistor pull_resistor_10 (.node(comparator_5_eq));
  Pull_Resistor pull_resistor_11 (.node(pull_resistor_11_node));
  Comparator #(.width(4), .mode("unsigned")) comparator_6 (
    .a(Y1), .b(4'b1100), .gt(pull_resistor_11_node), .eq(comparator_6_eq));  // open: lt
  Pull_Resistor pull_resistor_12 (.node(comparator_6_eq));
  Pull_Resistor pull_resistor_13 (.node(pull_resistor_13_node));
  Comparator #(.width(4), .mode("unsigned")) comparator_7 (
    .a(Y2), .b(4'b1100), .gt(pull_resistor_13_node), .eq(comparator_7_eq));  // open: lt
  Pull_Resistor pull_resistor_14 (.node(comparator_7_eq));
  Pull_Resistor pull_resistor_15 (.node(pull_resistor_15_node));
  Comparator #(.width(4), .mode("unsigned")) comparator_8 (
    .a(Y3), .b(4'b1100), .gt(pull_resistor_15_node), .eq(comparator_8_eq));  // open: lt
  Pull_Resistor pull_resistor_16 (.node(comparator_8_eq));
  or or_6 (or_6_out, pull_resistor_9_node, comparator_5_eq);
  or or_7 (or_7_out, pull_resistor_11_node, comparator_6_eq);
  or or_8 (or_8_out, pull_resistor_13_node, comparator_7_eq);
  or or_9 (or_9_out, pull_resistor_15_node, comparator_8_eq);
  or or_10 (Y_OOR, or_6_out, or_7_out, or_8_out, or_9_out);
  or or_11 (out_of_range, X_OOR, Y_OOR);

  // Notes on the sheet:
  //   returns 0 if X,Y are in [0; MAX_MAP_X/Y)
endmodule
