// Logisim project ship_xyr_to_screen_xy.circ as structural Verilog: 1 circuit, main circuit main
module main (
  input  [3:0] INPUT,
  input  [3:0] in_2,
  input  CONST,
  output [5:0] OUT_X_00,
  output [5:0] OUT_Y_00,
  output [5:0] OUT_X_01,
  output [5:0] OUT_Y_01,
  output [5:0] OUT_X_10,
  output [5:0] OUT_Y_10,
  output [5:0] OUT_X_11,
  output [5:0] OUT_Y_11
);

  wire [5:0] adder_1_out, adder_2_out, adder_3_out, adder_4_out, adder_5_out, adder_6_out,
       bit_extender_1_out, bit_extender_2_out;

  assign bit_extender_1_out = {{2{1'b0}}, INPUT};  // Bit_Extender bit_extender_1
  assign bit_extender_2_out = {{2{1'b0}}, in_2};  // Bit_Extender bit_extender_2
  Multiplier #(.width(6)) multiplier_1 (.a(bit_extender_1_out), .b(6'b000101), .out(OUT_X_00));  // open: cin, cout
  Multiplier #(.width(6)) multiplier_2 (.a(bit_extender_2_out), .b(6'b000101), .out(OUT_Y_00));  // open: cin, cout
  Adder #(.width(6)) adder_1 (.a(OUT_X_00), .b(6'b000101), .out(adder_1_out));  // open: cin, cout
  Adder #(.width(6)) adder_2 (.a(6'b000101), .b(OUT_Y_00), .out(adder_2_out));  // open: cin, cout
  Adder #(.width(6)) adder_3 (.a(adder_1_out), .b(6'b000101), .out(adder_3_out));  // open: cin, cout
  Adder #(.width(6)) adder_4 (.a(6'b000101), .b(adder_2_out), .out(adder_4_out));  // open: cin, cout
  Adder #(.width(6)) adder_5 (.a(adder_3_out), .b(6'b000101), .out(adder_5_out));  // open: cin, cout
  Adder #(.width(6)) adder_6 (.a(6'b000101), .b(adder_4_out), .out(adder_6_out));  // open: cin, cout
  Multiplexer #(.width(6), .enable("false")) multiplexer_1 (
    .in0(adder_1_out), .in1(OUT_X_00), .out(OUT_X_01), .sel(CONST));
  Multiplexer #(.width(6), .enable("false")) multiplexer_2 (
    .in0(OUT_Y_00), .in1(adder_2_out), .out(OUT_Y_01), .sel(CONST));
  Multiplexer #(.width(6), .enable("false")) multiplexer_3 (
    .in0(adder_3_out), .in1(OUT_X_00), .out(OUT_X_10), .sel(CONST));
  Multiplexer #(.width(6), .enable("false")) multiplexer_4 (
    .in0(OUT_Y_00), .in1(adder_4_out), .out(OUT_Y_10), .sel(CONST));
  Multiplexer #(.width(6), .enable("false")) multiplexer_5 (
    .in0(adder_5_out), .in1(OUT_X_00), .out(OUT_X_11), .sel(CONST));
  Multiplexer #(.width(6), .enable("false")) multiplexer_6 (
    .in0(OUT_Y_00), .in1(adder_6_out), .out(OUT_Y_11), .sel(CONST));
  // Probe on OUT_X_10
  // Probe on OUT_X_01
  // Probe on OUT_X_00
  // Probe on OUT_X_11
  // Probe on OUT_Y_00
  // Probe on OUT_Y_10
  // Probe on OUT_Y_01
  // Probe on OUT_Y_11

  // Other names for the same wires on the sheet: ROTATED = CONST; SCREEN_SHIP_X_00[5:0] = OUT_X_00;
  //   SCREEN_SHIP_X_01[5:0] = OUT_X_01; SCREEN_SHIP_X_10[5:0] = OUT_X_10; SCREEN_SHIP_X_11[5:0] = OUT_X_11;
  //   SCREEN_SHIP_Y_00[5:0] = OUT_Y_00; SCREEN_SHIP_Y_01[5:0] = OUT_Y_01; SCREEN_SHIP_Y_10[5:0] = OUT_Y_10;
  //   SCREEN_SHIP_Y_11[5:0] = OUT_Y_11; SHIP_X[3:0] = INPUT; SHIP_Y[3:0] = in_2

  // Notes on the sheet:
  //   tutaj liczymy X, Y statku na ekranie (lewy gorny rog)
  //   nieobrocony statek jest poziomy!!!
  //   dla info statku maja na wysjciu byc 4x (x,y) [lewo, gora]
  //   tu X,Y trzech kolejnych (nie wazne czy zyja czy nie); musimy osobno dla X i dla Y policzyc bo moga byc rozne rozmiary
  //   in: {4x ship_x, 4x ship_y, 1x rotated} => out: {4x {6x screen_ship_x, 6x screen_ship_y}}
  //   OUTPUT
  //   X(dec)
  //   0,0 zawsze takie same; reszta zalezna od rotated?
  //   Y (dec)
endmodule
