// Logisim project ships_colliding.circ as structural Verilog: 1 circuit, main circuit main
module main (
  input  [14:0] SHIP_DATA_A,
  input  [14:0] SHIP_DATA_B,
  output COLLIDING
);

  wire _0_COL, _1_COL, _2_COL, _3_COL, and_1_out, and_2_out, and_3_out, and_4_out, and_5_out, and_6_out,
       and_7_out, and_8_out, and_9_out, and_10_out, and_11_out, and_12_out, and_13_out, and_14_out,
       and_15_out, and_16_out, comparator_2_eq, comparator_3_eq, comparator_4_eq, comparator_5_eq,
       comparator_7_eq, comparator_10_eq, comparator_11_eq, comparator_13_eq, comparator_15_eq,
       comparator_18_eq, comparator_21_eq, comparator_22_eq, comparator_23_eq, comparator_24_eq,
       comparator_25_eq, comparator_26_eq, comparator_27_eq, comparator_28_eq, comparator_31_eq,
       comparator_32_eq, pull_resistor_1_node, pull_resistor_6_node, pull_resistor_8_node,
       pull_resistor_9_node, pull_resistor_12_node, pull_resistor_14_node, pull_resistor_16_node,
       pull_resistor_17_node, pull_resistor_19_node, pull_resistor_20_node, pull_resistor_29_node,
       pull_resistor_30_node;
  wire [3:0] X0_A, X0_B, X1_A, X1_B, X2_A, X2_B, X3_A, X3_B, Y0_A, Y0_B, Y1_A, Y1_B, Y2_A, Y2_B, Y3_A, Y3_B;

  ship_data_to_all_ship_xy_main main_1 (
    .OUT_X_00(X0_A), .OUT_Y_00(Y0_A), .OUT_X_01(X1_A), .OUT_Y_01(Y1_A), .OUT_X_10(X2_A), .OUT_Y_10(Y2_A),
    .OUT_X_11(X3_A), .OUT_Y_11(Y3_A), .INPUT(SHIP_DATA_A));
  ship_data_to_all_ship_xy_main main_2 (
    .OUT_X_00(X0_B), .OUT_Y_00(Y0_B), .OUT_X_01(X1_B), .OUT_Y_01(Y1_B), .OUT_X_10(X2_B), .OUT_Y_10(Y2_B),
    .OUT_X_11(X3_B), .OUT_Y_11(Y3_B), .INPUT(SHIP_DATA_B));
  Pull_Resistor pull_resistor_1 (.node(pull_resistor_1_node));
  Comparator #(.width(4), .mode("unsigned")) comparator_1 (
    .a(X0_A), .b(X0_B), .eq(pull_resistor_1_node));  // open: gt, lt
  and and_1 (and_1_out, pull_resistor_1_node, comparator_2_eq);
  Comparator #(.width(4), .mode("unsigned")) comparator_2 (.a(Y0_A), .b(Y0_B), .eq(comparator_2_eq));  // open: gt, lt
  Pull_Resistor pull_resistor_2 (.node(comparator_2_eq));
  Comparator #(.width(4), .mode("unsigned")) comparator_3 (.a(X0_A), .b(X1_B), .eq(comparator_3_eq));  // open: gt, lt
  Pull_Resistor pull_resistor_3 (.node(comparator_3_eq));
  and and_2 (and_2_out, comparator_3_eq, comparator_4_eq);
  Comparator #(.width(4), .mode("unsigned")) comparator_4 (.a(Y0_A), .b(Y1_B), .eq(comparator_4_eq));  // open: gt, lt
  Pull_Resistor pull_resistor_4 (.node(comparator_4_eq));
  Comparator #(.width(4), .mode("unsigned")) comparator_5 (.a(X0_A), .b(X2_B), .eq(comparator_5_eq));  // open: gt, lt
  Pull_Resistor pull_resistor_5 (.node(comparator_5_eq));
  and and_3 (and_3_out, comparator_5_eq, pull_resistor_6_node);
  Pull_Resistor pull_resistor_6 (.node(pull_resistor_6_node));
  Comparator #(.width(4), .mode("unsigned")) comparator_6 (
    .a(Y0_A), .b(Y2_B), .eq(pull_resistor_6_node));  // open: gt, lt
  Comparator #(.width(4), .mode("unsigned")) comparator_7 (.a(X0_A), .b(X3_B), .eq(comparator_7_eq));  // open: gt, lt
  Pull_Resistor pull_resistor_7 (.node(comparator_7_eq));
  and and_4 (and_4_out, comparator_7_eq, pull_resistor_8_node);
  Pull_Resistor pull_resistor_8 (.node(pull_resistor_8_node));
  Comparator #(.width(4), .mode("unsigned")) comparator_8 (
    .a(Y0_A), .b(Y3_B), .eq(pull_resistor_8_node));  // open: gt, lt
  or or_1 (_0_COL, and_1_out, and_2_out, and_3_out, and_4_out);
  Pull_Resistor pull_resistor_9 (.node(pull_resistor_9_node));
  Comparator #(.width(4), .mode("unsigned")) comparator_9 (
    .a(X1_A), .b(X0_B), .eq(pull_resistor_9_node));  // open: gt, lt
  and and_5 (and_5_out, pull_resistor_9_node, comparator_10_eq);
  Comparator #(.width(4), .mode("unsigned")) comparator_10 (.a(Y1_A), .b(Y0_B), .eq(comparator_10_eq));  // open: gt, lt
  Pull_Resistor pull_resistor_10 (.node(comparator_10_eq));
  Comparator #(.width(4), .mode("unsigned")) comparator_11 (.a(X1_A), .b(X1_B), .eq(comparator_11_eq));  // open: gt, lt
  Pull_Resistor pull_resistor_11 (.node(comparator_11_eq));
  and and_6 (and_6_out, comparator_11_eq, pull_resistor_12_node);
  Pull_Resistor pull_resistor_12 (.node(pull_resistor_12_node));
  Comparator #(.width(4), .mode("unsigned")) comparator_12 (
    .a(Y1_A), .b(Y1_B), .eq(pull_resistor_12_node));  // open: gt, lt
  Comparator #(.width(4), .mode("unsigned")) comparator_13 (.a(X1_A), .b(X2_B), .eq(comparator_13_eq));  // open: gt, lt
  Pull_Resistor pull_resistor_13 (.node(comparator_13_eq));
  and and_7 (and_7_out, comparator_13_eq, pull_resistor_14_node);
  Pull_Resistor pull_resistor_14 (.node(pull_resistor_14_node));
  Comparator #(.width(4), .mode("unsigned")) comparator_14 (
    .a(Y1_A), .b(Y2_B), .eq(pull_resistor_14_node));  // open: gt, lt
  Comparator #(.width(4), .mode("unsigned")) comparator_15 (.a(X1_A), .b(X3_B), .eq(comparator_15_eq));  // open: gt, lt
  Pull_Resistor pull_resistor_15 (.node(comparator_15_eq));
  and and_8 (and_8_out, comparator_15_eq, pull_resistor_16_node);
  Pull_Resistor pull_resistor_16 (.node(pull_resistor_16_node));
  Comparator #(.width(4), .mode("unsigned")) comparator_16 (
    .a(Y1_A), .b(Y3_B), .eq(pull_resistor_16_node));  // open: gt, lt
  or or_2 (_1_COL, and_5_out, and_6_out, and_7_out, and_8_out);
  or or_3 (COLLIDING, _0_COL, _1_COL, _2_COL, _3_COL);
  Pull_Resistor pull_resistor_17 (.node(pull_resistor_17_node));
  Comparator #(.width(4), .mode("unsigned")) comparator_17 (
    .a(X2_A), .b(X0_B), .eq(pull_resistor_17_node));  // open: gt, lt
  Comparator #(.width(4), .mode("unsigned")) comparator_18 (.a(Y2_A), .b(Y0_B), .eq(comparator_18_eq));  // open: gt, lt
  Pull_Resistor pull_resistor_18 (.node(comparator_18_eq));
  Pull_Resistor pull_resistor_19 (.node(pull_resistor_19_node));
  Comparator #(.width(4), .mode("unsigned")) comparator_19 (
    .a(X2_A), .b(X1_B), .eq(pull_resistor_19_node));  // open: gt, lt
  Pull_Resistor pull_resistor_20 (.node(pull_resistor_20_node));
  Comparator #(.width(4), .mode("unsigned")) comparator_20 (
    .a(Y2_A), .b(Y1_B), .eq(pull_resistor_20_node));  // open: gt, lt
  Comparator #(.width(4), .mode("unsigned")) comparator_21 (.a(X2_A), .b(X2_B), .eq(comparator_21_eq));  // open: gt, lt
  Pull_Resistor pull_resistor_21 (.node(comparator_21_eq));
  Comparator #(.width(4), .mode("unsigned")) comparator_22 (.a(Y2_A), .b(Y2_B), .eq(comparator_22_eq));  // open: gt, lt
  Pull_Resistor pull_resistor_22 (.node(comparator_22_eq));
  Comparator #(.width(4), .mode("unsigned")) comparator_23 (.a(X2_A), .b(X3_B), .eq(comparator_23_eq));  // open: gt, lt
  Pull_Resistor pull_resistor_23 (.node(comparator_23_eq));
  Comparator #(.width(4), .mode("unsigned")) comparator_24 (.a(Y2_A), .b(Y3_B), .eq(comparator_24_eq));  // open: gt, lt
  Pull_Resistor pull_resistor_24 (.node(comparator_24_eq));
  and and_9 (and_9_out, pull_resistor_17_node, comparator_18_eq);
  and and_10 (and_10_out, pull_resistor_19_node, pull_resistor_20_node);
  and and_11 (and_11_out, comparator_21_eq, comparator_22_eq);
  and and_12 (and_12_out, comparator_23_eq, comparator_24_eq);
  or or_4 (_2_COL, and_9_out, and_10_out, and_11_out, and_12_out);
  Comparator #(.width(4), .mode("unsigned")) comparator_25 (.a(X3_A), .b(X0_B), .eq(comparator_25_eq));  // open: gt, lt
  Pull_Resistor pull_resistor_25 (.node(comparator_25_eq));
  Comparator #(.width(4), .mode("unsigned")) comparator_26 (.a(Y3_A), .b(Y0_B), .eq(comparator_26_eq));  // open: gt, lt
  Pull_Resistor pull_resistor_26 (.node(comparator_26_eq));
  Comparator #(.width(4), .mode("unsigned")) comparator_27 (.a(X3_A), .b(X1_B), .eq(comparator_27_eq));  // open: gt, lt
  Pull_Resistor pull_resistor_27 (.node(comparator_27_eq));
  Comparator #(.width(4), .mode("unsigned")) comparator_28 (.a(Y3_A), .b(Y1_B), .eq(comparator_28_eq));  // open: gt, lt
  Pull_Resistor pull_resistor_28 (.node(comparator_28_eq));
  Pull_Resistor pull_resistor_29 (.node(pull_resistor_29_node));
  Comparator #(.width(4), .mode("unsigned")) comparator_29 (
    .a(X3_A), .b(X2_B), .eq(pull_resistor_29_node));  // open: gt, lt
  Pull_Resistor pull_resistor_30 (.node(pull_resistor_30_node));
  Comparator #(.width(4), .mode("unsigned")) comparator_30 (
    .a(Y3_A), .b(Y2_B), .eq(pull_resistor_30_node));  // open: gt, lt
  Comparator #(.width(4), .mode("unsigned")) comparator_31 (.a(X3_A), .b(X3_B), .eq(comparator_31_eq));  // open: gt, lt
  Pull_Resistor pull_resistor_31 (.node(comparator_31_eq));
  Comparator #(.width(4), .mode("unsigned")) comparator_32 (.a(Y3_A), .b(Y3_B), .eq(comparator_32_eq));  // open: gt, lt
  Pull_Resistor pull_resistor_32 (.node(comparator_32_eq));
  and and_13 (and_13_out, comparator_25_eq, comparator_26_eq);
  and and_14 (and_14_out, comparator_27_eq, comparator_28_eq);
  and and_15 (and_15_out, pull_resistor_29_node, pull_resistor_30_node);
  and and_16 (and_16_out, comparator_31_eq, comparator_32_eq);
  or or_5 (_3_COL, and_13_out, and_14_out, and_15_out, and_16_out);
endmodule
