// Logisim project shooter.circ as structural Verilog: 1 circuit, main circuit main
module main (
  input  in_1,
  input  in_2,
  input  in_3,
  input  in_4,
  output out_5,
  output out_6,
  output out_7
);

  wire controlled_buffer_1_out, counter_1_carry, counter_2_carry, d_ff_1_q, demultiplexer_1_out1,
       demultiplexer_1_out3, not_1_out, or_1_out;
  wire [4:0] counter_2_q;

  D_Flip_Flop d_ff_1 (.clk(in_2), .D(in_2), .Q(d_ff_1_q), .reset(or_1_out));  // open: Qn, preset, en
  Pull_Resistor pull_resistor_1 (.node(in_2));
  not not_1 (not_1_out, in_3);
  Counter #(.width(4), .max('hf)) counter_1 (
    .carry(counter_1_carry), .clk(controlled_buffer_1_out), .clr(or_1_out));  // open: load, D, count, Q
  Counter #(.width(5), .max('h1f)) counter_2 (
    .Q(counter_2_q), .carry(counter_2_carry), .clk(counter_1_carry), .clr(or_1_out));  // open: load, D, count
  assign controlled_buffer_1_out = d_ff_1_q ? in_1 : 1'bz;  // Controlled_Buffer controlled_buffer_1
  Pull_Resistor pull_resistor_2 (.node(controlled_buffer_1_out));
  or or_1 (or_1_out, not_1_out, in_4, counter_2_carry);
  Demultiplexer #(.select(5)) demultiplexer_1 (
    .out1(demultiplexer_1_out1), .out3(demultiplexer_1_out3), .out31(out_7), .in(1'b1), .sel(counter_2_q),
    .en(d_ff_1_q));  // open: out0, out2, out4, out5, out6, out7, out8, out9, out10, out11, out12, out13, out14, out15, out16, out17, out18, out19, out20, out21, out22, out23, out24, out25, out26, out27, out28, out29, out30
  Pull_Resistor pull_resistor_3 (.node(demultiplexer_1_out1));
  assign out_5 = d_ff_1_q ? demultiplexer_1_out1 : 1'bz;  // Controlled_Buffer controlled_buffer_2
  assign out_6 = d_ff_1_q ? demultiplexer_1_out3 : 1'bz;  // Controlled_Buffer controlled_buffer_3
  Pull_Resistor pull_resistor_4 (.node(demultiplexer_1_out3));
  Pull_Resistor pull_resistor_5 (.node(out_7));

  // Other names for the same wires on the sheet: CLK = in_1; CLR = in_4; CONFIRM_CLOCK = out_6;
  //   POSITION_CLOCK = out_5; SHOOT = in_2; SHOOT_PHASE = in_3; SHOT_DONE = out_7
endmodule
