// Logisim project tick.circ as structural Verilog: 1 circuit, main circuit main
module main (
  input  in_1,
  output out_2
);

  wire clock_1_out, d_ff_1_q, d_ff_1_qn, d_ff_2_q, not_1_out;

  Clock clock_1 (.out(clock_1_out));
  D_Flip_Flop d_ff_1 (.clk(clock_1_out), .D(in_1), .Q(d_ff_1_q), .Qn(d_ff_1_qn));  // open: preset, en, reset
  not not_1 (not_1_out, clock_1_out);
  and and_1 (out_2, d_ff_1_q, d_ff_2_q);
  D_Flip_Flop d_ff_2 (.clk(not_1_out), .D(d_ff_1_qn), .Q(d_ff_2_q));  // open: Qn, preset, en, reset
endmodule
