// Logisim project tick2.circ as structural Verilog: 1 circuit, main circuit main
module main (
  input  CLK,
  input  IN,
  output out_3
);

  wire counter_1_carry, pull_resistor_1_node;

  Counter #(.width(1), .max('h1)) counter_1 (.carry(counter_1_carry), .clk(CLK));  // open: load, D, count, Q, clr
  Pull_Resistor pull_resistor_1 (.node(pull_resistor_1_node));
  assign pull_resistor_1_node = counter_1_carry ? CLK : 1'bz;  // Controlled_Buffer controlled_buffer_1
  Pull_Resistor pull_resistor_2 (.node(out_3));
  assign out_3 = pull_resistor_1_node ? IN : 1'bz;  // Controlled_Buffer controlled_buffer_2
endmodule
