// Logisim project timer.circ as structural Verilog: 1 circuit, main circuit main
// 0x4
module main (
  input  CLK,
  input  START,
  input  SAVE,
  output [9:0] CURR_TIME,
  output [9:0] TOP1,
  output [9:0] TOP2,
  output [9:0] TOP2_2
);

  wire and_1_out, and_2_out, and_3_out, and_4_out, comparator_1_eq, comparator_2_eq, comparator_3_lt,
       comparator_4_eq, comparator_5_lt, comparator_6_eq, comparator_7_lt, comparator_8_eq, counter_1_carry,
       counter_3_carry, d_ff_1_q, HS_SET, not_1_out, or_1_out, SAVE_TEMP, TEMP_NOT_CHANGING, TOP1_SCORED,
       TOP2_SCORED, TOP3_SCORED;
  wire [1:0] priority_encoder_1_out;
  wire [2:0] counter_3_q;
  wire [9:0] shifter_1_out, shifter_2_out, TEMP_TOP1, TEMP_TOP2, TEMP_TOP3;
  wire [29:0] multiplexer_1_out;
  wire [29:10] TOP1_NEW_MEM;
  wire [29:20] TOP2_NEW_MEM;

  Counter #(.width(13), .max('h1f4)) counter_1 (
    .carry(counter_1_carry), .clk(and_1_out), .clr(not_1_out));  // open: load, D, count, Q
  and and_1 (and_1_out, CLK, START);
  Counter #(.width(10), .max('h3ff)) counter_2 (
    .Q(CURR_TIME), .clk(counter_1_carry), .clr(not_1_out));  // open: load, D, count, carry
  not not_1 (not_1_out, START);
  Counter #(.width(3), .max('h3)) counter_3 (
    .Q(counter_3_q), .carry(counter_3_carry), .clk(and_2_out), .clr(or_1_out));  // open: load, D, count
  and and_2 (and_2_out, d_ff_1_q, CLK);
  D_Flip_Flop d_ff_1 (.clk(SAVE), .D(SAVE), .Q(d_ff_1_q), .reset(or_1_out));  // open: Qn, preset, en
  or or_1 (or_1_out, counter_3_carry, and_3_out);
  Register #(.width(30)) register_1 (
    .D({TOP2_2, TOP2, TOP1}), .Q({TEMP_TOP3, TEMP_TOP2, TEMP_TOP1}), .clk(SAVE_TEMP));  // open: en, clr
  and and_3 (and_3_out, HS_SET, TEMP_NOT_CHANGING);
  Comparator #(.width(3), .mode("unsigned")) comparator_1 (
    .a(counter_3_q), .b(3'b001), .eq(comparator_1_eq));  // open: gt, lt
  Comparator #(.width(3), .mode("unsigned")) comparator_2 (
    .a(counter_3_q), .b(3'b010), .gt(TEMP_NOT_CHANGING), .eq(comparator_2_eq));  // open: lt
  Shifter #(.width(30)) shifter_1 (
    .in({TEMP_TOP3, TEMP_TOP2, TEMP_TOP1}), .\dist (5'b01010), .out({TOP1_NEW_MEM, shifter_1_out}));
  D_Flip_Flop d_ff_2 (
    .clk(comparator_1_eq), .D(comparator_1_eq), .Q(SAVE_TEMP), .reset(comparator_2_eq));  // open: Qn, preset, en
  Shifter #(.width(20)) shifter_2 (.in({TEMP_TOP3, TEMP_TOP2}), .\dist (5'b01010), .out({TOP2_NEW_MEM, shifter_2_out}));
  Comparator #(.width(10), .mode("unsigned")) comparator_3 (
    .a(CURR_TIME), .b(TOP1), .lt(comparator_3_lt));  // open: gt, eq
  or or_2 (TOP1_SCORED, comparator_3_lt, comparator_4_eq);
  Comparator #(.width(10), .mode("unsigned")) comparator_4 (
    .a(TOP1), .b({10{1'b0}}), .eq(comparator_4_eq));  // open: gt, lt
  Comparator #(.width(10), .mode("unsigned")) comparator_5 (
    .a(CURR_TIME), .b(TOP2), .lt(comparator_5_lt));  // open: gt, eq
  or or_3 (TOP2_SCORED, comparator_5_lt, comparator_6_eq);
  Comparator #(.width(10), .mode("unsigned")) comparator_6 (
    .a(TOP2), .b({10{1'b0}}), .eq(comparator_6_eq));  // open: gt, lt
  Comparator #(.width(10), .mode("unsigned")) comparator_7 (
    .a(CURR_TIME), .b(TOP2_2), .lt(comparator_7_lt));  // open: gt, eq
  or or_4 (TOP3_SCORED, comparator_7_lt, comparator_8_eq);
  Comparator #(.width(10), .mode("unsigned")) comparator_8 (
    .a(TOP2_2), .b({10{1'b0}}), .eq(comparator_8_eq));  // open: gt, lt
  Priority_Encoder #(.select(2)) priority_encoder_1 (
    .in0(TOP3_SCORED), .in1(TOP2_SCORED), .in2(TOP1_SCORED), .out(priority_encoder_1_out), .gs(HS_SET));  // open: in3, en_out, en_in
  Multiplexer #(.select(2), .width(30), .enable("false")) multiplexer_1 (
    .in0({CURR_TIME, TEMP_TOP2, TEMP_TOP1}), .in1({TOP2_NEW_MEM, CURR_TIME, TEMP_TOP1}),
    .in2({TOP1_NEW_MEM, CURR_TIME}), .out(multiplexer_1_out), .sel(priority_encoder_1_out));  // open: in3
  Register #(.width(30)) register_2 (
    .D(multiplexer_1_out), .Q({TOP2_2, TOP2, TOP1}), .clk(and_4_out));  // open: en, clr
  and and_4 (and_4_out, HS_SET, TEMP_NOT_CHANGING, CLK);

  // Other names for the same wires on the sheet: TOP2_NEW_MEM[19:0] = {CURR_TIME, TEMP_TOP1};
  //   TOP3_NEW_MEM[29:0] = {CURR_TIME, TEMP_TOP2, TEMP_TOP1};
  //   TOP_SCORES_TEMP[29:0] = {TEMP_TOP3, TEMP_TOP2, TEMP_TOP1}; CURR_SEC[9:0] = CURR_TIME;
  //   TOP1_NEW_MEM[9:0] = CURR_TIME; TOP_SCORES[29:0] = {TOP2_2, TOP2, TOP1}; TOP3[9:0] = TOP2_2
endmodule
