// Logisim project timer_demo_TEST.circ as structural Verilog: 1 circuit, main circuit main
module main (
  input  CLK,
  input  START,
  input  SAVE
);

  wire and_1_out, and_2_out, and_3_out, and_4_out, comparator_1_eq, comparator_2_eq, comparator_3_lt,
       comparator_4_eq, comparator_5_lt, comparator_6_eq, comparator_7_lt, comparator_8_eq, counter_2_carry,
       CURRENT_out_2, CURRENT_out_3, CURRENT_out_4, CURRENT_out_5, CURRENT_out_6, CURRENT_out_7,
       CURRENT_out_8, CURRENT_out_9, CURRENT_out_10, CURRENT_out_11, CURRENT_out_12, CURRENT_out_13,
       CURRENT_out_14, CURRENT_out_15, CURRENT_out_16, CURRENT_out_17, CURRENT_out_18, CURRENT_out_19,
       CURRENT_out_20, CURRENT_out_21, CURRENT_out_22, CURRENT_out_23, CURRENT_out_24, CURRENT_out_25,
       CURRENT_out_26, CURRENT_out_27, CURRENT_out_28, CURRENT_out_29, CURRENT_out_30, CURRENT_out_31,
       CURRENT_out_32, CURRENT_out_33, d_ff_1_q, HS_SET, not_1_out, or_1_out, SAVE_TEMP, TEMP_NOT_CHANGING,
       TOP1_out_2, TOP1_out_3, TOP1_out_4, TOP1_out_5, TOP1_out_6, TOP1_out_7, TOP1_out_8, TOP1_out_9,
       TOP1_out_10, TOP1_out_11, TOP1_out_12, TOP1_out_13, TOP1_out_14, TOP1_out_15, TOP1_out_16,
       TOP1_out_17, TOP1_out_18, TOP1_out_19, TOP1_out_20, TOP1_out_21, TOP1_out_22, TOP1_out_23,
       TOP1_out_24, TOP1_out_25, TOP1_out_26, TOP1_out_27, TOP1_out_28, TOP1_out_29, TOP1_out_30,
       TOP1_out_31, TOP1_out_32, TOP1_out_33, TOP1_SCORED, TOP2_out_2, TOP2_out_3, TOP2_out_4, TOP2_out_5,
       TOP2_out_6, TOP2_out_7, TOP2_out_8, TOP2_out_9, TOP2_out_10, TOP2_out_11, TOP2_out_12, TOP2_out_13,
       TOP2_out_14, TOP2_out_15, TOP2_out_16, TOP2_out_17, TOP2_out_18, TOP2_out_19, TOP2_out_20,
       TOP2_out_21, TOP2_out_22, TOP2_out_23, TOP2_out_24, TOP2_out_25, TOP2_out_26, TOP2_out_27,
       TOP2_out_28, TOP2_out_29, TOP2_out_30, TOP2_out_31, TOP2_out_32, TOP2_out_33, TOP2_SCORED, TOP3_out_2,
       TOP3_out_3, TOP3_out_4, TOP3_out_5, TOP3_out_6, TOP3_out_7, TOP3_out_8, TOP3_out_9, TOP3_out_10,
       TOP3_out_11, TOP3_out_12, TOP3_out_13, TOP3_out_14, TOP3_out_15, TOP3_out_16, TOP3_out_17,
       TOP3_out_18, TOP3_out_19, TOP3_out_20, TOP3_out_21, TOP3_out_22, TOP3_out_23, TOP3_out_24,
       TOP3_out_25, TOP3_out_26, TOP3_out_27, TOP3_out_28, TOP3_out_29, TOP3_out_30, TOP3_out_31,
       TOP3_out_32, TOP3_out_33, TOP3_SCORED;
  wire [1:0] priority_encoder_1_out;
  wire [2:0] counter_2_q;
  wire [9:0] CURR_SEC, shifter_1_out, shifter_2_out, TEMP_TOP1, TEMP_TOP2, TEMP_TOP3, TOP1, TOP2, TOP3;
  wire [29:0] multiplexer_1_out;
  wire [29:10] TOP1_NEW_MEM;
  wire [29:20] TOP2_NEW_MEM;

  Counter #(.width(10), .max('h3ff)) counter_1 (
    .Q(CURR_SEC), .clk(and_1_out), .clr(not_1_out));  // open: load, D, count, carry
  not not_1 (not_1_out, START);
  and and_1 (and_1_out, CLK, START);
  Counter #(.width(3), .max('h3)) counter_2 (
    .Q(counter_2_q), .carry(counter_2_carry), .clk(and_2_out), .clr(or_1_out));  // open: load, D, count
  and and_2 (and_2_out, d_ff_1_q, CLK);
  D_Flip_Flop d_ff_1 (.clk(SAVE), .D(SAVE), .Q(d_ff_1_q), .reset(or_1_out));  // open: Qn, preset, en
  or or_1 (or_1_out, counter_2_carry, and_3_out);
  Register #(.width(30)) register_1 (
    .D({TOP3, TOP2, TOP1}), .Q({TEMP_TOP3, TEMP_TOP2, TEMP_TOP1}), .clk(SAVE_TEMP));  // open: en, clr
  and and_3 (and_3_out, HS_SET, TEMP_NOT_CHANGING);
  Comparator #(.width(3), .mode("unsigned")) comparator_1 (
    .a(counter_2_q), .b(3'b001), .eq(comparator_1_eq));  // open: gt, lt
  Comparator #(.width(3), .mode("unsigned")) comparator_2 (
    .a(counter_2_q), .b(3'b010), .gt(TEMP_NOT_CHANGING), .eq(comparator_2_eq));  // open: lt
  Shifter #(.width(30)) shifter_1 (
    .in({TEMP_TOP3, TEMP_TOP2, TEMP_TOP1}), .\dist (5'b01010), .out({TOP1_NEW_MEM, shifter_1_out}));
  D_Flip_Flop d_ff_2 (
    .clk(comparator_1_eq), .D(comparator_1_eq), .Q(SAVE_TEMP), .reset(comparator_2_eq));  // open: Qn, preset, en
  Shifter #(.width(20)) shifter_2 (.in({TEMP_TOP3, TEMP_TOP2}), .\dist (5'b01010), .out({TOP2_NEW_MEM, shifter_2_out}));
  Comparator #(.width(10), .mode("unsigned")) comparator_3 (
    .a(CURR_SEC), .b(TOP1), .lt(comparator_3_lt));  // open: gt, eq
  or or_2 (TOP1_SCORED, comparator_3_lt, comparator_4_eq);
  Comparator #(.width(10), .mode("unsigned")) comparator_4 (
    .a(TOP1), .b({10{1'b0}}), .eq(comparator_4_eq));  // open: gt, lt
  Comparator #(.width(10), .mode("unsigned")) comparator_5 (
    .a(CURR_SEC), .b(TOP2), .lt(comparator_5_lt));  // open: gt, eq
  or or_3 (TOP2_SCORED, comparator_5_lt, comparator_6_eq);
  Comparator #(.width(10), .mode("unsigned")) comparator_6 (
    .a(TOP2), .b({10{1'b0}}), .eq(comparator_6_eq));  // open: gt, lt
  Comparator #(.width(10), .mode("unsigned")) comparator_7 (
    .a(CURR_SEC), .b(TOP3), .lt(comparator_7_lt));  // open: gt, eq
  or or_4 (TOP3_SCORED, comparator_7_lt, comparator_8_eq);
  Comparator #(.width(10), .mode("unsigned")) comparator_8 (
    .a(TOP3), .b({10{1'b0}}), .eq(comparator_8_eq));  // open: gt, lt
  Priority_Encoder #(.select(2)) priority_encoder_1 (
    .in0(TOP3_SCORED), .in1(TOP2_SCORED), .in2(TOP1_SCORED), .out(priority_encoder_1_out), .gs(HS_SET));  // open: in3, en_out, en_in
  Multiplexer #(.select(2), .width(30), .enable("false")) multiplexer_1 (
    .in0({CURR_SEC, TEMP_TOP2, TEMP_TOP1}), .in1({TOP2_NEW_MEM, CURR_SEC, TEMP_TOP1}),
    .in2({TOP1_NEW_MEM, CURR_SEC}), .out(multiplexer_1_out), .sel(priority_encoder_1_out));  // open: in3
  Register #(.width(30)) register_2 (.D(multiplexer_1_out), .Q({TOP3, TOP2, TOP1}), .clk(and_4_out));  // open: en, clr
  and and_4 (and_4_out, HS_SET, TEMP_NOT_CHANGING, CLK);
  _7_Segment_Display u_7_segment_display_1 (
    .g(CURRENT_out_10), .f(CURRENT_out_11), .a(CURRENT_out_12), .b(CURRENT_out_13), .e(CURRENT_out_26),
    .d(CURRENT_out_27), .c(CURRENT_out_28), .dp(CURRENT_out_29));
  secs_to_score_main CURRENT (
    .SECS_IPT(CURR_SEC), .out_10(CURRENT_out_10), .out_11(CURRENT_out_11), .out_12(CURRENT_out_12),
    .out_13(CURRENT_out_13), .out_26(CURRENT_out_26), .out_27(CURRENT_out_27), .out_28(CURRENT_out_28),
    .out_29(CURRENT_out_29), .out_14(CURRENT_out_14), .out_15(CURRENT_out_15), .out_16(CURRENT_out_16),
    .out_17(CURRENT_out_17), .out_30(CURRENT_out_30), .out_31(CURRENT_out_31), .out_32(CURRENT_out_32),
    .out_33(CURRENT_out_33), .out_2(CURRENT_out_2), .out_3(CURRENT_out_3), .out_4(CURRENT_out_4),
    .out_5(CURRENT_out_5), .out_18(CURRENT_out_18), .out_19(CURRENT_out_19), .out_20(CURRENT_out_20),
    .out_21(CURRENT_out_21), .out_6(CURRENT_out_6), .out_7(CURRENT_out_7), .out_8(CURRENT_out_8),
    .out_9(CURRENT_out_9), .out_22(CURRENT_out_22), .out_23(CURRENT_out_23), .out_24(CURRENT_out_24),
    .out_25(CURRENT_out_25));
  secs_to_score_main u_TOP1 (
    .SECS_IPT(TOP1), .out_10(TOP1_out_10), .out_11(TOP1_out_11), .out_12(TOP1_out_12), .out_13(TOP1_out_13),
    .out_26(TOP1_out_26), .out_27(TOP1_out_27), .out_28(TOP1_out_28), .out_29(TOP1_out_29),
    .out_14(TOP1_out_14), .out_15(TOP1_out_15), .out_16(TOP1_out_16), .out_17(TOP1_out_17),
    .out_30(TOP1_out_30), .out_31(TOP1_out_31), .out_32(TOP1_out_32), .out_33(TOP1_out_33),
    .out_2(TOP1_out_2), .out_3(TOP1_out_3), .out_4(TOP1_out_4), .out_5(TOP1_out_5), .out_18(TOP1_out_18),
    .out_19(TOP1_out_19), .out_20(TOP1_out_20), .out_21(TOP1_out_21), .out_6(TOP1_out_6), .out_7(TOP1_out_7),
    .out_8(TOP1_out_8), .out_9(TOP1_out_9), .out_22(TOP1_out_22), .out_23(TOP1_out_23), .out_24(TOP1_out_24),
    .out_25(TOP1_out_25));
  _7_Segment_Display u_7_segment_display_2 (
    .g(TOP1_out_10), .f(TOP1_out_11), .a(TOP1_out_12), .b(TOP1_out_13), .e(TOP1_out_26), .d(TOP1_out_27),
    .c(TOP1_out_28), .dp(TOP1_out_29));
  secs_to_score_main u_TOP2 (
    .SECS_IPT(TOP2), .out_10(TOP2_out_10), .out_11(TOP2_out_11), .out_12(TOP2_out_12), .out_13(TOP2_out_13),
    .out_26(TOP2_out_26), .out_27(TOP2_out_27), .out_28(TOP2_out_28), .out_29(TOP2_out_29),
    .out_14(TOP2_out_14), .out_15(TOP2_out_15), .out_16(TOP2_out_16), .out_17(TOP2_out_17),
    .out_30(TOP2_out_30), .out_31(TOP2_out_31), .out_32(TOP2_out_32), .out_33(TOP2_out_33),
    .out_2(TOP2_out_2), .out_3(TOP2_out_3), .out_4(TOP2_out_4), .out_5(TOP2_out_5), .out_18(TOP2_out_18),
    .out_19(TOP2_out_19), .out_20(TOP2_out_20), .out_21(TOP2_out_21), .out_6(TOP2_out_6), .out_7(TOP2_out_7),
    .out_8(TOP2_out_8), .out_9(TOP2_out_9), .out_22(TOP2_out_22), .out_23(TOP2_out_23), .out_24(TOP2_out_24),
    .out_25(TOP2_out_25));
  _7_Segment_Display u_7_segment_display_3 (
    .g(TOP2_out_10), .f(TOP2_out_11), .a(TOP2_out_12), .b(TOP2_out_13), .e(TOP2_out_26), .d(TOP2_out_27),
    .c(TOP2_out_28), .dp(TOP2_out_29));
  secs_to_score_main u_TOP3 (
    .SECS_IPT(TOP3), .out_10(TOP3_out_10), .out_11(TOP3_out_11), .out_12(TOP3_out_12), .out_13(TOP3_out_13),
    .out_26(TOP3_out_26), .out_27(TOP3_out_27), .out_28(TOP3_out_28), .out_29(TOP3_out_29),
    .out_14(TOP3_out_14), .out_15(TOP3_out_15), .out_16(TOP3_out_16), .out_17(TOP3_out_17),
    .out_30(TOP3_out_30), .out_31(TOP3_out_31), .out_32(TOP3_out_32), .out_33(TOP3_out_33),
    .out_2(TOP3_out_2), .out_3(TOP3_out_3), .out_4(TOP3_out_4), .out_5(TOP3_out_5), .out_18(TOP3_out_18),
    .out_19(TOP3_out_19), .out_20(TOP3_out_20), .out_21(TOP3_out_21), .out_6(TOP3_out_6), .out_7(TOP3_out_7),
    .out_8(TOP3_out_8), .out_9(TOP3_out_9), .out_22(TOP3_out_22), .out_23(TOP3_out_23), .out_24(TOP3_out_24),
    .out_25(TOP3_out_25));
  _7_Segment_Display u_7_segment_display_4 (
    .g(TOP3_out_10), .f(TOP3_out_11), .a(TOP3_out_12), .b(TOP3_out_13), .e(TOP3_out_26), .d(TOP3_out_27),
    .c(TOP3_out_28), .dp(TOP3_out_29));
  _7_Segment_Display u_7_segment_display_5 (
    .g(CURRENT_out_14), .f(CURRENT_out_15), .a(CURRENT_out_16), .b(CURRENT_out_17), .e(CURRENT_out_30),
    .d(CURRENT_out_31), .c(CURRENT_out_32), .dp(CURRENT_out_33));
  _7_Segment_Display u_7_segment_display_6 (
    .g(CURRENT_out_2), .f(CURRENT_out_3), .a(CURRENT_out_4), .b(CURRENT_out_5), .e(CURRENT_out_18),
    .d(CURRENT_out_19), .c(CURRENT_out_20), .dp(CURRENT_out_21));
  _7_Segment_Display u_7_segment_display_7 (
    .g(TOP1_out_2), .f(TOP1_out_3), .a(TOP1_out_4), .b(TOP1_out_5), .e(TOP1_out_18), .d(TOP1_out_19),
    .c(TOP1_out_20), .dp(TOP1_out_21));
  _7_Segment_Display u_7_segment_display_8 (
    .g(TOP1_out_14), .f(TOP1_out_15), .a(TOP1_out_16), .b(TOP1_out_17), .e(TOP1_out_30), .d(TOP1_out_31),
    .c(TOP1_out_32), .dp(TOP1_out_33));
  _7_Segment_Display u_7_segment_display_9 (
    .g(TOP2_out_2), .f(TOP2_out_3), .a(TOP2_out_4), .b(TOP2_out_5), .e(TOP2_out_18), .d(TOP2_out_19),
    .c(TOP2_out_20), .dp(TOP2_out_21));
  _7_Segment_Display u_7_segment_display_10 (
    .g(TOP2_out_14), .f(TOP2_out_15), .a(TOP2_out_16), .b(TOP2_out_17), .e(TOP2_out_30), .d(TOP2_out_31),
    .c(TOP2_out_32), .dp(TOP2_out_33));
  _7_Segment_Display u_7_segment_display_11 (
    .g(TOP3_out_2), .f(TOP3_out_3), .a(TOP3_out_4), .b(TOP3_out_5), .e(TOP3_out_18), .d(TOP3_out_19),
    .c(TOP3_out_20), .dp(TOP3_out_21));
  _7_Segment_Display u_7_segment_display_12 (
    .g(TOP3_out_14), .f(TOP3_out_15), .a(TOP3_out_16), .b(TOP3_out_17), .e(TOP3_out_30), .d(TOP3_out_31),
    .c(TOP3_out_32), .dp(TOP3_out_33));
  _7_Segment_Display u_7_segment_display_13 (
    .g(CURRENT_out_6), .f(CURRENT_out_7), .a(CURRENT_out_8), .b(CURRENT_out_9), .e(CURRENT_out_22),
    .d(CURRENT_out_23), .c(CURRENT_out_24), .dp(CURRENT_out_25));
  _7_Segment_Display u_7_segment_display_14 (
    .g(TOP1_out_6), .f(TOP1_out_7), .a(TOP1_out_8), .b(TOP1_out_9), .e(TOP1_out_22), .d(TOP1_out_23),
    .c(TOP1_out_24), .dp(TOP1_out_25));
  _7_Segment_Display u_7_segment_display_15 (
    .g(TOP2_out_6), .f(TOP2_out_7), .a(TOP2_out_8), .b(TOP2_out_9), .e(TOP2_out_22), .d(TOP2_out_23),
    .c(TOP2_out_24), .dp(TOP2_out_25));
  _7_Segment_Display u_7_segment_display_16 (
    .g(TOP3_out_6), .f(TOP3_out_7), .a(TOP3_out_8), .b(TOP3_out_9), .e(TOP3_out_22), .d(TOP3_out_23),
    .c(TOP3_out_24), .dp(TOP3_out_25));

  // Other names for the same wires on the sheet: TOP2_NEW_MEM[19:0] = {CURR_SEC, TEMP_TOP1};
  //   TOP3_NEW_MEM[29:0] = {CURR_SEC, TEMP_TOP2, TEMP_TOP1};
  //   TOP_SCORES_TEMP[29:0] = {TEMP_TOP3, TEMP_TOP2, TEMP_TOP1}; TOP1_NEW_MEM[9:0] = CURR_SEC;
  //   TOP_SCORES[29:0] = {TOP3, TOP2, TOP1}
endmodule
